// Logisim project cpu21-riscv.circ as structural Verilog: 23 circuits, main circuit ◇单周期RISC-V
module \单周期RISC_V  (
  input  IR1,
  input  IR2,
  input  IR3,
  output RegWrite,
  output MemWrite,
  output [31:0] PC,
  output [31:0] IR,
  output [31:0] RDin,
  output [31:0] MDin,
  output [31:0] LedData
);

  wire AluSrcB, and_2_out, and_3_out, and_5_out, and_6_out, and_7_out, Beq, BLTU, Bne, Branch, CLK,
       clock_1_out, comparator_1_eq, comparator_2_eq, comparator_2_lt, d_ff_1_q, ecall, EQ, Go, halt, IR1_t,
       IR2_t, IR3_t, IRA, IRB, IRC, JAL, Jalr, LBU, LT, MemToReg, nand_1_out, not_1_out, not_2_out, PCToReg,
       RST, S_Type, U_Type, uret, W1, W2, W3;
  wire [1:0] Index;
  wire [3:0] AluOP;
  wire [4:0] multiplexer_5_out, multiplexer_6_out;
  wire [7:0] multiplexer_10_out;
  wire [11:0] imm12_B, multiplexer_7_out;
  wire [12:0] CNT_num;
  wire [15:0] \分支成功数 , \总周期数 ;
  wire [19:0] imm20_J;
  wire [31:0] adder_1_out, adder_2_out, adder_3_out, and_1_out, bit_extender_1_out, bit_extender_2_out,
       bit_extender_3_out, bit_extender_4_out, MDout, multiplexer_1_out, multiplexer_2_out,
       multiplexer_4_out, multiplexer_8_out, PC_4, R1, ram_1_data, RPCin;
  wire [31:2] Result;

  Button \u_继续运行  (.out(Go));
  Button _1 (.out(IRA));
  Button _2 (.out(IRB));
  Button _3 (.out(IRC));
  LED #(.active("true")) led_1 (.in(W1));
  LED #(.active("true")) led_2 (.in(W2));
  LED #(.active("true")) led_3 (.in(W3));
  assign bit_extender_1_out = {{12{imm20_J[19]}}, imm20_J};  // Bit_Extender bit_extender_1
  assign bit_extender_2_out = {{20{imm12_B[11]}}, imm12_B};  // Bit_Extender bit_extender_2
  Hex_Digit_Display hex_digit_display_1 (.value(LedData[31:28]));  // open: dp
  Adder #(.width(32)) adder_1 (.a(bit_extender_1_out), .b(PC), .out(adder_1_out));  // open: cin, cout
  assign and_1_out = {Result, Index} & 32'hfffffffe;  // AND_Gate and_1, 32 bits wide
  Adder #(.width(32)) adder_2 (.a(bit_extender_2_out), .b(PC), .out(adder_2_out));  // open: cin, cout
  Comparator #(.width(32), .mode("twosComplement")) comparator_1 (
    .a(R1), .b(32'h22), .eq(comparator_1_eq));  // open: gt, lt
  Adder #(.width(32)) adder_3 (.a(PC), .b({IR[31:12], {12{1'b0}}}), .out(adder_3_out));  // open: cin, cout
  Hex_Digit_Display hex_digit_display_2 (.value(LedData[23:20]));  // open: dp
  Hex_Digit_Display hex_digit_display_3 (.value(LedData[27:24]));  // open: dp
  Multiplexer #(.select(1), .width(32), .disabled("Z"), .enable("false")) multiplexer_1 (
    .in0(PC_4), .in1(adder_1_out), .out(multiplexer_1_out), .sel(JAL));
  Multiplexer #(.select(1), .width(32), .disabled("Z"), .enable("false")) multiplexer_2 (
    .in0(multiplexer_1_out), .in1(and_1_out), .out(multiplexer_2_out), .sel(Jalr));
  Adder #(.width(32)) adder_4 (.a(PC), .b(32'h4), .out(PC_4));  // open: cin, cout
  and and_2 (and_2_out, ecall, comparator_1_eq);
  and and_3 (and_3_out, ~comparator_1_eq, ecall);  // AND_Gate
  or or_1 (PCToReg, JAL, Jalr, U_Type);
  Multiplexer #(.select(1), .width(32), .disabled("Z"), .enable("false")) multiplexer_3 (
    .in0(PC_4), .in1(adder_3_out), .out(RPCin), .sel(U_Type));
  Hex_Digit_Display hex_digit_display_4 (.value(LedData[15:12]));  // open: dp
  Hex_Digit_Display hex_digit_display_5 (.value(LedData[19:16]));  // open: dp
  Button button_1 (.out(RST));
  Multiplexer #(.select(1), .width(32), .disabled("Z"), .enable("false")) multiplexer_4 (
    .in0(multiplexer_2_out), .in1(adder_2_out), .out(multiplexer_4_out), .sel(Branch));
  Register #(.width(32), .trigger("rising"), .Select("low")) register_1 (
    .D(MDin), .en(and_2_out), .Q(LedData), .clk(CLK), .clr(RST));
  and and_4 (halt, and_3_out, ~Go);  // AND_Gate
  Hex_Digit_Display hex_digit_display_6 (.value(LedData[7:4]));  // open: dp
  Hex_Digit_Display hex_digit_display_7 (.value(LedData[11:8]));  // open: dp
  // Probe on \总周期数 
  not not_1 (not_1_out, halt);
  Counter #(.width(16), .max('hffff), .ongoal("wrap"), .trigger("rising"), .behavior("new")) counter_1 (
    .count(not_1_out), .Q(\总周期数 ), .clk(CLK), .clr(RST));  // open: load, D, carry, preset, down
  not not_2 (not_2_out, halt);
  Hex_Digit_Display hex_digit_display_8 (.value(LedData[3:0]));  // open: dp
  Register #(.width(32), .trigger("rising"), .Select("low")) u_PC (
    .D(multiplexer_4_out), .en(not_2_out), .Q(PC), .clk(CLK), .clr(RST));
  and and_5 (and_5_out, Beq, EQ);
  and and_6 (and_6_out, ~EQ, Bne);  // AND_Gate
  and and_7 (and_7_out, LT, BLTU);
  or or_2 (Branch, and_5_out, and_6_out, and_7_out);
  or or_3 (IR1_t, IR1, IRA);
  // RiscV_Probe riscv_probe_1: pin names not known; wires that end beside it: IR
  // Probe on \分支成功数 
  Counter #(.width(16), .max('hffff), .ongoal("wrap"), .trigger("rising"), .behavior("new")) counter_2 (
    .count(Branch), .Q(\分支成功数 ), .clk(CLK), .clr(RST));  // open: load, D, carry, preset, down
  or or_4 (IR2_t, IR2, IRB);
  ROM #(.addrWidth(10), .dataWidth(32), .Select("high")) rom_1 (.addr(PC[11:2]), .data(IR));
  or or_5 (IR3_t, IR3, IRC);
  \单周期硬布线控制器  \u_单周期硬布线控制器_1  (
    .Funct({IR[30], IR[25], IR[14:12]}), .OP(IR[6:2]), .ALU_OP(AluOP), .MemToReg(MemToReg),
    .MemWrite(MemWrite), .ALU_SRC(AluSrcB), .RegWrite(RegWrite), .ecall(ecall), .S_type(S_Type), .Jalr(Jalr),
    .Beq(Beq), .JAL(JAL), .Bne(Bne), .in_3(IR[21]), .uret(uret), .BLTU(BLTU), .U_Type(U_Type), .LBU(LBU));  // open: R1, R2, CSRRSI, CSRRCI
  Multiplexer #(.select(1), .width(5), .disabled("Z"), .enable("false")) multiplexer_5 (
    .in0(IR[19:15]), .in1(5'b10001), .out(multiplexer_5_out), .sel(ecall));
  Multiplexer #(.select(1), .width(5), .disabled("Z"), .enable("false")) multiplexer_6 (
    .in0(IR[24:20]), .in1(5'b01010), .out(multiplexer_6_out), .sel(ecall));
  Shifter #(.width(12), .shift("ll")) shifter_1 (
    .in({IR[31], IR[7], IR[30:25], IR[11:8]}), .\dist (4'b0001), .out(imm12_B));
  Shifter #(.width(20), .shift("ll")) shifter_2 (
    .in({IR[31], IR[19:12], IR[20], IR[30:21]}), .\dist (5'b00001), .out(imm20_J));
  Regifile regifile_1 (
    .Din(RDin), .Clk(CLK), .R1(R1), .R2(MDin), .WE(RegWrite), .W_num(IR[11:7]), .R1_num(multiplexer_5_out),
    .R2_num(multiplexer_6_out));
  Multiplexer #(.select(1), .width(12), .disabled("Z"), .enable("false")) multiplexer_7 (
    .in0(IR[31:20]), .in1({IR[31:25], IR[11:7]}), .out(multiplexer_7_out), .sel(S_Type));
  Multiplexer #(.select(1), .width(32), .disabled("Z"), .enable("false")) multiplexer_8 (
    .in0(MDin), .in1(bit_extender_3_out), .out(multiplexer_8_out), .sel(AluSrcB));
  assign bit_extender_3_out = {{20{multiplexer_7_out[11]}}, multiplexer_7_out};  // Bit_Extender bit_extender_3
  ALU alu_1 (
    .X(R1), .Y(multiplexer_8_out), .AluOP(AluOP), .Equal(EQ), .Result({Result, Index}), .out_6(LT));  // open: Result_2, out_4
  Multiplexer #(.select(2), .width(32), .disabled("Z"), .enable("false")) multiplexer_9 (
    .in0({Result, Index}), .in1(MDout), .in2(RPCin), .in3(RPCin), .out(RDin), .sel({PCToReg, MemToReg}));
  D_Flip_Flop #(.trigger("high"), .Pre_Clr_Positions("LEGACY"), .NegatePresetClear("false"), .enable("true"), .NewFFLayout("false")) d_ff_1 (.Q(d_ff_1_q));  // open: clk, D, Qn, preset, en, reset
  // Probe on 13'hc
  Comparator #(.width(13), .mode("twosComplement")) comparator_2 (
    .a(CNT_num), .b(13'hc), .eq(comparator_2_eq), .lt(comparator_2_lt));  // open: gt
  Clock #(.highDuration(1), .lowDuration(1)) clock_1 (.out(clock_1_out));
  Counter #(.width(13), .max('h1fff), .ongoal("stay"), .trigger("rising"), .behavior("old")) counter_3 (
    .count(comparator_2_lt), .Q(CNT_num), .clk(clock_1_out));  // open: load, D, carry, clr, preset
  RAM #(.addrWidth(10), .dataWidth(32), .bus("separate"), .Select("high")) ram_1 (
    .addr(Result[11:2]), .din(MDin), .data(ram_1_data), .str(MemWrite), .clk(CLK), .ld(MemToReg), .clr(RST));  // open: sel
  nand nand_1 (nand_1_out, d_ff_1_q, comparator_2_eq);
  Multiplexer #(.select(2), .width(8), .disabled("Z"), .enable("false")) multiplexer_10 (
    .in0(ram_1_data[7:0]), .in1(ram_1_data[15:8]), .in2(ram_1_data[23:16]), .in3(ram_1_data[31:24]),
    .out(multiplexer_10_out), .sel(Index));
  assign CLK = nand_1_out ? clock_1_out : 1'bz;  // Controlled_Buffer controlled_buffer_1
  Pull_Resistor #(.pull(1)) pull_resistor_1 (.node(CLK));
  assign bit_extender_4_out = {{24{1'b0}}, multiplexer_10_out};  // Bit_Extender bit_extender_4
  Multiplexer #(.select(1), .width(32), .disabled("Z"), .enable("false")) multiplexer_11 (
    .in0(ram_1_data), .in1(bit_extender_4_out), .out(MDout), .sel(LBU));

  // Other names for the same wires on the sheet: imm32_U[31:12] = IR[31:12]; imm12_I[11:0] = IR[31:20];
  //   imm12_S[11:0] = {IR[31:25], IR[11:7]}; R2[31:0] = MDin; Result[1:0] = Index

  // Notes on the sheet:
  //   中断源
  //   中断等待指示
  //   数码管输出应该用寄存器锁存，否则显示数据只能一闪而过
  //   数码管输出
  //   指令探针
  //   指令存储器
  //   指令字
  //   contents of rom_1 (hex, n*v repeats v):
  //   13 430497 900533 2200893 73 430497 900533 2200893 73 430497 900533 2200893 73 430497 900533 2200893
  //   73 430497 900533 2200893 73 430497 900533 2200893 73 430497 900533 2200893 73 430497 900533 2200893
  //   73 a00893 73
  //   为方便自动评测，需要输出PC，IR，寄存器堆写如数据RDin
  //   RAM写使能MemWrite、RAM写入数据MDin等信号
  //   控制位
  //   暂停节拍，不能为0
  //   戳工具置1进入计数暂停模式，ctrl+k时钟自动运行到对应节拍暂停
  //   ctrl+k关闭时钟连续运行，将控制位置零，进入单步调试模式调试
  //   用这个时钟源需要去掉电路中的其他时钟源
  //   数据存储器
  //   可计数暂停的时钟源
endmodule

// 单周期硬布线控制器
module \单周期硬布线控制器  (
  input  [4:0] OP,
  input  [4:0] Funct,
  input  in_3,
  output [3:0] ALU_OP,
  output uret,
  output MemToReg,
  output ecall,
  output MemWrite,
  output ALU_SRC,
  output RegWrite,
  output S_type,
  output Beq,
  output Bne,
  output Jalr,
  output JAL,
  output BLTU,
  output U_Type,
  output LBU,
  output R1,
  output R2,
  output CSRRSI,
  output CSRRCI
);

  wire \控制信号自动生成_1_ecall ;

  \运算控制器自动生成  \u_运算控制器自动生成_1  (
    .OP2(OP[0]), .OP3(OP[1]), .OP4(OP[2]), .OP5(OP[3]), .OP6(OP[4]), .F12(Funct[0]), .F13(Funct[1]),
    .F14(Funct[2]), .F25(Funct[3]), .F30(Funct[4]), .S0(ALU_OP[0]), .S1(ALU_OP[1]), .S2(ALU_OP[2]),
    .S3(ALU_OP[3]));
  \控制信号自动生成  \u_控制信号自动生成_1  (
    .OP2(OP[0]), .OP3(OP[1]), .OP4(OP[2]), .OP5(OP[3]), .MemToReg(MemToReg), .OP6(OP[4]), .F12(Funct[0]),
    .F13(Funct[1]), .F14(Funct[2]), .F25(Funct[3]), .F30(Funct[4]), .MemWrite(MemWrite), .ALU_SRC(ALU_SRC),
    .RegWrite(RegWrite), .ecall(\控制信号自动生成_1_ecall ), .S_Type(S_type), .BEQ(Beq), .BNE(Bne), .JALR(Jalr),
    .JAL(JAL), .BLTU(BLTU), .U_Type(U_Type), .LBU(LBU), .R1(R1), .R2(R2), .CSRRSI(CSRRSI), .CSRRCI(CSRRCI));
  and and_1 (uret, in_3, \控制信号自动生成_1_ecall );
  and and_2 (ecall, ~in_3, \控制信号自动生成_1_ecall );  // AND_Gate

  // Other names for the same wires on the sheet: IR21 = in_3; OP_CODE[4:0] = OP

  // Notes on the sheet:
  //   运算器控制器，根据指令生成运算器功能选择信号
  //   控制信号生成，产生数据通路需要的其他控制信号
endmodule

// 运算器控制器
module \运算控制器自动生成  (
  input  OP2,
  input  OP3,
  input  OP4,
  input  OP5,
  input  OP6,
  input  F12,
  input  F13,
  input  F14,
  input  F25,
  input  F30,
  output S0,
  output S1,
  output S2,
  output S3
);

  wire and_1_out, and_2_out, and_3_out, and_4_out, and_5_out, and_6_out, and_7_out, and_8_out, and_9_out,
       and_10_out, and_11_out, and_12_out, and_13_out, and_14_out, and_15_out, and_16_out, and_17_out,
       and_18_out, and_19_out, and_20_out, and_21_out, and_22_out, and_23_out, and_24_out, and_25_out,
       and_26_out, and_27_out, and_28_out, and_29_out, and_30_out, and_31_out, and_32_out, and_33_out,
       and_34_out, and_35_out, and_36_out, and_37_out, and_38_out, and_39_out, and_40_out, and_41_out,
       not_1_out, not_2_out, not_3_out, not_4_out, not_5_out, not_6_out, not_7_out, not_8_out, not_9_out,
       not_10_out, not_11_out, not_12_out, not_13_out, not_14_out, not_15_out, not_16_out, not_17_out,
       not_18_out, not_19_out, not_20_out, not_21_out, not_22_out, not_23_out, not_24_out, not_25_out,
       not_26_out, not_27_out, not_28_out, not_29_out, not_30_out, not_31_out, not_32_out, not_33_out,
       not_34_out, not_35_out, not_36_out, not_37_out, not_38_out, not_39_out, not_40_out, not_41_out,
       not_42_out, not_43_out, not_44_out, not_45_out, not_46_out, not_47_out, not_48_out, not_49_out,
       not_50_out, not_51_out, not_52_out, not_53_out, not_54_out, not_55_out, not_56_out, not_57_out,
       not_58_out, not_59_out, not_60_out, not_61_out, not_62_out, not_63_out, not_64_out, not_65_out,
       not_66_out, not_67_out, not_68_out, not_69_out, not_70_out, not_71_out, not_72_out, not_73_out,
       not_74_out, not_75_out, not_76_out, not_77_out, not_78_out, not_79_out, not_80_out, not_81_out,
       not_82_out, not_83_out, not_84_out, not_85_out, not_86_out, not_87_out, not_88_out, not_89_out,
       not_90_out, not_91_out, not_92_out, not_93_out, not_94_out, not_95_out, not_96_out, not_97_out,
       not_98_out, not_99_out, not_100_out, not_101_out, not_102_out, not_103_out, not_104_out, not_105_out,
       not_106_out, not_107_out, not_108_out, not_109_out, not_110_out, not_111_out, not_112_out,
       not_113_out, not_114_out, not_115_out, not_116_out, not_117_out, not_118_out, not_119_out,
       not_120_out, not_121_out, not_122_out, not_123_out, not_124_out, not_125_out, not_126_out,
       not_127_out, not_128_out, not_129_out, not_130_out, not_131_out, not_132_out, not_133_out,
       not_134_out, not_135_out, not_136_out, not_137_out, not_138_out, not_139_out, not_140_out,
       not_141_out, not_142_out, not_143_out, not_144_out, not_145_out, not_146_out, not_147_out,
       not_148_out, not_149_out, not_150_out, not_151_out, not_152_out, not_153_out, not_154_out,
       not_155_out, not_156_out, not_157_out, not_158_out, not_159_out, not_160_out, not_161_out,
       not_162_out, not_163_out, not_164_out, not_165_out, not_166_out, not_167_out, not_168_out,
       not_169_out, not_170_out, not_171_out, not_172_out, not_173_out, not_174_out, not_175_out,
       not_176_out, not_177_out, not_178_out, not_179_out, not_180_out, not_181_out, not_182_out,
       not_183_out, not_184_out, not_185_out, not_186_out, not_187_out, not_188_out, not_189_out,
       not_190_out, not_191_out, not_192_out, not_193_out, not_194_out, not_195_out, not_196_out,
       not_197_out, not_198_out, not_199_out, not_200_out, not_201_out, not_202_out, not_203_out,
       not_204_out, not_205_out, not_206_out, not_207_out, not_208_out, not_209_out, not_210_out,
       not_211_out, not_212_out, not_213_out, not_214_out, not_215_out, not_216_out, not_217_out,
       not_218_out, not_219_out, not_220_out, not_221_out, not_222_out, not_223_out, not_224_out,
       not_225_out, not_226_out, not_227_out, not_228_out, not_229_out, not_230_out, not_231_out, not_232_out;

  not not_1 (not_1_out, F30);
  not not_2 (not_2_out, F25);
  not not_3 (not_3_out, F14);
  not not_4 (not_4_out, F13);
  not not_5 (not_5_out, F12);
  not not_6 (not_6_out, OP6);
  not not_7 (not_7_out, OP3);
  not not_8 (not_8_out, OP2);
  not not_9 (not_9_out, F30);
  not not_10 (not_10_out, F25);
  not not_11 (not_11_out, OP6);
  not not_12 (not_12_out, OP3);
  not not_13 (not_13_out, OP2);
  not not_14 (not_14_out, F30);
  not not_15 (not_15_out, F25);
  not not_16 (not_16_out, F14);
  not not_17 (not_17_out, F12);
  not not_18 (not_18_out, OP6);
  not not_19 (not_19_out, OP3);
  not not_20 (not_20_out, OP2);
  not not_21 (not_21_out, F14);
  not not_22 (not_22_out, F13);
  not not_23 (not_23_out, F12);
  not not_24 (not_24_out, OP6);
  not not_25 (not_25_out, OP5);
  not not_26 (not_26_out, OP3);
  not not_27 (not_27_out, OP2);
  not not_28 (not_28_out, OP6);
  not not_29 (not_29_out, OP5);
  not not_30 (not_30_out, OP3);
  not not_31 (not_31_out, OP2);
  not not_32 (not_32_out, F13);
  not not_33 (not_33_out, F12);
  not not_34 (not_34_out, OP6);
  not not_35 (not_35_out, OP5);
  not not_36 (not_36_out, OP3);
  not not_37 (not_37_out, OP2);
  not not_38 (not_38_out, F14);
  not not_39 (not_39_out, F12);
  not not_40 (not_40_out, OP6);
  not not_41 (not_41_out, OP5);
  not not_42 (not_42_out, OP3);
  not not_43 (not_43_out, OP2);
  not not_44 (not_44_out, F25);
  not not_45 (not_45_out, F13);
  not not_46 (not_46_out, OP6);
  not not_47 (not_47_out, OP5);
  not not_48 (not_48_out, OP3);
  not not_49 (not_49_out, OP2);
  not not_50 (not_50_out, F14);
  not not_51 (not_51_out, F12);
  not not_52 (not_52_out, OP6);
  not not_53 (not_53_out, OP5);
  not not_54 (not_54_out, OP4);
  not not_55 (not_55_out, OP3);
  not not_56 (not_56_out, OP2);
  not not_57 (not_57_out, F14);
  not not_58 (not_58_out, F12);
  not not_59 (not_59_out, OP6);
  not not_60 (not_60_out, OP4);
  not not_61 (not_61_out, OP3);
  not not_62 (not_62_out, OP2);
  not not_63 (not_63_out, F14);
  not not_64 (not_64_out, F13);
  not not_65 (not_65_out, F12);
  not not_66 (not_66_out, OP4);
  not not_67 (not_67_out, OP3);
  not not_68 (not_68_out, OP2);
  not not_69 (not_69_out, F14);
  not not_70 (not_70_out, F13);
  not not_71 (not_71_out, OP4);
  not not_72 (not_72_out, OP3);
  not not_73 (not_73_out, OP2);
  not not_74 (not_74_out, OP4);
  not not_75 (not_75_out, F14);
  not not_76 (not_76_out, F13);
  not not_77 (not_77_out, F12);
  not not_78 (not_78_out, OP4);
  not not_79 (not_79_out, OP3);
  not not_80 (not_80_out, F25);
  not not_81 (not_81_out, F14);
  not not_82 (not_82_out, F13);
  not not_83 (not_83_out, F12);
  not not_84 (not_84_out, OP6);
  not not_85 (not_85_out, OP3);
  not not_86 (not_86_out, OP2);
  not not_87 (not_87_out, F30);
  not not_88 (not_88_out, F25);
  not not_89 (not_89_out, OP6);
  not not_90 (not_90_out, OP3);
  not not_91 (not_91_out, OP2);
  not not_92 (not_92_out, F30);
  not not_93 (not_93_out, F25);
  not not_94 (not_94_out, F14);
  not not_95 (not_95_out, F12);
  not not_96 (not_96_out, OP6);
  not not_97 (not_97_out, OP3);
  not not_98 (not_98_out, OP2);
  not not_99 (not_99_out, OP6);
  not not_100 (not_100_out, OP5);
  not not_101 (not_101_out, OP3);
  not not_102 (not_102_out, OP2);
  not not_103 (not_103_out, F14);
  not not_104 (not_104_out, F12);
  not not_105 (not_105_out, OP6);
  not not_106 (not_106_out, OP5);
  not not_107 (not_107_out, OP3);
  not not_108 (not_108_out, OP2);
  not not_109 (not_109_out, F30);
  not not_110 (not_110_out, F25);
  not not_111 (not_111_out, F13);
  not not_112 (not_112_out, OP6);
  not not_113 (not_113_out, OP5);
  not not_114 (not_114_out, OP3);
  not not_115 (not_115_out, OP2);
  not not_116 (not_116_out, F30);
  not not_117 (not_117_out, F25);
  not not_118 (not_118_out, F13);
  not not_119 (not_119_out, OP6);
  not not_120 (not_120_out, OP3);
  not not_121 (not_121_out, OP2);
  not not_122 (not_122_out, F30);
  not not_123 (not_123_out, F25);
  not not_124 (not_124_out, F14);
  not not_125 (not_125_out, F13);
  not not_126 (not_126_out, F12);
  not not_127 (not_127_out, OP6);
  not not_128 (not_128_out, OP3);
  not not_129 (not_129_out, OP2);
  not not_130 (not_130_out, F25);
  not not_131 (not_131_out, F14);
  not not_132 (not_132_out, F13);
  not not_133 (not_133_out, F12);
  not not_134 (not_134_out, OP6);
  not not_135 (not_135_out, OP3);
  not not_136 (not_136_out, OP2);
  not not_137 (not_137_out, F30);
  not not_138 (not_138_out, F25);
  not not_139 (not_139_out, OP6);
  not not_140 (not_140_out, OP3);
  not not_141 (not_141_out, OP2);
  not not_142 (not_142_out, F30);
  not not_143 (not_143_out, F25);
  not not_144 (not_144_out, F14);
  not not_145 (not_145_out, OP6);
  not not_146 (not_146_out, OP3);
  not not_147 (not_147_out, OP2);
  not not_148 (not_148_out, F14);
  not not_149 (not_149_out, F13);
  not not_150 (not_150_out, F12);
  not not_151 (not_151_out, OP6);
  not not_152 (not_152_out, OP5);
  not not_153 (not_153_out, OP3);
  not not_154 (not_154_out, OP2);
  not not_155 (not_155_out, OP6);
  not not_156 (not_156_out, OP5);
  not not_157 (not_157_out, OP3);
  not not_158 (not_158_out, OP2);
  not not_159 (not_159_out, F14);
  not not_160 (not_160_out, F12);
  not not_161 (not_161_out, OP6);
  not not_162 (not_162_out, OP5);
  not not_163 (not_163_out, OP4);
  not not_164 (not_164_out, OP3);
  not not_165 (not_165_out, OP2);
  not not_166 (not_166_out, F14);
  not not_167 (not_167_out, F12);
  not not_168 (not_168_out, OP6);
  not not_169 (not_169_out, OP4);
  not not_170 (not_170_out, OP3);
  not not_171 (not_171_out, OP2);
  not not_172 (not_172_out, F14);
  not not_173 (not_173_out, F13);
  not not_174 (not_174_out, F12);
  not not_175 (not_175_out, OP4);
  not not_176 (not_176_out, OP3);
  not not_177 (not_177_out, OP2);
  not not_178 (not_178_out, F14);
  not not_179 (not_179_out, F13);
  not not_180 (not_180_out, OP4);
  not not_181 (not_181_out, OP3);
  not not_182 (not_182_out, OP2);
  not not_183 (not_183_out, OP4);
  not not_184 (not_184_out, F14);
  not not_185 (not_185_out, F13);
  not not_186 (not_186_out, F12);
  not not_187 (not_187_out, OP4);
  not not_188 (not_188_out, OP3);
  not not_189 (not_189_out, F12);
  not not_190 (not_190_out, OP4);
  not not_191 (not_191_out, OP3);
  not not_192 (not_192_out, OP2);
  not not_193 (not_193_out, F30);
  not not_194 (not_194_out, F25);
  not not_195 (not_195_out, F12);
  not not_196 (not_196_out, OP6);
  not not_197 (not_197_out, OP3);
  not not_198 (not_198_out, OP2);
  not not_199 (not_199_out, F30);
  not not_200 (not_200_out, F25);
  not not_201 (not_201_out, F14);
  not not_202 (not_202_out, F12);
  not not_203 (not_203_out, OP6);
  not not_204 (not_204_out, OP3);
  not not_205 (not_205_out, OP2);
  not not_206 (not_206_out, F30);
  not not_207 (not_207_out, F25);
  not not_208 (not_208_out, F14);
  not not_209 (not_209_out, OP6);
  not not_210 (not_210_out, OP3);
  not not_211 (not_211_out, OP2);
  not not_212 (not_212_out, F12);
  not not_213 (not_213_out, OP6);
  not not_214 (not_214_out, OP5);
  not not_215 (not_215_out, OP3);
  not not_216 (not_216_out, OP2);
  not not_217 (not_217_out, F13);
  not not_218 (not_218_out, F12);
  not not_219 (not_219_out, OP6);
  not not_220 (not_220_out, OP5);
  not not_221 (not_221_out, OP3);
  not not_222 (not_222_out, OP2);
  not not_223 (not_223_out, F14);
  not not_224 (not_224_out, F12);
  not not_225 (not_225_out, OP6);
  not not_226 (not_226_out, OP5);
  not not_227 (not_227_out, OP3);
  not not_228 (not_228_out, OP2);
  not not_229 (not_229_out, F12);
  not not_230 (not_230_out, OP4);
  not not_231 (not_231_out, OP3);
  not not_232 (not_232_out, OP2);
  and and_1 (and_1_out, not_1_out, not_2_out, not_3_out, not_4_out, not_5_out, not_6_out, OP5, OP4, not_7_out, not_8_out);
  and and_2 (and_2_out, not_9_out, not_10_out, F14, F13, F12, not_11_out, OP5, OP4, not_12_out, not_13_out);
  and and_3 (and_3_out, not_14_out, not_15_out, not_16_out, F13, not_17_out, not_18_out, OP5, OP4, not_19_out, not_20_out);
  and and_4 (and_4_out, not_21_out, not_22_out, not_23_out, not_24_out, not_25_out, OP4, not_26_out, not_27_out);
  and and_5 (and_5_out, F14, F13, F12, not_28_out, not_29_out, OP4, not_30_out, not_31_out);
  and and_6 (and_6_out, F14, not_32_out, not_33_out, not_34_out, not_35_out, OP4, not_36_out, not_37_out);
  and and_7 (and_7_out, not_38_out, F13, not_39_out, not_40_out, not_41_out, OP4, not_42_out, not_43_out);
  and and_8 (and_8_out, F30, not_44_out, F14, not_45_out, F12, not_46_out, not_47_out, OP4, not_48_out, not_49_out);
  and and_9 (and_9_out, not_50_out, F13, not_51_out, not_52_out, not_53_out, not_54_out, not_55_out, not_56_out);
  and and_10 (and_10_out, not_57_out, F13, not_58_out, not_59_out, OP5, not_60_out, not_61_out, not_62_out);
  and and_11 (and_11_out, not_63_out, not_64_out, not_65_out, OP6, OP5, not_66_out, not_67_out, not_68_out);
  and and_12 (and_12_out, not_69_out, not_70_out, F12, OP6, OP5, not_71_out, not_72_out, not_73_out);
  and and_13 (and_13_out, OP6, OP5, not_74_out, OP3, OP2);
  and and_14 (and_14_out, not_75_out, not_76_out, not_77_out, OP6, OP5, not_78_out, not_79_out, OP2);
  and and_15 (and_15_out, F30, not_80_out, not_81_out, not_82_out, not_83_out, not_84_out, OP5, OP4, not_85_out, not_86_out);
  and and_16 (and_16_out, not_87_out, not_88_out, F14, F13, F12, not_89_out, OP5, OP4, not_90_out, not_91_out);
  and and_17 (and_17_out, not_92_out, not_93_out, not_94_out, F13, not_95_out, not_96_out, OP5, OP4, not_97_out, not_98_out);
  and and_18 (and_18_out, F14, F13, F12, not_99_out, not_100_out, OP4, not_101_out, not_102_out);
  and and_19 (and_19_out, not_103_out, F13, not_104_out, not_105_out, not_106_out, OP4, not_107_out, not_108_out);
  and and_20 (and_20_out, not_109_out, not_110_out, F14, not_111_out, F12, not_112_out, not_113_out, OP4, not_114_out, not_115_out);
  and and_21 (and_21_out, not_116_out, not_117_out, F14, not_118_out, F12, not_119_out, OP5, OP4, not_120_out, not_121_out);
  and and_22 (and_22_out, not_122_out, not_123_out, not_124_out, not_125_out, not_126_out, not_127_out, OP5, OP4, not_128_out, not_129_out);
  and and_23 (and_23_out, F30, not_130_out, not_131_out, not_132_out, not_133_out, not_134_out, OP5, OP4, not_135_out, not_136_out);
  and and_24 (and_24_out, not_137_out, not_138_out, F14, F13, F12, not_139_out, OP5, OP4, not_140_out, not_141_out);
  and and_25 (and_25_out, not_142_out, not_143_out, not_144_out, F13, F12, not_145_out, OP5, OP4, not_146_out, not_147_out);
  and and_26 (and_26_out, not_148_out, not_149_out, not_150_out, not_151_out, not_152_out, OP4, not_153_out, not_154_out);
  and and_27 (and_27_out, F14, F13, F12, not_155_out, not_156_out, OP4, not_157_out, not_158_out);
  and and_28 (and_28_out, not_159_out, F13, not_160_out, not_161_out, not_162_out, not_163_out, not_164_out, not_165_out);
  and and_29 (and_29_out, not_166_out, F13, not_167_out, not_168_out, OP5, not_169_out, not_170_out, not_171_out);
  and and_30 (and_30_out, not_172_out, not_173_out, not_174_out, OP6, OP5, not_175_out, not_176_out, not_177_out);
  and and_31 (and_31_out, not_178_out, not_179_out, F12, OP6, OP5, not_180_out, not_181_out, not_182_out);
  and and_32 (and_32_out, OP6, OP5, not_183_out, OP3, OP2);
  and and_33 (and_33_out, not_184_out, not_185_out, not_186_out, OP6, OP5, not_187_out, not_188_out, OP2);
  and and_34 (and_34_out, F14, F13, not_189_out, OP6, OP5, not_190_out, not_191_out, not_192_out);
  and and_35 (and_35_out, not_193_out, not_194_out, F14, F13, not_195_out, not_196_out, OP5, OP4, not_197_out, not_198_out);
  and and_36 (and_36_out, not_199_out, not_200_out, not_201_out, F13, not_202_out, not_203_out, OP5, OP4, not_204_out, not_205_out);
  and and_37 (and_37_out, not_206_out, not_207_out, not_208_out, F13, F12, not_209_out, OP5, OP4, not_210_out, not_211_out);
  and and_38 (and_38_out, F14, F13, not_212_out, not_213_out, not_214_out, OP4, not_215_out, not_216_out);
  and and_39 (and_39_out, F14, not_217_out, not_218_out, not_219_out, not_220_out, OP4, not_221_out, not_222_out);
  and and_40 (and_40_out, not_223_out, F13, not_224_out, not_225_out, not_226_out, OP4, not_227_out, not_228_out);
  and and_41 (and_41_out, F14, F13, not_229_out, OP6, OP5, not_230_out, not_231_out, not_232_out);
  or or_1 (S0, and_1_out, and_2_out, and_3_out, and_4_out, and_5_out, and_6_out, and_7_out, and_8_out, and_9_out, and_10_out, and_11_out, and_12_out, and_13_out, and_14_out);
  or or_2 (S1, and_15_out, and_16_out, and_17_out, and_18_out, and_19_out, and_20_out, and_21_out);
  or or_3 (S2, and_22_out, and_23_out, and_24_out, and_25_out, and_26_out, and_27_out, and_28_out, and_29_out, and_30_out, and_31_out, and_32_out, and_33_out, and_34_out);
  or or_4 (S3, and_35_out, and_36_out, and_37_out, and_38_out, and_39_out, and_40_out, and_41_out);
endmodule

// 控制信号生成
module \控制信号自动生成  (
  input  OP2,
  input  OP3,
  input  OP4,
  input  OP5,
  input  OP6,
  input  F12,
  input  F13,
  input  F14,
  input  F25,
  input  F30,
  output MemToReg,
  output MemWrite,
  output ALU_SRC,
  output RegWrite,
  output ecall,
  output S_Type,
  output BEQ,
  output BNE,
  output JALR,
  output JAL,
  output BLTU,
  output U_Type,
  output LBU,
  output R1,
  output R2,
  output CSRRSI,
  output CSRRCI
);

  wire and_1_out, and_2_out, and_4_out, and_5_out, and_6_out, and_7_out, and_8_out, and_9_out, and_10_out,
       and_11_out, and_12_out, and_13_out, and_14_out, and_15_out, and_16_out, and_17_out, and_18_out,
       and_19_out, and_20_out, and_21_out, and_22_out, and_23_out, and_24_out, and_25_out, and_26_out,
       and_27_out, and_28_out, and_29_out, and_30_out, and_31_out, and_32_out, and_33_out, and_34_out,
       and_35_out, and_36_out, and_37_out, and_46_out, and_47_out, and_48_out, and_49_out, and_50_out,
       and_51_out, and_52_out, and_53_out, and_54_out, and_55_out, and_56_out, and_57_out, and_58_out,
       and_59_out, and_60_out, and_61_out, and_62_out, and_63_out, and_64_out, and_65_out, and_66_out,
       and_67_out, and_68_out, and_69_out, and_70_out, and_71_out, and_72_out, and_73_out, and_74_out,
       and_75_out, and_76_out, and_77_out, and_78_out, and_79_out, and_80_out, not_1_out, not_2_out,
       not_3_out, not_4_out, not_5_out, not_6_out, not_7_out, not_8_out, not_9_out, not_10_out, not_11_out,
       not_12_out, not_13_out, not_14_out, not_15_out, not_16_out, not_17_out, not_18_out, not_19_out,
       not_20_out, not_21_out, not_22_out, not_23_out, not_24_out, not_25_out, not_26_out, not_27_out,
       not_28_out, not_29_out, not_30_out, not_31_out, not_32_out, not_33_out, not_34_out, not_35_out,
       not_36_out, not_37_out, not_38_out, not_39_out, not_40_out, not_41_out, not_42_out, not_43_out,
       not_44_out, not_45_out, not_46_out, not_47_out, not_48_out, not_49_out, not_50_out, not_51_out,
       not_52_out, not_53_out, not_54_out, not_55_out, not_56_out, not_57_out, not_58_out, not_59_out,
       not_60_out, not_61_out, not_62_out, not_63_out, not_64_out, not_65_out, not_66_out, not_67_out,
       not_68_out, not_69_out, not_70_out, not_71_out, not_72_out, not_73_out, not_74_out, not_75_out,
       not_76_out, not_77_out, not_78_out, not_79_out, not_80_out, not_81_out, not_82_out, not_83_out,
       not_84_out, not_85_out, not_86_out, not_87_out, not_88_out, not_89_out, not_90_out, not_91_out,
       not_92_out, not_93_out, not_94_out, not_95_out, not_96_out, not_97_out, not_98_out, not_99_out,
       not_100_out, not_101_out, not_102_out, not_103_out, not_104_out, not_105_out, not_106_out,
       not_107_out, not_108_out, not_109_out, not_110_out, not_111_out, not_112_out, not_113_out,
       not_114_out, not_115_out, not_116_out, not_117_out, not_118_out, not_119_out, not_120_out,
       not_121_out, not_122_out, not_123_out, not_124_out, not_125_out, not_126_out, not_127_out,
       not_128_out, not_129_out, not_130_out, not_131_out, not_132_out, not_133_out, not_134_out,
       not_135_out, not_136_out, not_137_out, not_138_out, not_139_out, not_140_out, not_141_out,
       not_142_out, not_143_out, not_144_out, not_145_out, not_146_out, not_147_out, not_148_out,
       not_149_out, not_150_out, not_151_out, not_152_out, not_153_out, not_154_out, not_155_out,
       not_156_out, not_157_out, not_158_out, not_159_out, not_160_out, not_161_out, not_162_out,
       not_163_out, not_164_out, not_165_out, not_166_out, not_167_out, not_168_out, not_169_out,
       not_170_out, not_171_out, not_172_out, not_173_out, not_174_out, not_175_out, not_176_out,
       not_177_out, not_178_out, not_179_out, not_180_out, not_181_out, not_182_out, not_183_out,
       not_184_out, not_185_out, not_186_out, not_187_out, not_188_out, not_189_out, not_190_out,
       not_191_out, not_192_out, not_193_out, not_194_out, not_195_out, not_196_out, not_197_out,
       not_198_out, not_199_out, not_200_out, not_201_out, not_202_out, not_203_out, not_204_out,
       not_205_out, not_206_out, not_207_out, not_208_out, not_209_out, not_210_out, not_211_out,
       not_212_out, not_213_out, not_214_out, not_215_out, not_216_out, not_217_out, not_218_out,
       not_219_out, not_220_out, not_221_out, not_222_out, not_223_out, not_224_out, not_225_out,
       not_226_out, not_227_out, not_228_out, not_229_out, not_230_out, not_231_out, not_232_out,
       not_233_out, not_234_out, not_235_out, not_236_out, not_237_out, not_238_out, not_239_out,
       not_240_out, not_241_out, not_242_out, not_243_out, not_244_out, not_245_out, not_246_out,
       not_247_out, not_248_out, not_249_out, not_250_out, not_251_out, not_252_out, not_253_out,
       not_254_out, not_255_out, not_256_out, not_257_out, not_258_out, not_259_out, not_260_out,
       not_261_out, not_262_out, not_263_out, not_264_out, not_265_out, not_266_out, not_267_out,
       not_268_out, not_269_out, not_270_out, not_271_out, not_272_out, not_273_out, not_274_out,
       not_275_out, not_276_out, not_277_out, not_278_out, not_279_out, not_280_out, not_281_out,
       not_282_out, not_283_out, not_284_out, not_285_out, not_286_out, not_287_out, not_288_out,
       not_289_out, not_290_out, not_291_out, not_292_out, not_293_out, not_294_out, not_295_out,
       not_296_out, not_297_out, not_298_out, not_299_out, not_300_out, not_301_out, not_302_out,
       not_303_out, not_304_out, not_305_out, not_306_out, not_307_out, not_308_out, not_309_out,
       not_310_out, not_311_out, not_312_out, not_313_out, not_314_out, not_315_out, not_316_out,
       not_317_out, not_318_out, not_319_out, not_320_out, not_321_out, not_322_out, not_323_out,
       not_324_out, not_325_out, not_326_out, not_327_out, not_328_out, not_329_out, not_330_out,
       not_331_out, not_332_out, not_333_out, not_334_out, not_335_out, not_336_out, not_337_out,
       not_338_out, not_339_out, not_340_out, not_341_out, not_342_out, not_343_out, not_344_out,
       not_345_out, not_346_out, not_347_out, not_348_out, not_349_out, not_350_out, not_351_out,
       not_352_out, not_353_out, not_354_out, not_355_out, not_356_out, not_357_out, not_358_out,
       not_359_out, not_360_out, not_361_out, not_362_out, not_363_out, not_364_out, not_365_out,
       not_366_out, not_367_out, not_368_out, not_369_out, not_370_out, not_371_out, not_372_out,
       not_373_out, not_374_out, not_375_out, not_376_out, not_377_out, not_378_out, not_379_out,
       not_380_out, not_381_out, not_382_out, not_383_out, not_384_out, not_385_out, not_386_out,
       not_387_out, not_388_out, not_389_out, not_390_out, not_391_out, not_392_out, not_393_out,
       not_394_out, not_395_out, not_396_out, not_397_out, not_398_out, not_399_out, not_400_out,
       not_401_out, not_402_out, not_403_out, not_404_out, not_405_out, not_406_out, not_407_out,
       not_408_out, not_409_out, not_410_out, not_411_out, not_412_out, not_413_out, not_414_out,
       not_415_out, not_416_out, not_417_out, not_418_out, not_419_out, not_420_out, not_421_out,
       not_422_out, not_423_out, not_424_out, not_425_out, not_426_out, not_427_out, not_428_out,
       not_429_out, not_430_out, not_431_out, not_432_out, not_433_out, not_434_out, not_435_out,
       not_436_out, not_437_out, not_438_out, not_439_out, not_440_out, not_441_out, not_442_out,
       not_443_out, not_444_out, not_445_out, not_446_out, not_447_out, not_448_out, not_449_out,
       not_450_out, not_451_out, not_452_out, not_453_out, not_454_out, not_455_out, not_456_out,
       not_457_out, not_458_out, not_459_out, not_460_out, not_461_out, not_462_out, not_463_out,
       not_464_out, not_465_out, not_466_out, not_467_out, not_468_out, not_469_out, not_470_out,
       not_471_out, not_472_out, not_473_out, not_474_out, not_475_out, not_476_out, not_477_out,
       not_478_out, not_479_out, not_480_out, not_481_out;

  not not_1 (not_1_out, F14);
  not not_2 (not_2_out, F12);
  not not_3 (not_3_out, OP6);
  not not_4 (not_4_out, OP5);
  not not_5 (not_5_out, OP4);
  not not_6 (not_6_out, OP3);
  not not_7 (not_7_out, OP2);
  not not_8 (not_8_out, F13);
  not not_9 (not_9_out, F12);
  not not_10 (not_10_out, OP6);
  not not_11 (not_11_out, OP5);
  not not_12 (not_12_out, OP4);
  not not_13 (not_13_out, OP3);
  not not_14 (not_14_out, OP2);
  not not_15 (not_15_out, F14);
  not not_16 (not_16_out, F12);
  not not_17 (not_17_out, OP6);
  not not_18 (not_18_out, OP4);
  not not_19 (not_19_out, OP3);
  not not_20 (not_20_out, OP2);
  not not_21 (not_21_out, F14);
  not not_22 (not_22_out, F13);
  not not_23 (not_23_out, F12);
  not not_24 (not_24_out, OP6);
  not not_25 (not_25_out, OP5);
  not not_26 (not_26_out, OP3);
  not not_27 (not_27_out, OP2);
  not not_28 (not_28_out, OP6);
  not not_29 (not_29_out, OP5);
  not not_30 (not_30_out, OP3);
  not not_31 (not_31_out, OP2);
  not not_32 (not_32_out, F12);
  not not_33 (not_33_out, OP6);
  not not_34 (not_34_out, OP5);
  not not_35 (not_35_out, OP3);
  not not_36 (not_36_out, OP2);
  not not_37 (not_37_out, F13);
  not not_38 (not_38_out, F12);
  not not_39 (not_39_out, OP6);
  not not_40 (not_40_out, OP5);
  not not_41 (not_41_out, OP3);
  not not_42 (not_42_out, OP2);
  not not_43 (not_43_out, F14);
  not not_44 (not_44_out, F12);
  not not_45 (not_45_out, OP6);
  not not_46 (not_46_out, OP5);
  not not_47 (not_47_out, OP3);
  not not_48 (not_48_out, OP2);
  not not_49 (not_49_out, F30);
  not not_50 (not_50_out, F25);
  not not_51 (not_51_out, F14);
  not not_52 (not_52_out, F13);
  not not_53 (not_53_out, OP6);
  not not_54 (not_54_out, OP5);
  not not_55 (not_55_out, OP3);
  not not_56 (not_56_out, OP2);
  not not_57 (not_57_out, F30);
  not not_58 (not_58_out, F25);
  not not_59 (not_59_out, F13);
  not not_60 (not_60_out, OP6);
  not not_61 (not_61_out, OP5);
  not not_62 (not_62_out, OP3);
  not not_63 (not_63_out, OP2);
  not not_64 (not_64_out, F25);
  not not_65 (not_65_out, F13);
  not not_66 (not_66_out, OP6);
  not not_67 (not_67_out, OP5);
  not not_68 (not_68_out, OP3);
  not not_69 (not_69_out, OP2);
  not not_70 (not_70_out, F14);
  not not_71 (not_71_out, F12);
  not not_72 (not_72_out, OP6);
  not not_73 (not_73_out, OP5);
  not not_74 (not_74_out, OP4);
  not not_75 (not_75_out, OP3);
  not not_76 (not_76_out, OP2);
  not not_77 (not_77_out, F14);
  not not_78 (not_78_out, F12);
  not not_79 (not_79_out, OP6);
  not not_80 (not_80_out, OP4);
  not not_81 (not_81_out, OP3);
  not not_82 (not_82_out, OP2);
  not not_83 (not_83_out, F14);
  not not_84 (not_84_out, F13);
  not not_85 (not_85_out, F12);
  not not_86 (not_86_out, OP4);
  not not_87 (not_87_out, OP3);
  not not_88 (not_88_out, F13);
  not not_89 (not_89_out, F12);
  not not_90 (not_90_out, OP6);
  not not_91 (not_91_out, OP5);
  not not_92 (not_92_out, OP4);
  not not_93 (not_93_out, OP3);
  not not_94 (not_94_out, OP2);
  not not_95 (not_95_out, F30);
  not not_96 (not_96_out, F25);
  not not_97 (not_97_out, F14);
  not not_98 (not_98_out, F13);
  not not_99 (not_99_out, F12);
  not not_100 (not_100_out, OP6);
  not not_101 (not_101_out, OP3);
  not not_102 (not_102_out, OP2);
  not not_103 (not_103_out, F25);
  not not_104 (not_104_out, F14);
  not not_105 (not_105_out, F13);
  not not_106 (not_106_out, F12);
  not not_107 (not_107_out, OP6);
  not not_108 (not_108_out, OP3);
  not not_109 (not_109_out, OP2);
  not not_110 (not_110_out, F30);
  not not_111 (not_111_out, F25);
  not not_112 (not_112_out, OP6);
  not not_113 (not_113_out, OP3);
  not not_114 (not_114_out, OP2);
  not not_115 (not_115_out, F30);
  not not_116 (not_116_out, F25);
  not not_117 (not_117_out, F12);
  not not_118 (not_118_out, OP6);
  not not_119 (not_119_out, OP3);
  not not_120 (not_120_out, OP2);
  not not_121 (not_121_out, F30);
  not not_122 (not_122_out, F25);
  not not_123 (not_123_out, F14);
  not not_124 (not_124_out, F12);
  not not_125 (not_125_out, OP6);
  not not_126 (not_126_out, OP3);
  not not_127 (not_127_out, OP2);
  not not_128 (not_128_out, F30);
  not not_129 (not_129_out, F25);
  not not_130 (not_130_out, F14);
  not not_131 (not_131_out, OP6);
  not not_132 (not_132_out, OP3);
  not not_133 (not_133_out, OP2);
  not not_134 (not_134_out, F14);
  not not_135 (not_135_out, F13);
  not not_136 (not_136_out, F12);
  not not_137 (not_137_out, OP6);
  not not_138 (not_138_out, OP5);
  not not_139 (not_139_out, OP3);
  not not_140 (not_140_out, OP2);
  not not_141 (not_141_out, OP6);
  not not_142 (not_142_out, OP5);
  not not_143 (not_143_out, OP3);
  not not_144 (not_144_out, OP2);
  not not_145 (not_145_out, F12);
  not not_146 (not_146_out, OP6);
  not not_147 (not_147_out, OP5);
  not not_148 (not_148_out, OP3);
  not not_149 (not_149_out, OP2);
  not not_150 (not_150_out, F13);
  not not_151 (not_151_out, F12);
  not not_152 (not_152_out, OP6);
  not not_153 (not_153_out, OP5);
  not not_154 (not_154_out, OP3);
  not not_155 (not_155_out, OP2);
  not not_156 (not_156_out, F14);
  not not_157 (not_157_out, F12);
  not not_158 (not_158_out, OP6);
  not not_159 (not_159_out, OP5);
  not not_160 (not_160_out, OP3);
  not not_161 (not_161_out, OP2);
  not not_162 (not_162_out, F30);
  not not_163 (not_163_out, F25);
  not not_164 (not_164_out, F14);
  not not_165 (not_165_out, F13);
  not not_166 (not_166_out, OP6);
  not not_167 (not_167_out, OP5);
  not not_168 (not_168_out, OP3);
  not not_169 (not_169_out, OP2);
  not not_170 (not_170_out, F30);
  not not_171 (not_171_out, F25);
  not not_172 (not_172_out, F13);
  not not_173 (not_173_out, OP6);
  not not_174 (not_174_out, OP5);
  not not_175 (not_175_out, OP3);
  not not_176 (not_176_out, OP2);
  not not_177 (not_177_out, F25);
  not not_178 (not_178_out, F13);
  not not_179 (not_179_out, OP6);
  not not_180 (not_180_out, OP5);
  not not_181 (not_181_out, OP3);
  not not_182 (not_182_out, OP2);
  not not_183 (not_183_out, F14);
  not not_184 (not_184_out, F12);
  not not_185 (not_185_out, OP6);
  not not_186 (not_186_out, OP5);
  not not_187 (not_187_out, OP4);
  not not_188 (not_188_out, OP3);
  not not_189 (not_189_out, OP2);
  not not_190 (not_190_out, OP4);
  not not_191 (not_191_out, F14);
  not not_192 (not_192_out, F13);
  not not_193 (not_193_out, F12);
  not not_194 (not_194_out, OP4);
  not not_195 (not_195_out, OP3);
  not not_196 (not_196_out, F30);
  not not_197 (not_197_out, F25);
  not not_198 (not_198_out, F13);
  not not_199 (not_199_out, OP6);
  not not_200 (not_200_out, OP3);
  not not_201 (not_201_out, OP2);
  not not_202 (not_202_out, OP6);
  not not_203 (not_203_out, OP5);
  not not_204 (not_204_out, OP3);
  not not_205 (not_205_out, F13);
  not not_206 (not_206_out, F12);
  not not_207 (not_207_out, OP6);
  not not_208 (not_208_out, OP5);
  not not_209 (not_209_out, OP4);
  not not_210 (not_210_out, OP3);
  not not_211 (not_211_out, OP2);
  not not_212 (not_212_out, F30);
  not not_213 (not_213_out, F25);
  not not_214 (not_214_out, F14);
  not not_215 (not_215_out, F13);
  not not_216 (not_216_out, F12);
  not not_217 (not_217_out, OP3);
  not not_218 (not_218_out, OP2);
  not not_219 (not_219_out, F30);
  not not_220 (not_220_out, F25);
  not not_221 (not_221_out, F14);
  not not_222 (not_222_out, F13);
  not not_223 (not_223_out, F12);
  not not_224 (not_224_out, OP3);
  not not_225 (not_225_out, OP2);
  not not_226 (not_226_out, F14);
  not not_227 (not_227_out, F12);
  not not_228 (not_228_out, OP6);
  not not_229 (not_229_out, OP4);
  not not_230 (not_230_out, OP3);
  not not_231 (not_231_out, OP2);
  not not_232 (not_232_out, F14);
  not not_233 (not_233_out, F13);
  not not_234 (not_234_out, F12);
  not not_235 (not_235_out, OP4);
  not not_236 (not_236_out, OP3);
  not not_237 (not_237_out, OP2);
  not not_238 (not_238_out, F14);
  not not_239 (not_239_out, F13);
  not not_240 (not_240_out, OP4);
  not not_241 (not_241_out, OP3);
  not not_242 (not_242_out, OP2);
  not not_243 (not_243_out, F14);
  not not_244 (not_244_out, F13);
  not not_245 (not_245_out, F12);
  not not_246 (not_246_out, OP4);
  not not_247 (not_247_out, OP3);
  not not_248 (not_248_out, OP4);
  not not_249 (not_249_out, F12);
  not not_250 (not_250_out, OP4);
  not not_251 (not_251_out, OP3);
  not not_252 (not_252_out, OP2);
  not not_253 (not_253_out, OP6);
  not not_254 (not_254_out, OP5);
  not not_255 (not_255_out, OP3);
  not not_256 (not_256_out, F13);
  not not_257 (not_257_out, F12);
  not not_258 (not_258_out, OP6);
  not not_259 (not_259_out, OP5);
  not not_260 (not_260_out, OP4);
  not not_261 (not_261_out, OP3);
  not not_262 (not_262_out, OP2);
  not not_263 (not_263_out, F30);
  not not_264 (not_264_out, F25);
  not not_265 (not_265_out, F14);
  not not_266 (not_266_out, F13);
  not not_267 (not_267_out, F12);
  not not_268 (not_268_out, OP6);
  not not_269 (not_269_out, OP3);
  not not_270 (not_270_out, OP2);
  not not_271 (not_271_out, F25);
  not not_272 (not_272_out, F14);
  not not_273 (not_273_out, F13);
  not not_274 (not_274_out, F12);
  not not_275 (not_275_out, OP6);
  not not_276 (not_276_out, OP3);
  not not_277 (not_277_out, OP2);
  not not_278 (not_278_out, F30);
  not not_279 (not_279_out, F25);
  not not_280 (not_280_out, OP6);
  not not_281 (not_281_out, OP3);
  not not_282 (not_282_out, OP2);
  not not_283 (not_283_out, F30);
  not not_284 (not_284_out, F25);
  not not_285 (not_285_out, F12);
  not not_286 (not_286_out, OP6);
  not not_287 (not_287_out, OP3);
  not not_288 (not_288_out, OP2);
  not not_289 (not_289_out, F30);
  not not_290 (not_290_out, F25);
  not not_291 (not_291_out, F14);
  not not_292 (not_292_out, F12);
  not not_293 (not_293_out, OP6);
  not not_294 (not_294_out, OP3);
  not not_295 (not_295_out, OP2);
  not not_296 (not_296_out, F30);
  not not_297 (not_297_out, F25);
  not not_298 (not_298_out, F14);
  not not_299 (not_299_out, OP6);
  not not_300 (not_300_out, OP3);
  not not_301 (not_301_out, OP2);
  not not_302 (not_302_out, F14);
  not not_303 (not_303_out, F13);
  not not_304 (not_304_out, F12);
  not not_305 (not_305_out, OP6);
  not not_306 (not_306_out, OP5);
  not not_307 (not_307_out, OP3);
  not not_308 (not_308_out, OP2);
  not not_309 (not_309_out, OP6);
  not not_310 (not_310_out, OP5);
  not not_311 (not_311_out, OP3);
  not not_312 (not_312_out, OP2);
  not not_313 (not_313_out, F12);
  not not_314 (not_314_out, OP6);
  not not_315 (not_315_out, OP5);
  not not_316 (not_316_out, OP3);
  not not_317 (not_317_out, OP2);
  not not_318 (not_318_out, F13);
  not not_319 (not_319_out, F12);
  not not_320 (not_320_out, OP6);
  not not_321 (not_321_out, OP5);
  not not_322 (not_322_out, OP3);
  not not_323 (not_323_out, OP2);
  not not_324 (not_324_out, F14);
  not not_325 (not_325_out, F12);
  not not_326 (not_326_out, OP6);
  not not_327 (not_327_out, OP5);
  not not_328 (not_328_out, OP3);
  not not_329 (not_329_out, OP2);
  not not_330 (not_330_out, F30);
  not not_331 (not_331_out, F25);
  not not_332 (not_332_out, F14);
  not not_333 (not_333_out, F13);
  not not_334 (not_334_out, OP6);
  not not_335 (not_335_out, OP5);
  not not_336 (not_336_out, OP3);
  not not_337 (not_337_out, OP2);
  not not_338 (not_338_out, F30);
  not not_339 (not_339_out, F25);
  not not_340 (not_340_out, F13);
  not not_341 (not_341_out, OP6);
  not not_342 (not_342_out, OP5);
  not not_343 (not_343_out, OP3);
  not not_344 (not_344_out, OP2);
  not not_345 (not_345_out, F25);
  not not_346 (not_346_out, F13);
  not not_347 (not_347_out, OP6);
  not not_348 (not_348_out, OP5);
  not not_349 (not_349_out, OP3);
  not not_350 (not_350_out, OP2);
  not not_351 (not_351_out, F14);
  not not_352 (not_352_out, F12);
  not not_353 (not_353_out, OP6);
  not not_354 (not_354_out, OP5);
  not not_355 (not_355_out, OP4);
  not not_356 (not_356_out, OP3);
  not not_357 (not_357_out, OP2);
  not not_358 (not_358_out, F14);
  not not_359 (not_359_out, F12);
  not not_360 (not_360_out, OP6);
  not not_361 (not_361_out, OP4);
  not not_362 (not_362_out, OP3);
  not not_363 (not_363_out, OP2);
  not not_364 (not_364_out, F30);
  not not_365 (not_365_out, F25);
  not not_366 (not_366_out, F14);
  not not_367 (not_367_out, F13);
  not not_368 (not_368_out, F12);
  not not_369 (not_369_out, OP3);
  not not_370 (not_370_out, OP2);
  not not_371 (not_371_out, F14);
  not not_372 (not_372_out, F13);
  not not_373 (not_373_out, F12);
  not not_374 (not_374_out, OP4);
  not not_375 (not_375_out, OP3);
  not not_376 (not_376_out, OP2);
  not not_377 (not_377_out, F14);
  not not_378 (not_378_out, F13);
  not not_379 (not_379_out, OP4);
  not not_380 (not_380_out, OP3);
  not not_381 (not_381_out, OP2);
  not not_382 (not_382_out, F14);
  not not_383 (not_383_out, F13);
  not not_384 (not_384_out, F12);
  not not_385 (not_385_out, OP4);
  not not_386 (not_386_out, OP3);
  not not_387 (not_387_out, F30);
  not not_388 (not_388_out, F25);
  not not_389 (not_389_out, F13);
  not not_390 (not_390_out, OP6);
  not not_391 (not_391_out, OP3);
  not not_392 (not_392_out, OP2);
  not not_393 (not_393_out, F13);
  not not_394 (not_394_out, F12);
  not not_395 (not_395_out, OP6);
  not not_396 (not_396_out, OP5);
  not not_397 (not_397_out, OP4);
  not not_398 (not_398_out, OP3);
  not not_399 (not_399_out, OP2);
  not not_400 (not_400_out, F12);
  not not_401 (not_401_out, OP4);
  not not_402 (not_402_out, OP3);
  not not_403 (not_403_out, OP2);
  not not_404 (not_404_out, F30);
  not not_405 (not_405_out, F25);
  not not_406 (not_406_out, F14);
  not not_407 (not_407_out, F13);
  not not_408 (not_408_out, F12);
  not not_409 (not_409_out, OP6);
  not not_410 (not_410_out, OP3);
  not not_411 (not_411_out, OP2);
  not not_412 (not_412_out, F25);
  not not_413 (not_413_out, F14);
  not not_414 (not_414_out, F13);
  not not_415 (not_415_out, F12);
  not not_416 (not_416_out, OP6);
  not not_417 (not_417_out, OP3);
  not not_418 (not_418_out, OP2);
  not not_419 (not_419_out, F30);
  not not_420 (not_420_out, F25);
  not not_421 (not_421_out, OP6);
  not not_422 (not_422_out, OP3);
  not not_423 (not_423_out, OP2);
  not not_424 (not_424_out, F30);
  not not_425 (not_425_out, F25);
  not not_426 (not_426_out, F12);
  not not_427 (not_427_out, OP6);
  not not_428 (not_428_out, OP3);
  not not_429 (not_429_out, OP2);
  not not_430 (not_430_out, F30);
  not not_431 (not_431_out, F25);
  not not_432 (not_432_out, F14);
  not not_433 (not_433_out, F12);
  not not_434 (not_434_out, OP6);
  not not_435 (not_435_out, OP3);
  not not_436 (not_436_out, OP2);
  not not_437 (not_437_out, F30);
  not not_438 (not_438_out, F25);
  not not_439 (not_439_out, F14);
  not not_440 (not_440_out, OP6);
  not not_441 (not_441_out, OP3);
  not not_442 (not_442_out, OP2);
  not not_443 (not_443_out, F14);
  not not_444 (not_444_out, F12);
  not not_445 (not_445_out, OP6);
  not not_446 (not_446_out, OP4);
  not not_447 (not_447_out, OP3);
  not not_448 (not_448_out, OP2);
  not not_449 (not_449_out, F30);
  not not_450 (not_450_out, F25);
  not not_451 (not_451_out, F14);
  not not_452 (not_452_out, F13);
  not not_453 (not_453_out, F12);
  not not_454 (not_454_out, OP3);
  not not_455 (not_455_out, OP2);
  not not_456 (not_456_out, F14);
  not not_457 (not_457_out, F13);
  not not_458 (not_458_out, F12);
  not not_459 (not_459_out, OP4);
  not not_460 (not_460_out, OP3);
  not not_461 (not_461_out, OP2);
  not not_462 (not_462_out, F14);
  not not_463 (not_463_out, F13);
  not not_464 (not_464_out, OP4);
  not not_465 (not_465_out, OP3);
  not not_466 (not_466_out, OP2);
  not not_467 (not_467_out, F30);
  not not_468 (not_468_out, F25);
  not not_469 (not_469_out, F13);
  not not_470 (not_470_out, OP6);
  not not_471 (not_471_out, OP3);
  not not_472 (not_472_out, OP2);
  not not_473 (not_473_out, F12);
  not not_474 (not_474_out, OP4);
  not not_475 (not_475_out, OP3);
  not not_476 (not_476_out, OP2);
  not not_477 (not_477_out, F12);
  not not_478 (not_478_out, OP3);
  not not_479 (not_479_out, OP2);
  not not_480 (not_480_out, OP3);
  not not_481 (not_481_out, OP2);
  and and_1 (and_1_out, not_1_out, F13, not_2_out, not_3_out, not_4_out, not_5_out, not_6_out, not_7_out);
  and and_2 (and_2_out, F14, not_8_out, not_9_out, not_10_out, not_11_out, not_12_out, not_13_out, not_14_out);
  and and_3 (MemWrite, not_15_out, F13, not_16_out, not_17_out, OP5, not_18_out, not_19_out, not_20_out);
  and and_4 (and_4_out, not_21_out, not_22_out, not_23_out, not_24_out, not_25_out, OP4, not_26_out, not_27_out);
  and and_5 (and_5_out, F14, F13, F12, not_28_out, not_29_out, OP4, not_30_out, not_31_out);
  and and_6 (and_6_out, F14, F13, not_32_out, not_33_out, not_34_out, OP4, not_35_out, not_36_out);
  and and_7 (and_7_out, F14, not_37_out, not_38_out, not_39_out, not_40_out, OP4, not_41_out, not_42_out);
  and and_8 (and_8_out, not_43_out, F13, not_44_out, not_45_out, not_46_out, OP4, not_47_out, not_48_out);
  and and_9 (and_9_out, not_49_out, not_50_out, not_51_out, not_52_out, F12, not_53_out, not_54_out, OP4, not_55_out, not_56_out);
  and and_10 (and_10_out, not_57_out, not_58_out, F14, not_59_out, F12, not_60_out, not_61_out, OP4, not_62_out, not_63_out);
  and and_11 (and_11_out, F30, not_64_out, F14, not_65_out, F12, not_66_out, not_67_out, OP4, not_68_out, not_69_out);
  and and_12 (and_12_out, not_70_out, F13, not_71_out, not_72_out, not_73_out, not_74_out, not_75_out, not_76_out);
  and and_13 (and_13_out, not_77_out, F13, not_78_out, not_79_out, OP5, not_80_out, not_81_out, not_82_out);
  and and_14 (and_14_out, not_83_out, not_84_out, not_85_out, OP6, OP5, not_86_out, not_87_out, OP2);
  and and_15 (and_15_out, F14, not_88_out, not_89_out, not_90_out, not_91_out, not_92_out, not_93_out, not_94_out);
  and and_16 (and_16_out, not_95_out, not_96_out, not_97_out, not_98_out, not_99_out, not_100_out, OP5, OP4, not_101_out, not_102_out);
  and and_17 (and_17_out, F30, not_103_out, not_104_out, not_105_out, not_106_out, not_107_out, OP5, OP4, not_108_out, not_109_out);
  and and_18 (and_18_out, not_110_out, not_111_out, F14, F13, F12, not_112_out, OP5, OP4, not_113_out, not_114_out);
  and and_19 (and_19_out, not_115_out, not_116_out, F14, F13, not_117_out, not_118_out, OP5, OP4, not_119_out, not_120_out);
  and and_20 (and_20_out, not_121_out, not_122_out, not_123_out, F13, not_124_out, not_125_out, OP5, OP4, not_126_out, not_127_out);
  and and_21 (and_21_out, not_128_out, not_129_out, not_130_out, F13, F12, not_131_out, OP5, OP4, not_132_out, not_133_out);
  and and_22 (and_22_out, not_134_out, not_135_out, not_136_out, not_137_out, not_138_out, OP4, not_139_out, not_140_out);
  and and_23 (and_23_out, F14, F13, F12, not_141_out, not_142_out, OP4, not_143_out, not_144_out);
  and and_24 (and_24_out, F14, F13, not_145_out, not_146_out, not_147_out, OP4, not_148_out, not_149_out);
  and and_25 (and_25_out, F14, not_150_out, not_151_out, not_152_out, not_153_out, OP4, not_154_out, not_155_out);
  and and_26 (and_26_out, not_156_out, F13, not_157_out, not_158_out, not_159_out, OP4, not_160_out, not_161_out);
  and and_27 (and_27_out, not_162_out, not_163_out, not_164_out, not_165_out, F12, not_166_out, not_167_out, OP4, not_168_out, not_169_out);
  and and_28 (and_28_out, not_170_out, not_171_out, F14, not_172_out, F12, not_173_out, not_174_out, OP4, not_175_out, not_176_out);
  and and_29 (and_29_out, F30, not_177_out, F14, not_178_out, F12, not_179_out, not_180_out, OP4, not_181_out, not_182_out);
  and and_30 (and_30_out, not_183_out, F13, not_184_out, not_185_out, not_186_out, not_187_out, not_188_out, not_189_out);
  and and_31 (and_31_out, OP6, OP5, not_190_out, OP3, OP2);
  and and_32 (and_32_out, not_191_out, not_192_out, not_193_out, OP6, OP5, not_194_out, not_195_out, OP2);
  and and_33 (and_33_out, not_196_out, not_197_out, F14, not_198_out, F12, not_199_out, OP5, OP4, not_200_out, not_201_out);
  and and_34 (and_34_out, not_202_out, not_203_out, OP4, not_204_out, OP2);
  and and_35 (and_35_out, F14, not_205_out, not_206_out, not_207_out, not_208_out, not_209_out, not_210_out, not_211_out);
  and and_36 (and_36_out, not_212_out, not_213_out, not_214_out, not_215_out, not_216_out, OP6, OP5, OP4, not_217_out, not_218_out);
  and and_37 (and_37_out, not_219_out, not_220_out, not_221_out, not_222_out, not_223_out, OP6, OP5, OP4, not_224_out, not_225_out);
  and and_38 (S_Type, not_226_out, F13, not_227_out, not_228_out, OP5, not_229_out, not_230_out, not_231_out);
  and and_39 (BEQ, not_232_out, not_233_out, not_234_out, OP6, OP5, not_235_out, not_236_out, not_237_out);
  and and_40 (BNE, not_238_out, not_239_out, F12, OP6, OP5, not_240_out, not_241_out, not_242_out);
  and and_41 (JALR, not_243_out, not_244_out, not_245_out, OP6, OP5, not_246_out, not_247_out, OP2);
  and and_42 (JAL, OP6, OP5, not_248_out, OP3, OP2);
  and and_43 (BLTU, F14, F13, not_249_out, OP6, OP5, not_250_out, not_251_out, not_252_out);
  and and_44 (U_Type, not_253_out, not_254_out, OP4, not_255_out, OP2);
  and and_45 (LBU, F14, not_256_out, not_257_out, not_258_out, not_259_out, not_260_out, not_261_out, not_262_out);
  and and_46 (and_46_out, not_263_out, not_264_out, not_265_out, not_266_out, not_267_out, not_268_out, OP5, OP4, not_269_out, not_270_out);
  and and_47 (and_47_out, F30, not_271_out, not_272_out, not_273_out, not_274_out, not_275_out, OP5, OP4, not_276_out, not_277_out);
  and and_48 (and_48_out, not_278_out, not_279_out, F14, F13, F12, not_280_out, OP5, OP4, not_281_out, not_282_out);
  and and_49 (and_49_out, not_283_out, not_284_out, F14, F13, not_285_out, not_286_out, OP5, OP4, not_287_out, not_288_out);
  and and_50 (and_50_out, not_289_out, not_290_out, not_291_out, F13, not_292_out, not_293_out, OP5, OP4, not_294_out, not_295_out);
  and and_51 (and_51_out, not_296_out, not_297_out, not_298_out, F13, F12, not_299_out, OP5, OP4, not_300_out, not_301_out);
  and and_52 (and_52_out, not_302_out, not_303_out, not_304_out, not_305_out, not_306_out, OP4, not_307_out, not_308_out);
  and and_53 (and_53_out, F14, F13, F12, not_309_out, not_310_out, OP4, not_311_out, not_312_out);
  and and_54 (and_54_out, F14, F13, not_313_out, not_314_out, not_315_out, OP4, not_316_out, not_317_out);
  and and_55 (and_55_out, F14, not_318_out, not_319_out, not_320_out, not_321_out, OP4, not_322_out, not_323_out);
  and and_56 (and_56_out, not_324_out, F13, not_325_out, not_326_out, not_327_out, OP4, not_328_out, not_329_out);
  and and_57 (and_57_out, not_330_out, not_331_out, not_332_out, not_333_out, F12, not_334_out, not_335_out, OP4, not_336_out, not_337_out);
  and and_58 (and_58_out, not_338_out, not_339_out, F14, not_340_out, F12, not_341_out, not_342_out, OP4, not_343_out, not_344_out);
  and and_59 (and_59_out, F30, not_345_out, F14, not_346_out, F12, not_347_out, not_348_out, OP4, not_349_out, not_350_out);
  and and_60 (and_60_out, not_351_out, F13, not_352_out, not_353_out, not_354_out, not_355_out, not_356_out, not_357_out);
  and and_61 (and_61_out, not_358_out, F13, not_359_out, not_360_out, OP5, not_361_out, not_362_out, not_363_out);
  and and_62 (and_62_out, not_364_out, not_365_out, not_366_out, not_367_out, not_368_out, OP6, OP5, OP4, not_369_out, not_370_out);
  and and_63 (and_63_out, not_371_out, not_372_out, not_373_out, OP6, OP5, not_374_out, not_375_out, not_376_out);
  and and_64 (and_64_out, not_377_out, not_378_out, F12, OP6, OP5, not_379_out, not_380_out, not_381_out);
  and and_65 (and_65_out, not_382_out, not_383_out, not_384_out, OP6, OP5, not_385_out, not_386_out, OP2);
  and and_66 (and_66_out, not_387_out, not_388_out, F14, not_389_out, F12, not_390_out, OP5, OP4, not_391_out, not_392_out);
  and and_67 (and_67_out, F14, not_393_out, not_394_out, not_395_out, not_396_out, not_397_out, not_398_out, not_399_out);
  and and_68 (and_68_out, F14, F13, not_400_out, OP6, OP5, not_401_out, not_402_out, not_403_out);
  and and_69 (and_69_out, not_404_out, not_405_out, not_406_out, not_407_out, not_408_out, not_409_out, OP5, OP4, not_410_out, not_411_out);
  and and_70 (and_70_out, F30, not_412_out, not_413_out, not_414_out, not_415_out, not_416_out, OP5, OP4, not_417_out, not_418_out);
  and and_71 (and_71_out, not_419_out, not_420_out, F14, F13, F12, not_421_out, OP5, OP4, not_422_out, not_423_out);
  and and_72 (and_72_out, not_424_out, not_425_out, F14, F13, not_426_out, not_427_out, OP5, OP4, not_428_out, not_429_out);
  and and_73 (and_73_out, not_430_out, not_431_out, not_432_out, F13, not_433_out, not_434_out, OP5, OP4, not_435_out, not_436_out);
  and and_74 (and_74_out, not_437_out, not_438_out, not_439_out, F13, F12, not_440_out, OP5, OP4, not_441_out, not_442_out);
  and and_75 (and_75_out, not_443_out, F13, not_444_out, not_445_out, OP5, not_446_out, not_447_out, not_448_out);
  and and_76 (and_76_out, not_449_out, not_450_out, not_451_out, not_452_out, not_453_out, OP6, OP5, OP4, not_454_out, not_455_out);
  and and_77 (and_77_out, not_456_out, not_457_out, not_458_out, OP6, OP5, not_459_out, not_460_out, not_461_out);
  and and_78 (and_78_out, not_462_out, not_463_out, F12, OP6, OP5, not_464_out, not_465_out, not_466_out);
  and and_79 (and_79_out, not_467_out, not_468_out, F14, not_469_out, F12, not_470_out, OP5, OP4, not_471_out, not_472_out);
  and and_80 (and_80_out, F14, F13, not_473_out, OP6, OP5, not_474_out, not_475_out, not_476_out);
  and and_81 (CSRRSI, F14, F13, not_477_out, OP6, OP5, OP4, not_478_out, not_479_out);
  and and_82 (CSRRCI, F14, F13, F12, OP6, OP5, OP4, not_480_out, not_481_out);
  or or_1 (MemToReg, and_1_out, and_2_out);
  or or_2 (ecall, and_36_out, and_37_out);
  or or_3 (ALU_SRC, and_4_out, and_5_out, and_6_out, and_7_out, and_8_out, and_9_out, and_10_out, and_11_out, and_12_out, and_13_out, and_14_out, and_15_out);
  or or_4 (RegWrite, and_16_out, and_17_out, and_18_out, and_19_out, and_20_out, and_21_out, and_22_out, and_23_out, and_24_out, and_25_out, and_26_out, and_27_out, and_28_out, and_29_out, and_30_out, and_31_out, and_32_out, and_33_out, and_34_out, and_35_out);
  or or_5 (R2, and_69_out, and_70_out, and_71_out, and_72_out, and_73_out, and_74_out, and_75_out, and_76_out, and_77_out, and_78_out, and_79_out, and_80_out);
  or or_6 (R1, and_46_out, and_47_out, and_48_out, and_49_out, and_50_out, and_51_out, and_52_out, and_53_out, and_54_out, and_55_out, and_56_out, and_57_out, and_58_out, and_59_out, and_60_out, and_61_out, and_62_out, and_63_out, and_64_out, and_65_out, and_66_out, and_67_out, and_68_out);
endmodule

// ALU
module ALU (
  input  [31:0] X,
  input  [31:0] Y,
  input  [3:0] AluOP,
  output out_4,
  output Equal,
  output out_6,
  output [31:0] Result,
  output [31:0] Result_2
);

  wire [0:0] comparator_1_lt, comparator_2_lt;
  wire [31:0] adder_1_out, AND_out, divider_1_out, divider_1_rem, multiplier_1_cout, multiplier_1_out,
       NOR_out, OR_out, shifter_1_out, shifter_2_out, shifter_3_out, subtractor_1_out, XOR_out;

  assign AND_out = X & Y;  // AND_Gate AND, 32 bits wide
  assign OR_out = X | Y;  // OR_Gate OR, 32 bits wide
  Shifter #(.width(32), .shift("ll")) shifter_1 (.in(X), .\dist (Y[4:0]), .out(shifter_1_out));
  Shifter #(.width(32), .shift("ar")) shifter_2 (.in(X), .\dist (Y[4:0]), .out(shifter_2_out));
  Shifter #(.width(32), .shift("lr")) shifter_3 (.in(X), .\dist (Y[4:0]), .out(shifter_3_out));
  Multiplier #(.width(32)) multiplier_1 (.a(X), .b(Y), .out(multiplier_1_out), .cout(multiplier_1_cout));  // open: cin
  Divider #(.width(32)) divider_1 (.a(X), .b(Y), .out(divider_1_out), .rem(divider_1_rem));  // open: upper
  Adder #(.width(32)) adder_1 (.a(X), .b(Y), .out(adder_1_out));  // open: cin, cout
  Subtractor #(.width(32)) subtractor_1 (.a(X), .b(Y), .out(subtractor_1_out));  // open: bin, bout
  assign XOR_out = X ^ Y;  // XOR_Gate XOR, 32 bits wide
  assign NOR_out = ~(X | Y);  // NOR_Gate NOR, 32 bits wide
  Comparator #(.width(32), .mode("twosComplement")) comparator_1 (
    .a(X), .b(Y), .eq(Equal), .lt(comparator_1_lt[0]));  // open: gt
  Comparator #(.width(32), .mode("unsigned")) comparator_2 (.a(X), .b(Y), .lt(comparator_2_lt[0]));  // open: gt, eq
  Multiplexer #(.select(4), .width(32), .disabled("Z"), .enable("false")) multiplexer_1 (
    .in0(shifter_1_out), .in1(shifter_2_out), .in2(shifter_3_out), .in3(multiplier_1_out),
    .in4(divider_1_out), .in5(adder_1_out), .in6(subtractor_1_out), .in7(AND_out), .in8(OR_out),
    .in9(XOR_out), .in10(NOR_out), .in11({{31{1'b0}}, comparator_1_lt[0]}),
    .in12({{31{1'b0}}, comparator_2_lt[0]}), .in13({32{1'b0}}), .in14({32{1'b0}}), .in15({32{1'b0}}),
    .out(Result), .sel(AluOP));
  Multiplexer #(.select(4), .width(32), .disabled("Z"), .enable("false")) multiplexer_2 (
    .in0({32{1'b0}}), .in1({32{1'b0}}), .in2({32{1'b0}}), .in3(multiplier_1_cout), .in4(divider_1_rem),
    .in5({32{1'b0}}), .in6({32{1'b0}}), .in7({32{1'b0}}), .in8({32{1'b0}}), .in9({32{1'b0}}),
    .in10({32{1'b0}}), .in11({32{1'b0}}), .in12({32{1'b0}}), .in13({32{1'b0}}), .in14({32{1'b0}}),
    .in15({32{1'b0}}), .out(Result_2), .sel(AluOP));
  Multiplexer #(.select(4), .width(1), .disabled("Z"), .enable("false")) multiplexer_3 (
    .in0(1'b0), .in1(1'b0), .in2(1'b0), .in3(1'b0), .in4(1'b0), .in5(1'b0), .in6(1'b0), .in7(1'b0),
    .in8(1'b0), .in9(1'b0), .in10(1'b0), .in11(comparator_1_lt[0]), .in12(comparator_2_lt[0]), .in13(1'b0),
    .in14(1'b0), .in15(1'b0), .out(out_6), .sel(AluOP));
  not not_1 (out_4, out_6);

  // Other names for the same wires on the sheet: Result2[31:0] = Result_2; S[3:0] = AluOP; tunnel = out_6;
  //   tunnel_t = out_4

  // Notes on the sheet:
  //   不要改变此引脚区域内容，也不要改变ALU封装形式
  //   输入引脚
  //   输出引脚
endmodule

module Regifile (
  input  [31:0] Din,
  input  Clk,
  input  WE,
  input  [4:0] R1_num,
  input  [4:0] W_num,
  input  [4:0] R2_num,
  output [31:0] R1,
  output [31:0] R2
);

  // RegisterFile registerfile_1: pin names not known; wires that end beside it: Din, Clk, WE, W_num, R1_num, R2_num, R1, R2
endmodule

module \理想流水线  (
  output RegWrite,
  output MemWrite,
  output [31:0] IF_PC,
  output [31:0] ID_PC,
  output [31:0] EX_PC,
  output [31:0] M_PC,
  output [31:0] WB_PC,
  output [31:0] RDin,
  output [31:0] MDin,
  output [31:0] LedData
);

  wire and_2_out, and_4_out, and_5_out, and_6_out, BLTU, Branch, CLK, clock_2_out, comparator_1_eq,
       comparator_1_lt, comparator_2_eq, controlled_buffer_1_out, d_ff_1_q, ecall, en, EQ, EX_jal, EX_jalr,
       ex_mem_1_bltuout, ex_mem_1_haltout, ex_mem_1_jalout, ex_mem_1_jalrout, ex_mem_1_lbuout,
       ex_mem_1_memtoregout, ex_mem_1_regwriteout, ex_mem_1_u_typeout, ex_mem_1_uretout, Go, halt,
       id_ex_1_alusrcbout, id_ex_1_beqout, id_ex_1_bneout, id_ex_1_haltout, id_ex_1_lbuout,
       id_ex_1_memtoregout, id_ex_1_memwriteout, id_ex_1_regwriteout, id_ex_1_s_typeout, id_ex_1_u_typeout,
       id_ex_1_uretout, ID_Halt, IR1, IR2, IR3, LT, mem_wb_1_haltout, mem_wb_1_jalout, mem_wb_1_jalrout,
       mem_wb_1_lbuout, mem_wb_1_memtoregout, nand_1_out, not_1_out, not_2_out, or_2_out, RST, W1, W2, W3,
       WB_U_Type, \单周期硬布线控制器_1_alu_src , \单周期硬布线控制器_1_beq , \单周期硬布线控制器_1_bltu , \单周期硬布线控制器_1_bne ,
       \单周期硬布线控制器_1_jal , \单周期硬布线控制器_1_jalr , \单周期硬布线控制器_1_lbu , \单周期硬布线控制器_1_memtoreg ,
       \单周期硬布线控制器_1_memwrite , \单周期硬布线控制器_1_regwrite , \单周期硬布线控制器_1_s_type , \单周期硬布线控制器_1_u_type ,
       \单周期硬布线控制器_1_uret ;
  wire [1:0] mem_wb_1_indexout;
  wire [3:0] id_ex_1_aluopout, \单周期硬布线控制器_1_alu_op ;
  wire [4:0] ex_mem_1_w_out, id_ex_1_w_out, multiplexer_4_out, multiplexer_5_out, W_num;
  wire [7:0] multiplexer_8_out;
  wire [11:0] shifter_1_out;
  wire [12:0] CNT_num;
  wire [15:0] \LoadUse次数 , \分支成功数 , \总周期数 , \插入气泡数 , \无条件分支数 , \条件分支成功数 ;
  wire [19:0] shifter_2_out;
  wire [31:0] adder_1_out, adder_2_out, adder_5_out, and_1_out, bit_extender_1_out, bit_extender_2_out,
       bit_extender_3_out, bit_extender_4_out, bit_extender_5_out, EX_IR, ex_mem_1_immuout,
       ex_mem_1_resultout, id_ex_1_imm_i_out, id_ex_1_imm_s_out, id_ex_1_immuout, id_ex_1_r1out,
       id_ex_1_r2out, ID_IR, IF_IR, IF_PC_4, imm_B, imm_J, JAddr, MEM_IR, mem_wb_1_immuout,
       mem_wb_1_resultout, mem_wb_1_rmdataout, multiplexer_1_out, multiplexer_2_out, multiplexer_3_out,
       multiplexer_6_out, multiplexer_7_out, multiplexer_9_out, multiplexer_10_out, multiplexer_11_out, R1,
       R2, ram_1_data, WB_IR, WB_PC_4;

  Button \u_总复位  (.out(RST));
  Button _1 (.out(IR1));
  Button _2 (.out(IR2));
  Button _3 (.out(IR3));
  // Probe on \总周期数 
  // Probe on \总周期数 
  Button \u_继续运行  (.out(Go));
  LED #(.active("true")) led_1 (.in(W1));
  LED #(.active("true")) led_2 (.in(W2));
  LED #(.active("true")) led_3 (.in(W3));
  // Probe on \分支成功数 
  Hex_Digit_Display hex_digit_display_1 (.value(LedData[31:28]));  // open: dp
  // Probe on IF_PC[19:0]
  // RiscV_Probe riscv_probe_1: pin names not known; wires that end beside it: IF_IR
  Hex_Digit_Display hex_digit_display_2 (.value(LedData[27:24]));  // open: dp
  Hex_Digit_Display hex_digit_display_3 (.value(LedData[23:20]));  // open: dp
  // Probe on ID_PC[19:0]
  // RiscV_Probe riscv_probe_2: pin names not known; wires that end beside it: ID_IR
  not not_1 (not_1_out, halt);
  Adder #(.width(32)) adder_1 (.a(imm_J), .b(EX_PC), .out(adder_1_out));  // open: cin, cout
  Hex_Digit_Display hex_digit_display_4 (.value(LedData[19:16]));  // open: dp
  Hex_Digit_Display hex_digit_display_5 (.value(LedData[15:12]));  // open: dp
  Counter #(.width(16), .max('hffff), .ongoal("wrap"), .trigger("rising"), .behavior("new")) counter_1 (
    .count(not_1_out), .Q(\总周期数 ), .clk(CLK), .clr(RST));  // open: load, D, carry, preset, down
  Multiplexer #(.select(1), .width(32), .disabled("Z"), .enable("false")) multiplexer_1 (
    .in0(IF_PC_4), .in1(adder_1_out), .out(multiplexer_1_out), .sel(EX_jal));
  assign and_1_out = JAddr & 32'hfffffffe;  // AND_Gate and_1, 32 bits wide
  Adder #(.width(32)) adder_2 (.a(imm_B), .b(EX_PC), .out(adder_2_out));  // open: cin, cout
  Hex_Digit_Display hex_digit_display_6 (.value(LedData[11:8]));  // open: dp
  Hex_Digit_Display hex_digit_display_7 (.value(LedData[7:4]));  // open: dp
  Clock #(.highDuration(1), .lowDuration(1)) clock_1 (.out(CLK));
  // Probe on EX_PC[19:0]
  // RiscV_Probe riscv_probe_3: pin names not known; wires that end beside it: EX_IR
  Multiplexer #(.select(1), .width(32), .disabled("Z"), .enable("false")) multiplexer_2 (
    .in0(multiplexer_1_out), .in1(and_1_out), .out(multiplexer_2_out), .sel(EX_jalr));
  Multiplexer #(.select(1), .width(32), .disabled("Z"), .enable("false")) multiplexer_3 (
    .in0(multiplexer_2_out), .in1(adder_2_out), .out(multiplexer_3_out), .sel(Branch));
  Hex_Digit_Display hex_digit_display_8 (.value(LedData[3:0]));  // open: dp
  Register #(.width(32), .trigger("rising"), .Select("low")) PC (
    .D(multiplexer_3_out), .en(not_2_out), .Q(IF_PC), .clk(CLK), .clr(RST));
  not not_2 (not_2_out, halt);
  // Probe on \总周期数 
  // Probe on M_PC[19:0]
  // RiscV_Probe riscv_probe_4: pin names not known; wires that end beside it: MEM_IR
  // Probe on \总周期数 
  // Probe on \无条件分支数 
  // Probe on \条件分支成功数 
  // Probe on \插入气泡数 
  // Probe on \LoadUse次数 
  // Probe on IF_PC[11:0]
  // Probe on WB_PC[19:0]
  // RiscV_Probe riscv_probe_5: pin names not known; wires that end beside it: WB_IR
  ROM #(.addrWidth(10), .dataWidth(32), .Select("high")) rom_1 (.addr(IF_PC[11:2]), .data(IF_IR));
  Adder #(.width(32)) adder_3 (.a(IF_PC), .b(32'h4), .out(IF_PC_4));  // open: cin, cout
  // Probe on ID_PC[11:0]
  // Probe on EX_PC[11:0]
  IF_ID if_id_1 (
    .PCin(IF_PC), .IRin(IF_IR), .PCout(ID_PC), .IRout(ID_IR), .RST(RST), .EN_H(en), .CLK(CLK));  // open: PJin, PJout
  // Probe on M_PC[11:0]
  D_Flip_Flop #(.trigger("high"), .Pre_Clr_Positions("LEGACY"), .NegatePresetClear("false"), .enable("true"), .NewFFLayout("false")) d_ff_1 (.Q(d_ff_1_q));  // open: clk, D, Qn, preset, en, reset
  // Probe on 13'h4
  // Probe on WB_PC[11:0]
  Comparator #(.width(13), .mode("twosComplement")) comparator_1 (
    .a(CNT_num), .b(13'h4), .eq(comparator_1_eq), .lt(comparator_1_lt));  // open: gt
  Clock #(.highDuration(1), .lowDuration(1)) clock_2 (.out(clock_2_out));
  nand nand_1 (nand_1_out, d_ff_1_q, comparator_1_eq);
  Counter #(.width(13), .max('h1fff), .ongoal("stay"), .trigger("rising"), .behavior("old")) counter_2 (
    .count(comparator_1_lt), .Q(CNT_num), .clk(clock_2_out));  // open: load, D, carry, clr, preset
  \单周期硬布线控制器  \u_单周期硬布线控制器_1  (
    .Funct({ID_IR[30], ID_IR[25], ID_IR[14:12]}), .OP(ID_IR[6:2]), .ALU_OP(\单周期硬布线控制器_1_alu_op ),
    .MemToReg(\单周期硬布线控制器_1_memtoreg ), .MemWrite(\单周期硬布线控制器_1_memwrite ), .ALU_SRC(\单周期硬布线控制器_1_alu_src ),
    .RegWrite(\单周期硬布线控制器_1_regwrite ), .ecall(ecall), .S_type(\单周期硬布线控制器_1_s_type ),
    .Jalr(\单周期硬布线控制器_1_jalr ), .Beq(\单周期硬布线控制器_1_beq ), .JAL(\单周期硬布线控制器_1_jal ), .Bne(\单周期硬布线控制器_1_bne ),
    .in_3(ID_IR[21]), .uret(\单周期硬布线控制器_1_uret ), .BLTU(\单周期硬布线控制器_1_bltu ), .U_Type(\单周期硬布线控制器_1_u_type ),
    .LBU(\单周期硬布线控制器_1_lbu ));  // open: R1, R2, CSRRSI, CSRRCI
  Multiplexer #(.select(1), .width(5), .disabled("Z"), .enable("false")) multiplexer_4 (
    .in0(ID_IR[24:20]), .in1(5'b01010), .out(multiplexer_4_out), .sel(ecall));
  assign bit_extender_1_out = {{20{ID_IR[31]}}, ID_IR[31:20]};  // Bit_Extender bit_extender_1
  assign bit_extender_2_out = {{20{ID_IR[31]}}, {ID_IR[31:25], ID_IR[11:7]}};  // Bit_Extender bit_extender_2
  assign controlled_buffer_1_out = nand_1_out ? clock_2_out : 1'bz;  // Controlled_Buffer controlled_buffer_1
  Multiplexer #(.select(1), .width(5), .disabled("Z"), .enable("false")) multiplexer_5 (
    .in0(ID_IR[19:15]), .in1(5'b10001), .out(multiplexer_5_out), .sel(ecall));
  Shifter #(.width(12), .shift("ll")) shifter_1 (
    .in({ID_IR[31], ID_IR[7], ID_IR[30:25], ID_IR[11:8]}), .\dist (4'b0001), .out(shifter_1_out));
  assign bit_extender_3_out = {{20{shifter_1_out[11]}}, shifter_1_out};  // Bit_Extender bit_extender_3
  Shifter #(.width(20), .shift("ll")) shifter_2 (
    .in({ID_IR[31], ID_IR[19:12], ID_IR[20], ID_IR[30:21]}), .\dist (5'b00001), .out(shifter_2_out));
  assign bit_extender_4_out = {{12{shifter_2_out[19]}}, shifter_2_out};  // Bit_Extender bit_extender_4
  Pull_Resistor #(.pull(1)) pull_resistor_1 (.node(controlled_buffer_1_out));
  Regifile regifile_1 (
    .Din(RDin), .Clk(CLK), .R1(R1), .R2(R2), .WE(RegWrite), .W_num(W_num), .R1_num(multiplexer_5_out),
    .R2_num(multiplexer_4_out));
  Comparator #(.width(32), .mode("twosComplement")) comparator_2 (
    .a(R1), .b(32'h22), .eq(comparator_2_eq));  // open: gt, lt
  and and_2 (and_2_out, ecall, comparator_2_eq);
  and and_3 (ID_Halt, ~comparator_2_eq, ecall, ~Go);  // AND_Gate
  ID_EX id_ex_1 (
    .PCin(ID_PC), .IRin(ID_IR), .ImmIin(bit_extender_1_out), .ImmSin(bit_extender_2_out),
    .ImmBin(bit_extender_3_out), .ImmJin(bit_extender_4_out), .R1in(R1), .R2in(R2),
    .AluOpin(\单周期硬布线控制器_1_alu_op ), .RST(RST), .EN_H(en), .CLK(CLK), .Beqin(\单周期硬布线控制器_1_beq ),
    .Bnein(\单周期硬布线控制器_1_bne ), .MemToRegin(\单周期硬布线控制器_1_memtoreg ), .MemWritein(\单周期硬布线控制器_1_memwrite ),
    .AluSrcBin(\单周期硬布线控制器_1_alu_src ), .RegWritein(\单周期硬布线控制器_1_regwrite ), .S_typein(\单周期硬布线控制器_1_s_type ),
    .Jalin(\单周期硬布线控制器_1_jal ), .Jalrin(\单周期硬布线控制器_1_jalr ), .Haltin(ID_Halt), .Beqout(id_ex_1_beqout),
    .Bneout(id_ex_1_bneout), .MemToRegout(id_ex_1_memtoregout), .MemWriteout(id_ex_1_memwriteout),
    .AluSrcBout(id_ex_1_alusrcbout), .RegWriteout(id_ex_1_regwriteout), .S_Typeout(id_ex_1_s_typeout),
    .Jalout(EX_jal), .Jalrout(EX_jalr), .Haltout(id_ex_1_haltout), .AluOpout(id_ex_1_aluopout),
    .PCout(EX_PC), .IRout(EX_IR), .Imm_I_out(id_ex_1_imm_i_out), .Imm_S_out(id_ex_1_imm_s_out),
    .Imm_B_out(imm_B), .Imm_J_out(imm_J), .R1out(id_ex_1_r1out), .R2out(id_ex_1_r2out), .W_in(ID_IR[11:7]),
    .W_out(id_ex_1_w_out), .URETin(\单周期硬布线控制器_1_uret ), .LBUin(\单周期硬布线控制器_1_lbu ),
    .BLTUin(\单周期硬布线控制器_1_bltu ), .U_Typein(\单周期硬布线控制器_1_u_type ), .URETout(id_ex_1_uretout),
    .LBUout(id_ex_1_lbuout), .BLTUout(BLTU), .U_Typeout(id_ex_1_u_typeout),
    .ImmUin({ID_IR[31:12], {12{1'b0}}}), .ImmUout(id_ex_1_immuout));  // open: Ecallin, Ecallout, R1Forwardin, R1Forwardout, R2Forwardin, R2Forwardout, PJin, PJout
  Register #(.width(32), .trigger("rising"), .Select("low")) register_1 (
    .D(R2), .en(and_2_out), .Q(LedData), .clk(CLK), .clr(RST));
  Multiplexer #(.select(1), .width(32), .disabled("Z"), .enable("false")) multiplexer_6 (
    .in0(id_ex_1_imm_i_out), .in1(id_ex_1_imm_s_out), .out(multiplexer_6_out), .sel(id_ex_1_s_typeout));
  Multiplexer #(.select(1), .width(32), .disabled("Z"), .enable("false")) multiplexer_7 (
    .in0(id_ex_1_r2out), .in1(multiplexer_6_out), .out(multiplexer_7_out), .sel(id_ex_1_alusrcbout));
  and and_4 (and_4_out, id_ex_1_beqout, EQ);
  or or_1 (Branch, and_4_out, and_5_out, and_6_out);
  and and_5 (and_5_out, ~EQ, id_ex_1_bneout);  // AND_Gate
  and and_6 (and_6_out, BLTU, LT);
  ALU alu_1 (
    .X(id_ex_1_r1out), .Y(multiplexer_7_out), .AluOP(id_ex_1_aluopout), .Equal(EQ), .Result(JAddr), .out_6(LT));  // open: Result_2, out_4
  Counter #(.width(16), .max('hffff), .ongoal("wrap"), .trigger("rising"), .behavior("new")) counter_3 (
    .count(Branch), .Q(\分支成功数 ), .clk(CLK), .clr(RST));  // open: load, D, carry, preset, down
  EX_MEM ex_mem_1 (
    .PCin(EX_PC), .IRin(EX_IR), .Resultin(JAddr), .MDatain(id_ex_1_r2out), .PCout(M_PC), .IRout(MEM_IR),
    .Resultout(ex_mem_1_resultout), .Mdataout(MDin), .MemToRegin(id_ex_1_memtoregout),
    .MemWritein(id_ex_1_memwriteout), .Jalin(EX_jal), .RegWritein(id_ex_1_regwriteout),
    .Haltin(id_ex_1_haltout), .MemToRegout(ex_mem_1_memtoregout), .MemWriteout(MemWrite),
    .Jalout(ex_mem_1_jalout), .RegWriteout(ex_mem_1_regwriteout), .Haltout(ex_mem_1_haltout), .RST(RST),
    .EN_H(en), .CLK(CLK), .W_in(id_ex_1_w_out), .W_out(ex_mem_1_w_out), .URETin(id_ex_1_uretout),
    .LBUin(id_ex_1_lbuout), .BLTUin(BLTU), .U_Typein(id_ex_1_u_typeout), .URETout(ex_mem_1_uretout),
    .LBUout(ex_mem_1_lbuout), .BLTUout(ex_mem_1_bltuout), .U_Typeout(ex_mem_1_u_typeout), .Jalrin(EX_jalr),
    .Jalrout(ex_mem_1_jalrout), .ImmUin(id_ex_1_immuout), .ImmUout(ex_mem_1_immuout));
  RAM #(.addrWidth(10), .dataWidth(32), .bus("separate"), .Select("high")) ram_1 (
    .addr(ex_mem_1_resultout[11:2]), .din(MDin), .data(ram_1_data), .str(MemWrite), .clk(CLK),
    .ld(ex_mem_1_memtoregout), .clr(RST));  // open: sel
  MEM_WB mem_wb_1 (
    .PCin(M_PC), .IRin(MEM_IR), .Resultin(ex_mem_1_resultout), .RMDatain(ram_1_data), .PCout(WB_PC),
    .IRout(WB_IR), .Resultout(mem_wb_1_resultout), .RMdataout(mem_wb_1_rmdataout), .RST(RST),
    .W_in(ex_mem_1_w_out), .EN_H(en), .W_out(W_num), .CLK(CLK), .MemToRegin(ex_mem_1_memtoregout),
    .Jalin(ex_mem_1_jalout), .RegWritein(ex_mem_1_regwriteout), .Haltin(ex_mem_1_haltout),
    .MemToRegout(mem_wb_1_memtoregout), .RegWriteout(RegWrite), .Jalrin(ex_mem_1_jalrout),
    .URETin(ex_mem_1_uretout), .LBUin(ex_mem_1_lbuout), .BLTUin(ex_mem_1_bltuout),
    .U_Typein(ex_mem_1_u_typeout), .Jalout(mem_wb_1_jalout), .Jalrout(mem_wb_1_jalrout),
    .LBUout(mem_wb_1_lbuout), .U_Typeout(WB_U_Type), .ImmUin(ex_mem_1_immuout), .ImmUout(mem_wb_1_immuout),
    .Indexin(ex_mem_1_resultout[1:0]), .Indexout(mem_wb_1_indexout), .Haltout(mem_wb_1_haltout));  // open: URETout, BLTUout
  Multiplexer #(.select(2), .width(8), .disabled("Z"), .enable("false")) multiplexer_8 (
    .in0(mem_wb_1_rmdataout[7:0]), .in1(mem_wb_1_rmdataout[15:8]), .in2(mem_wb_1_rmdataout[23:16]),
    .in3(mem_wb_1_rmdataout[31:24]), .out(multiplexer_8_out), .sel(mem_wb_1_indexout));
  and and_7 (halt, mem_wb_1_haltout, ~Go);  // AND_Gate
  not not_3 (en, halt);
  Adder #(.width(32)) adder_4 (.a(32'h4), .b(WB_PC), .out(WB_PC_4));  // open: cin, cout
  or or_2 (or_2_out, mem_wb_1_jalout, mem_wb_1_jalrout, WB_U_Type);
  assign bit_extender_5_out = {{24{1'b0}}, multiplexer_8_out};  // Bit_Extender bit_extender_5
  Adder #(.width(32)) adder_5 (.a(WB_PC), .b(mem_wb_1_immuout), .out(adder_5_out));  // open: cin, cout
  Multiplexer #(.select(1), .width(32), .disabled("Z"), .enable("false")) multiplexer_9 (
    .in0(mem_wb_1_resultout), .in1(multiplexer_10_out), .out(multiplexer_9_out), .sel(mem_wb_1_memtoregout));
  Multiplexer #(.select(1), .width(32), .disabled("Z"), .enable("false")) multiplexer_10 (
    .in0(mem_wb_1_rmdataout), .in1(bit_extender_5_out), .out(multiplexer_10_out), .sel(mem_wb_1_lbuout));
  Multiplexer #(.select(1), .width(32), .disabled("Z"), .enable("false")) multiplexer_11 (
    .in0(WB_PC_4), .in1(adder_5_out), .out(multiplexer_11_out), .sel(WB_U_Type));
  Multiplexer #(.select(1), .width(32), .disabled("Z"), .enable("false")) multiplexer_12 (
    .in0(multiplexer_9_out), .in1(multiplexer_11_out), .out(RDin), .sel(or_2_out));

  // Other names for the same wires on the sheet: IR[31:0] = ID_IR; RD_num[4:0] = ID_IR[11:7]; MEM_MemWrite = MemWrite;
  //   MEM_PC[31:0] = M_PC; WB_RegWrite = RegWrite; WriteBackData[31:0] = RDin

  // Notes on the sheet:
  //   中断源
  //   时空图监测，可删除
  //   中断等待指示
  //   数码管输出
  //   指令存储器
  //   contents of rom_1 (hex, n*v repeats v):
  //   413 493 913 993 46413 14e493 296913 39e993 842023 942223 1242423 1342623 a00893 493 913 993 73
  //   控制位
  //   流水调试日志用
  //   暂停节拍，不能为0
  //   指令字
  //   戳工具置1进入计数暂停模式，ctrl+k时钟自动运行到对应节拍暂停
  //   ctrl+k关闭时钟连续运行，将控制位置零，进入单步调试模式调试
  //   用这个时钟源需要去掉电路中的其他时钟源
  //   rs1
  //   rs2
  //   rd
  //   可计数暂停的时钟源
  //   为方便自动评测，需要输出流水线各段保存的PC值，注意是PC不是PC+4，另外ID段寄存器写入信息，Mem段内存写入信息也要输出
endmodule

module \气泡流水线  (
  output RegWrite,
  output MemWrite,
  output [31:0] IF_PC,
  output [31:0] ID_PC,
  output [31:0] EX_PC,
  output [31:0] M_PC,
  output [31:0] WB_PC,
  output [31:0] RDin,
  output [31:0] MDin,
  output [31:0] LedData
);

  wire and_2_out, and_3_out, and_4_out, and_6_out, and_7_out, and_8_out, BLTU, Branch, CLK, clock_1_out,
       comparator_1_eq, comparator_1_lt, comparator_2_eq, d_ff_1_q, en, EQ, EX_ecall, EX_jal, EX_jalr,
       ex_mem_1_bltuout, ex_mem_1_haltout, ex_mem_1_jalout, ex_mem_1_jalrout, ex_mem_1_lbuout,
       ex_mem_1_memtoregout, ex_mem_1_u_typeout, ex_mem_1_uretout, EX_RegWrite, Go, halt, ID_ecall,
       id_ex_1_alusrcbout, id_ex_1_beqout, id_ex_1_bltuout, id_ex_1_bneout, id_ex_1_haltout,
       id_ex_1_memtoregout, id_ex_1_memwriteout, id_ex_1_s_typeout, id_ex_1_u_typeout, id_ex_1_uretout,
       ID_Halt, IR1, IR2, IR3, LT, MEM_RegWrite, mem_wb_1_haltout, mem_wb_1_jalout, mem_wb_1_jalrout,
       mem_wb_1_lbuout, mem_wb_1_memtoregout, nand_1_out, not_1_out, not_2_out, or_1_out, or_2_out, or_4_out,
       RST, W1, W2, W3, WB_U_Type, \单周期硬布线控制器_1_alu_src , \单周期硬布线控制器_1_beq , \单周期硬布线控制器_1_bltu ,
       \单周期硬布线控制器_1_bne , \单周期硬布线控制器_1_jal , \单周期硬布线控制器_1_jalr , \单周期硬布线控制器_1_lbu , \单周期硬布线控制器_1_memtoreg ,
       \单周期硬布线控制器_1_memwrite , \单周期硬布线控制器_1_r1 , \单周期硬布线控制器_1_r2 , \单周期硬布线控制器_1_regwrite ,
       \单周期硬布线控制器_1_s_type , \单周期硬布线控制器_1_u_type , \单周期硬布线控制器_1_uret , \数据相关 ;
  wire [1:0] mem_wb_1_indexout;
  wire [3:0] id_ex_1_aluopout, \单周期硬布线控制器_1_alu_op ;
  wire [4:0] EX_W_num, ID_R1_num, ID_R2_num, MEM_W_num, W_num;
  wire [7:0] multiplexer_8_out;
  wire [11:0] shifter_1_out;
  wire [12:0] CNT_num;
  wire [15:0] \LoadUse次数 , \分支成功数 , \总周期数 , \插入气泡数 , \无条件分支数 , \条件分支成功数 ;
  wire [19:0] shifter_2_out;
  wire [31:0] adder_1_out, adder_2_out, adder_5_out, and_1_out, bit_extender_1_out, bit_extender_2_out,
       bit_extender_3_out, bit_extender_4_out, bit_extender_5_out, EX_IR, ex_mem_1_immuout,
       ex_mem_1_resultout, id_ex_1_imm_i_out, id_ex_1_imm_s_out, id_ex_1_immuout, id_ex_1_r1out,
       id_ex_1_r2out, ID_IR, IF_IR, imm_B, imm_J, JAddr, MEM_IR, mem_wb_1_immuout, mem_wb_1_resultout,
       mem_wb_1_rmdataout, multiplexer_1_out, multiplexer_2_out, multiplexer_3_out, multiplexer_6_out,
       multiplexer_7_out, multiplexer_9_out, multiplexer_10_out, multiplexer_11_out, PC_4, R1, R2,
       ram_1_data, WB_IR, WB_PC_4;

  Button \u_总复位  (.out(RST));
  Button _1 (.out(IR1));
  Button _2 (.out(IR2));
  Button _3 (.out(IR3));
  // Probe on \总周期数 
  // Probe on \总周期数 
  Button \u_继续运行  (.out(Go));
  LED #(.active("true")) led_1 (.in(W1));
  LED #(.active("true")) led_2 (.in(W2));
  LED #(.active("true")) led_3 (.in(W3));
  // Probe on \分支成功数 
  Hex_Digit_Display hex_digit_display_1 (.value(LedData[31:28]));  // open: dp
  // Probe on IF_PC[19:0]
  // RiscV_Probe riscv_probe_1: pin names not known; wires that end beside it: IF_IR
  Hex_Digit_Display hex_digit_display_2 (.value(LedData[23:20]));  // open: dp
  Hex_Digit_Display hex_digit_display_3 (.value(LedData[27:24]));  // open: dp
  // Probe on ID_PC[19:0]
  // RiscV_Probe riscv_probe_2: pin names not known; wires that end beside it: ID_IR
  not not_1 (not_1_out, halt);
  Adder #(.width(32)) adder_1 (.a(imm_J), .b(EX_PC), .out(adder_1_out));  // open: cin, cout
  Hex_Digit_Display hex_digit_display_4 (.value(LedData[15:12]));  // open: dp
  Hex_Digit_Display hex_digit_display_5 (.value(LedData[19:16]));  // open: dp
  Counter #(.width(16), .max('hffff), .ongoal("wrap"), .trigger("rising"), .behavior("new")) counter_1 (
    .count(not_1_out), .Q(\总周期数 ), .clk(CLK), .clr(RST));  // open: load, D, carry, preset, down
  Multiplexer #(.select(1), .width(32), .disabled("Z"), .enable("false")) multiplexer_1 (
    .in0(PC_4), .in1(adder_1_out), .out(multiplexer_1_out), .sel(EX_jal));
  assign and_1_out = JAddr & 32'hfffffffe;  // AND_Gate and_1, 32 bits wide
  Adder #(.width(32)) adder_2 (.a(imm_B), .b(EX_PC), .out(adder_2_out));  // open: cin, cout
  Hex_Digit_Display hex_digit_display_6 (.value(LedData[11:8]));  // open: dp
  Hex_Digit_Display hex_digit_display_7 (.value(LedData[7:4]));  // open: dp
  // Probe on EX_PC[19:0]
  // RiscV_Probe riscv_probe_3: pin names not known; wires that end beside it: EX_IR
  Multiplexer #(.select(1), .width(32), .disabled("Z"), .enable("false")) multiplexer_2 (
    .in0(multiplexer_1_out), .in1(and_1_out), .out(multiplexer_2_out), .sel(EX_jalr));
  Multiplexer #(.select(1), .width(32), .disabled("Z"), .enable("false")) multiplexer_3 (
    .in0(multiplexer_2_out), .in1(adder_2_out), .out(multiplexer_3_out), .sel(Branch));
  Hex_Digit_Display hex_digit_display_8 (.value(LedData[3:0]));  // open: dp
  Register #(.width(32), .trigger("rising"), .Select("low")) PC (
    .D(multiplexer_3_out), .en(and_2_out), .Q(IF_PC), .clk(CLK), .clr(RST));
  and and_2 (and_2_out, ~\数据相关 , ~halt);  // AND_Gate
  // Probe on \总周期数 
  // Probe on M_PC[19:0]
  // RiscV_Probe riscv_probe_4: pin names not known; wires that end beside it: MEM_IR
  // Probe on \总周期数 
  // Probe on \无条件分支数 
  // Probe on \条件分支成功数 
  // Probe on \插入气泡数 
  // Probe on \LoadUse次数 
  // Probe on IF_PC[11:0]
  // Probe on WB_PC[19:0]
  // RiscV_Probe riscv_probe_5: pin names not known; wires that end beside it: WB_IR
  or or_1 (or_1_out, RST, Branch, EX_jalr, EX_jal);
  ROM #(.addrWidth(10), .dataWidth(32), .Select("high")) rom_1 (.addr(IF_PC[11:2]), .data(IF_IR));
  Adder #(.width(32)) adder_3 (.a(IF_PC), .b(32'h4), .out(PC_4));  // open: cin, cout
  // Probe on EX_PC[11:0]
  // Probe on ID_PC[11:0]
  IF_ID if_id_1 (
    .PCin(IF_PC), .IRin(IF_IR), .PCout(ID_PC), .IRout(ID_IR), .RST(or_1_out), .EN_H(and_3_out), .CLK(CLK));  // open: PJin, PJout
  and and_3 (and_3_out, ~\数据相关 , en);  // AND_Gate
  // Probe on M_PC[11:0]
  D_Flip_Flop #(.trigger("high"), .Pre_Clr_Positions("LEGACY"), .NegatePresetClear("false"), .enable("true"), .NewFFLayout("false")) d_ff_1 (.Q(d_ff_1_q));  // open: clk, D, Qn, preset, en, reset
  // Probe on 13'he24
  // Probe on WB_PC[11:0]
  Comparator #(.width(13), .mode("twosComplement")) comparator_1 (
    .a(CNT_num), .b(13'he24), .eq(comparator_1_eq), .lt(comparator_1_lt));  // open: gt
  Clock #(.highDuration(1), .lowDuration(1)) clock_1 (.out(clock_1_out));
  nand nand_1 (nand_1_out, d_ff_1_q, comparator_1_eq);
  Counter #(.width(13), .max('h1fff), .ongoal("stay"), .trigger("rising"), .behavior("old")) counter_2 (
    .count(comparator_1_lt), .Q(CNT_num), .clk(clock_1_out));  // open: load, D, carry, clr, preset
  \数据冲突处理_气泡  \u_数据冲突处理_气泡_1  (
    .ID_R1(\单周期硬布线控制器_1_r1 ), .EX_RW(EX_RegWrite), .ID_R2(\单周期硬布线控制器_1_r2 ), .MEM_RW(MEM_RegWrite),
    .ID_R1_num(ID_R1_num), .EX_W_num(EX_W_num), .ID_R2_num(ID_R2_num), .MEM_W_num(MEM_W_num), .out_9(\数据相关 ));
  \单周期硬布线控制器  \u_单周期硬布线控制器_1  (
    .Funct({ID_IR[30], ID_IR[25], ID_IR[14:12]}), .OP(ID_IR[6:2]), .ALU_OP(\单周期硬布线控制器_1_alu_op ),
    .MemToReg(\单周期硬布线控制器_1_memtoreg ), .MemWrite(\单周期硬布线控制器_1_memwrite ), .ALU_SRC(\单周期硬布线控制器_1_alu_src ),
    .RegWrite(\单周期硬布线控制器_1_regwrite ), .ecall(ID_ecall), .S_type(\单周期硬布线控制器_1_s_type ),
    .Jalr(\单周期硬布线控制器_1_jalr ), .Beq(\单周期硬布线控制器_1_beq ), .JAL(\单周期硬布线控制器_1_jal ), .Bne(\单周期硬布线控制器_1_bne ),
    .in_3(ID_IR[21]), .uret(\单周期硬布线控制器_1_uret ), .BLTU(\单周期硬布线控制器_1_bltu ), .U_Type(\单周期硬布线控制器_1_u_type ),
    .LBU(\单周期硬布线控制器_1_lbu ), .R1(\单周期硬布线控制器_1_r1 ), .R2(\单周期硬布线控制器_1_r2 ));  // open: CSRRSI, CSRRCI
  Multiplexer #(.select(1), .width(5), .disabled("Z"), .enable("false")) multiplexer_4 (
    .in0(ID_IR[24:20]), .in1(5'b01010), .out(ID_R2_num), .sel(ID_ecall));
  assign bit_extender_1_out = {{20{ID_IR[31]}}, ID_IR[31:20]};  // Bit_Extender bit_extender_1
  assign bit_extender_2_out = {{20{ID_IR[31]}}, {ID_IR[31:25], ID_IR[11:7]}};  // Bit_Extender bit_extender_2
  assign CLK = nand_1_out ? clock_1_out : 1'bz;  // Controlled_Buffer controlled_buffer_1
  Multiplexer #(.select(1), .width(5), .disabled("Z"), .enable("false")) multiplexer_5 (
    .in0(ID_IR[19:15]), .in1(5'b10001), .out(ID_R1_num), .sel(ID_ecall));
  assign bit_extender_3_out = {{20{shifter_1_out[11]}}, shifter_1_out};  // Bit_Extender bit_extender_3
  Shifter #(.width(12), .shift("ll")) shifter_1 (
    .in({ID_IR[31], ID_IR[7], ID_IR[30:25], ID_IR[11:8]}), .\dist (4'b0001), .out(shifter_1_out));
  assign bit_extender_4_out = {{12{shifter_2_out[19]}}, shifter_2_out};  // Bit_Extender bit_extender_4
  Shifter #(.width(20), .shift("ll")) shifter_2 (
    .in({ID_IR[31], ID_IR[19:12], ID_IR[20], ID_IR[30:21]}), .\dist (5'b00001), .out(shifter_2_out));
  Pull_Resistor #(.pull(1)) pull_resistor_1 (.node(CLK));
  not not_2 (not_2_out, CLK);
  Regifile regifile_1 (
    .Din(RDin), .Clk(not_2_out), .R1(R1), .R2(R2), .WE(RegWrite), .W_num(W_num), .R1_num(ID_R1_num),
    .R2_num(ID_R2_num));
  Comparator #(.width(32), .mode("twosComplement")) comparator_2 (
    .a(R1), .b(32'h22), .eq(comparator_2_eq));  // open: gt, lt
  or or_2 (or_2_out, \数据相关 , or_1_out);
  and and_4 (and_4_out, ID_ecall, comparator_2_eq);
  and and_5 (ID_Halt, ~comparator_2_eq, ID_ecall, ~Go);  // AND_Gate
  ID_EX id_ex_1 (
    .PCin(ID_PC), .IRin(ID_IR), .ImmIin(bit_extender_1_out), .ImmSin(bit_extender_2_out),
    .ImmBin(bit_extender_3_out), .ImmJin(bit_extender_4_out), .R1in(R1), .R2in(R2),
    .AluOpin(\单周期硬布线控制器_1_alu_op ), .RST(or_2_out), .EN_H(en), .CLK(CLK), .Beqin(\单周期硬布线控制器_1_beq ),
    .Bnein(\单周期硬布线控制器_1_bne ), .MemToRegin(\单周期硬布线控制器_1_memtoreg ), .MemWritein(\单周期硬布线控制器_1_memwrite ),
    .AluSrcBin(\单周期硬布线控制器_1_alu_src ), .RegWritein(\单周期硬布线控制器_1_regwrite ), .S_typein(\单周期硬布线控制器_1_s_type ),
    .Jalin(\单周期硬布线控制器_1_jal ), .Jalrin(\单周期硬布线控制器_1_jalr ), .Haltin(ID_Halt), .Beqout(id_ex_1_beqout),
    .Bneout(id_ex_1_bneout), .MemToRegout(id_ex_1_memtoregout), .MemWriteout(id_ex_1_memwriteout),
    .AluSrcBout(id_ex_1_alusrcbout), .RegWriteout(EX_RegWrite), .S_Typeout(id_ex_1_s_typeout),
    .Jalout(EX_jal), .Jalrout(EX_jalr), .Haltout(id_ex_1_haltout), .AluOpout(id_ex_1_aluopout),
    .PCout(EX_PC), .IRout(EX_IR), .Imm_I_out(id_ex_1_imm_i_out), .Imm_S_out(id_ex_1_imm_s_out),
    .Imm_B_out(imm_B), .Imm_J_out(imm_J), .R1out(id_ex_1_r1out), .R2out(id_ex_1_r2out), .W_in(ID_IR[11:7]),
    .W_out(EX_W_num), .URETin(\单周期硬布线控制器_1_uret ), .LBUin(\单周期硬布线控制器_1_lbu ), .BLTUin(\单周期硬布线控制器_1_bltu ),
    .U_Typein(\单周期硬布线控制器_1_u_type ), .URETout(id_ex_1_uretout), .LBUout(BLTU), .BLTUout(id_ex_1_bltuout),
    .U_Typeout(id_ex_1_u_typeout), .ImmUin({ID_IR[31:12], {12{1'b0}}}), .ImmUout(id_ex_1_immuout),
    .Ecallin(ID_ecall), .Ecallout(EX_ecall));  // open: R1Forwardin, R1Forwardout, R2Forwardin, R2Forwardout, PJin, PJout
  Register #(.width(32), .trigger("rising"), .Select("low")) register_1 (
    .D(R2), .en(and_4_out), .Q(LedData), .clk(CLK), .clr(RST));
  Multiplexer #(.select(1), .width(32), .disabled("Z"), .enable("false")) multiplexer_6 (
    .in0(id_ex_1_imm_i_out), .in1(id_ex_1_imm_s_out), .out(multiplexer_6_out), .sel(id_ex_1_s_typeout));
  Multiplexer #(.select(1), .width(32), .disabled("Z"), .enable("false")) multiplexer_7 (
    .in0(id_ex_1_r2out), .in1(multiplexer_6_out), .out(multiplexer_7_out), .sel(id_ex_1_alusrcbout));
  and and_6 (and_6_out, id_ex_1_beqout, EQ);
  or or_3 (Branch, and_6_out, and_7_out, and_8_out);
  and and_7 (and_7_out, ~EQ, id_ex_1_bneout);  // AND_Gate
  and and_8 (and_8_out, BLTU, LT);
  ALU alu_1 (
    .X(id_ex_1_r1out), .Y(multiplexer_7_out), .AluOP(id_ex_1_aluopout), .Equal(EQ), .Result(JAddr), .out_6(LT));  // open: Result_2, out_4
  Counter #(.width(16), .max('hffff), .ongoal("wrap"), .trigger("rising"), .behavior("new")) counter_3 (
    .count(Branch), .Q(\分支成功数 ), .clk(CLK), .clr(RST));  // open: load, D, carry, preset, down
  EX_MEM ex_mem_1 (
    .PCin(EX_PC), .IRin(EX_IR), .Resultin(JAddr), .MDatain(id_ex_1_r2out), .PCout(M_PC), .IRout(MEM_IR),
    .Resultout(ex_mem_1_resultout), .Mdataout(MDin), .MemToRegin(id_ex_1_memtoregout),
    .MemWritein(id_ex_1_memwriteout), .Jalin(EX_jal), .RegWritein(EX_RegWrite), .Haltin(id_ex_1_haltout),
    .MemToRegout(ex_mem_1_memtoregout), .MemWriteout(MemWrite), .Jalout(ex_mem_1_jalout),
    .RegWriteout(MEM_RegWrite), .Haltout(ex_mem_1_haltout), .RST(RST), .EN_H(en), .CLK(CLK), .W_in(EX_W_num),
    .W_out(MEM_W_num), .URETin(id_ex_1_uretout), .LBUin(BLTU), .BLTUin(id_ex_1_bltuout),
    .U_Typein(id_ex_1_u_typeout), .URETout(ex_mem_1_uretout), .LBUout(ex_mem_1_lbuout),
    .BLTUout(ex_mem_1_bltuout), .U_Typeout(ex_mem_1_u_typeout), .Jalrin(EX_jalr), .Jalrout(ex_mem_1_jalrout),
    .ImmUin(id_ex_1_immuout), .ImmUout(ex_mem_1_immuout));
  RAM #(.addrWidth(10), .dataWidth(32), .bus("separate"), .Select("high")) ram_1 (
    .addr(ex_mem_1_resultout[11:2]), .din(MDin), .data(ram_1_data), .str(MemWrite), .clk(CLK),
    .ld(ex_mem_1_memtoregout), .clr(RST));  // open: sel
  MEM_WB mem_wb_1 (
    .PCin(M_PC), .IRin(MEM_IR), .Resultin(ex_mem_1_resultout), .RMDatain(ram_1_data), .PCout(WB_PC),
    .IRout(WB_IR), .Resultout(mem_wb_1_resultout), .RMdataout(mem_wb_1_rmdataout), .RST(RST),
    .W_in(MEM_W_num), .EN_H(en), .W_out(W_num), .CLK(CLK), .MemToRegin(ex_mem_1_memtoregout),
    .Jalin(ex_mem_1_jalout), .RegWritein(MEM_RegWrite), .Haltin(ex_mem_1_haltout),
    .MemToRegout(mem_wb_1_memtoregout), .RegWriteout(RegWrite), .Jalrin(ex_mem_1_jalrout),
    .URETin(ex_mem_1_uretout), .LBUin(ex_mem_1_lbuout), .BLTUin(ex_mem_1_bltuout),
    .U_Typein(ex_mem_1_u_typeout), .Jalout(mem_wb_1_jalout), .Jalrout(mem_wb_1_jalrout),
    .LBUout(mem_wb_1_lbuout), .U_Typeout(WB_U_Type), .ImmUin(ex_mem_1_immuout), .ImmUout(mem_wb_1_immuout),
    .Indexin(ex_mem_1_resultout[1:0]), .Indexout(mem_wb_1_indexout), .Haltout(mem_wb_1_haltout));  // open: URETout, BLTUout
  Multiplexer #(.select(2), .width(8), .disabled("Z"), .enable("false")) multiplexer_8 (
    .in0(mem_wb_1_rmdataout[7:0]), .in1(mem_wb_1_rmdataout[15:8]), .in2(mem_wb_1_rmdataout[23:16]),
    .in3(mem_wb_1_rmdataout[31:24]), .out(multiplexer_8_out), .sel(mem_wb_1_indexout));
  and and_9 (halt, mem_wb_1_haltout, ~Go);  // AND_Gate
  not not_3 (en, halt);
  Adder #(.width(32)) adder_4 (.a(32'h4), .b(WB_PC), .out(WB_PC_4));  // open: cin, cout
  or or_4 (or_4_out, mem_wb_1_jalout, mem_wb_1_jalrout, WB_U_Type);
  assign bit_extender_5_out = {{24{1'b0}}, multiplexer_8_out};  // Bit_Extender bit_extender_5
  Adder #(.width(32)) adder_5 (.a(WB_PC), .b(mem_wb_1_immuout), .out(adder_5_out));  // open: cin, cout
  Multiplexer #(.select(1), .width(32), .disabled("Z"), .enable("false")) multiplexer_9 (
    .in0(mem_wb_1_resultout), .in1(multiplexer_10_out), .out(multiplexer_9_out), .sel(mem_wb_1_memtoregout));
  Multiplexer #(.select(1), .width(32), .disabled("Z"), .enable("false")) multiplexer_10 (
    .in0(mem_wb_1_rmdataout), .in1(bit_extender_5_out), .out(multiplexer_10_out), .sel(mem_wb_1_lbuout));
  Multiplexer #(.select(1), .width(32), .disabled("Z"), .enable("false")) multiplexer_11 (
    .in0(WB_PC_4), .in1(adder_5_out), .out(multiplexer_11_out), .sel(WB_U_Type));
  Multiplexer #(.select(1), .width(32), .disabled("Z"), .enable("false")) multiplexer_12 (
    .in0(multiplexer_9_out), .in1(multiplexer_11_out), .out(RDin), .sel(or_4_out));

  // Other names for the same wires on the sheet: IR[31:0] = ID_IR; RD_num[4:0] = ID_IR[11:7]; MEM_MemWrite = MemWrite;
  //   MEM_PC[31:0] = M_PC; WB_RegWrite = RegWrite; WriteBackData[31:0] = RDin

  // Notes on the sheet:
  //   中断源
  //   时空图监测，可删除
  //   中断等待指示
  //   数码管输出
  //   指令存储器
  //   contents of rom_1 (hex, n*v repeats v):
  //   100493 100006f 100493 200913 300993 100006f 100493 200913 300993 100006f 100493 200913 300993
  //   100006f 100493 200913 300993 29c000ef 100413 100493 1f49493 900533 2200893 73 24d493 48463 fedff06f
  //   900533 2200893 73 100493 249493 900533 2200893 73 48463 fedff06f 100493 1f49493 900533 2200893 73
  //   4034d493 900533 2200893 73 4044d493 900533 2200893 73 4044d493 900533 2200893 73 4044d493 900533
  //   2200893 73 4044d493 900533 2200893 73 4044d493 900533 2200893 73 4044d493 900533 2200893 73 4044d493
  //   900533 2200893 73 100413 1f41993 41f9d993 433 c00913 300b13 140413 f47413 800293 100313 499993
  //   89e9b3 1300533 2200893 73 406282b3 fe0294e3 140413 f00f93 1f47433 1c41413 800293 100313 49d993
  //   89e9b3 1300533 2200893 73 406282b3 fe0294e3 1c45413 406b0b33 b0463 f95ff06f 2b3 fff2c293 829293
  //   ff2e293 500533 2200893 73 fff00413 493 84a023 140413 448493 84a023 140413 448493 84a023 140413
  //   448493 84a023 140413 448493 84a023 140413 448493 84a023 140413 448493 84a023 140413 448493 84a023
  //   140413 448493 84a023 140413 448493 84a023 140413 448493 84a023 140413 448493 84a023 140413 448493
  //   84a023 140413 448493 84a023 140413 448493 84a023 140413 448493 84a023 140413 448493 140413 433
  //   3c00493 42983 4aa03 149a2b3 28663 134a023 1442023 ffc48493 fe9412e3 800533 2200893 73 440413 3c00493
  //   fc9416e3 a00893 73 413 140413 800533 2200893 73 240413 800533 2200893 73 340413 800533 2200893 73
  //   440413 800533 2200893 73 540413 800533 2200893 73 640413 800533 2200893 73 740413 800533 2200893 73
  //   840413 800533 2200893 2200893 73 8067
  //   控制位
  //   流水调试日志用
  //   暂停节拍，不能为0
  //   指令字
  //   戳工具置1进入计数暂停模式，ctrl+k时钟自动运行到对应节拍暂停
  //   ctrl+k关闭时钟连续运行，将控制位置零，进入单步调试模式调试
  //   rs1
  //   rs2
  //   rd
  //   可计数暂停的时钟源
  //   为方便自动评测，需要输出流水线各段保存的PC值，注意是PC不是PC+4，另外ID段寄存器写入信息，Mem段内存写入信息也要输出
endmodule
module \重定向流水线  (
  output RegWrite,
  output MemWrite,
  output [31:0] IF_PC,
  output [31:0] ID_PC,
  output [31:0] EX_PC,
  output [31:0] M_PC,
  output [31:0] WB_PC,
  output [31:0] RDin,
  output [31:0] MDin,
  output [31:0] LedData
);

  wire and_2_out, and_3_out, and_4_out, and_5_out, and_6_out, and_7_out, BLTU, Branch, CLK, clock_1_out,
       comparator_1_eq, comparator_1_lt, comparator_2_eq, d_ff_1_q, en, EQ, EX_AluSrcB, EX_ecall, EX_Halt,
       EX_jal, EX_jalr, ex_mem_1_bltuout, ex_mem_1_haltout, ex_mem_1_jalout, ex_mem_1_jalrout,
       ex_mem_1_lbuout, ex_mem_1_memtoregout, ex_mem_1_u_typeout, ex_mem_1_uretout, EX_RegWrite, EX_S_Type,
       Go, halt, ID_ecall, id_ex_1_beqout, id_ex_1_bltuout, id_ex_1_bneout, id_ex_1_memtoregout,
       id_ex_1_memwriteout, id_ex_1_u_typeout, id_ex_1_uretout, IR1, IR2, IR3, LoadUse, LT, MEM_RegWrite,
       mem_wb_1_haltout, mem_wb_1_jalout, mem_wb_1_jalrout, mem_wb_1_lbuout, mem_wb_1_memtoregout,
       nand_1_out, not_1_out, not_2_out, or_1_out, or_2_out, or_4_out, RST, W1, W2, W3, WB_U_Type,
       \单周期硬布线控制器_1_alu_src , \单周期硬布线控制器_1_beq , \单周期硬布线控制器_1_bltu , \单周期硬布线控制器_1_bne , \单周期硬布线控制器_1_jal ,
       \单周期硬布线控制器_1_jalr , \单周期硬布线控制器_1_lbu , \单周期硬布线控制器_1_memtoreg , \单周期硬布线控制器_1_memwrite ,
       \单周期硬布线控制器_1_r1 , \单周期硬布线控制器_1_r2 , \单周期硬布线控制器_1_regwrite , \单周期硬布线控制器_1_s_type ,
       \单周期硬布线控制器_1_u_type , \单周期硬布线控制器_1_uret , \数据相关 ;
  wire [1:0] EX_R1Forward, EX_R2Forward, mem_wb_1_indexout, R1Forward, R2Forward;
  wire [3:0] id_ex_1_aluopout, \单周期硬布线控制器_1_alu_op ;
  wire [4:0] EX_W_num, ID_R1_num, ID_R2_num, MEM_W_num, W_num;
  wire [7:0] multiplexer_10_out;
  wire [11:0] shifter_1_out;
  wire [12:0] CNT_num;
  wire [15:0] \LoadUse次数 , \分支成功数 , \总周期数 , \插入气泡数 , \无条件分支数 , \条件分支成功数 ;
  wire [19:0] shifter_2_out;
  wire [31:0] adder_1_out, adder_2_out, adder_4_out, Ain, and_1_out, Bin, bit_extender_1_out,
       bit_extender_2_out, bit_extender_3_out, bit_extender_4_out, bit_extender_5_out, EX_IR,
       ex_mem_1_immuout, EX_R1F, EX_R2, EX_R2F, id_ex_1_immuout, ID_IR, IF_IR, imm_B, imm_I, imm_J, imm_S,
       JAddr, MEM_IR, MEM_Result, mem_wb_1_immuout, mem_wb_1_resultout, mem_wb_1_rmdataout,
       multiplexer_1_out, multiplexer_2_out, multiplexer_3_out, multiplexer_8_out, multiplexer_11_out,
       multiplexer_12_out, multiplexer_13_out, PC_4, R1, R2, ram_1_data, WB_IR, WB_PC_4;

  Button \u_总复位  (.out(RST));
  Button _1 (.out(IR1));
  Button _2 (.out(IR2));
  Button _3 (.out(IR3));
  // Probe on \总周期数 
  // Probe on \总周期数 
  Button \u_继续运行  (.out(Go));
  LED #(.active("true")) led_1 (.in(W1));
  LED #(.active("true")) led_2 (.in(W2));
  LED #(.active("true")) led_3 (.in(W3));
  // Probe on \分支成功数 
  Hex_Digit_Display hex_digit_display_1 (.value(LedData[31:28]));  // open: dp
  // Probe on IF_PC[19:0]
  // RiscV_Probe riscv_probe_1: pin names not known; wires that end beside it: IF_IR
  Hex_Digit_Display hex_digit_display_2 (.value(LedData[23:20]));  // open: dp
  Hex_Digit_Display hex_digit_display_3 (.value(LedData[27:24]));  // open: dp
  // Probe on ID_PC[19:0]
  // RiscV_Probe riscv_probe_2: pin names not known; wires that end beside it: ID_IR
  not not_1 (not_1_out, halt);
  Adder #(.width(32)) adder_1 (.a(imm_J), .b(EX_PC), .out(adder_1_out));  // open: cin, cout
  Hex_Digit_Display hex_digit_display_4 (.value(LedData[15:12]));  // open: dp
  Hex_Digit_Display hex_digit_display_5 (.value(LedData[19:16]));  // open: dp
  Counter #(.width(16), .max('hffff), .ongoal("wrap"), .trigger("rising"), .behavior("new")) counter_1 (
    .count(not_1_out), .Q(\总周期数 ), .clk(CLK), .clr(RST));  // open: load, D, carry, preset, down
  Multiplexer #(.select(1), .width(32), .disabled("Z"), .enable("false")) multiplexer_1 (
    .in0(PC_4), .in1(adder_1_out), .out(multiplexer_1_out), .sel(EX_jal));
  assign and_1_out = JAddr & 32'hfffffffe;  // AND_Gate and_1, 32 bits wide
  Adder #(.width(32)) adder_2 (.a(imm_B), .b(EX_PC), .out(adder_2_out));  // open: cin, cout
  Hex_Digit_Display hex_digit_display_6 (.value(LedData[11:8]));  // open: dp
  Hex_Digit_Display hex_digit_display_7 (.value(LedData[7:4]));  // open: dp
  // Probe on EX_PC[19:0]
  // RiscV_Probe riscv_probe_3: pin names not known; wires that end beside it: EX_IR
  Multiplexer #(.select(1), .width(32), .disabled("Z"), .enable("false")) multiplexer_2 (
    .in0(multiplexer_1_out), .in1(and_1_out), .out(multiplexer_2_out), .sel(EX_jalr));
  Hex_Digit_Display hex_digit_display_8 (.value(LedData[3:0]));  // open: dp
  Multiplexer #(.select(1), .width(32), .disabled("Z"), .enable("false")) multiplexer_3 (
    .in0(multiplexer_2_out), .in1(adder_2_out), .out(multiplexer_3_out), .sel(Branch));
  Register #(.width(32), .trigger("rising"), .Select("low")) PC (
    .D(multiplexer_3_out), .en(and_2_out), .Q(IF_PC), .clk(CLK), .clr(RST));
  and and_2 (and_2_out, ~LoadUse, ~halt);  // AND_Gate
  // Probe on \总周期数 
  // Probe on M_PC[19:0]
  // RiscV_Probe riscv_probe_4: pin names not known; wires that end beside it: MEM_IR
  // Probe on \总周期数 
  // Probe on \无条件分支数 
  // Probe on \条件分支成功数 
  // Probe on \插入气泡数 
  // Probe on \LoadUse次数 
  // Probe on IF_PC[11:0]
  // Probe on WB_PC[19:0]
  // RiscV_Probe riscv_probe_5: pin names not known; wires that end beside it: WB_IR
  ROM #(.addrWidth(10), .dataWidth(32), .Select("high")) rom_1 (.addr(IF_PC[11:2]), .data(IF_IR));
  Adder #(.width(32)) adder_3 (.a(IF_PC), .b(32'h4), .out(PC_4));  // open: cin, cout
  // Probe on EX_PC[11:0]
  // Probe on ID_PC[11:0]
  or or_1 (or_1_out, RST, Branch, EX_jalr, EX_jal);
  IF_ID if_id_1 (
    .PCin(IF_PC), .IRin(IF_IR), .PCout(ID_PC), .IRout(ID_IR), .RST(or_1_out), .EN_H(and_3_out), .CLK(CLK));  // open: PJin, PJout
  and and_3 (and_3_out, ~LoadUse, en);  // AND_Gate
  // Probe on M_PC[11:0]
  D_Flip_Flop #(.trigger("high"), .Pre_Clr_Positions("LEGACY"), .NegatePresetClear("false"), .enable("true"), .NewFFLayout("false")) d_ff_1 (.Q(d_ff_1_q));  // open: clk, D, Qn, preset, en, reset
  // Probe on 13'hc
  // Probe on WB_PC[11:0]
  Comparator #(.width(13), .mode("twosComplement")) comparator_1 (
    .a(CNT_num), .b(13'hc), .eq(comparator_1_eq), .lt(comparator_1_lt));  // open: gt
  Clock #(.highDuration(1), .lowDuration(1)) clock_1 (.out(clock_1_out));
  nand nand_1 (nand_1_out, d_ff_1_q, comparator_1_eq);
  Counter #(.width(13), .max('h1fff), .ongoal("stay"), .trigger("rising"), .behavior("old")) counter_2 (
    .count(comparator_1_lt), .Q(CNT_num), .clk(clock_1_out));  // open: load, D, carry, clr, preset
  \数据冲突处理_重定向  \u_数据冲突处理_重定向_1  (
    .ID_R1(\单周期硬布线控制器_1_r1 ), .EX_RW(EX_RegWrite), .ID_R2(\单周期硬布线控制器_1_r2 ), .MEM_RW(MEM_RegWrite),
    .ID_R1_num(ID_R1_num), .EX_W_num(EX_W_num), .ID_R2_num(ID_R2_num), .MEM_W_num(MEM_W_num),
    .EX_OP(EX_IR[6:2]), .\数据相关 (\数据相关 ), .LoadUse(LoadUse), .R1Forward(R1Forward), .R2Forward(R2Forward));
  \单周期硬布线控制器  \u_单周期硬布线控制器_1  (
    .Funct({ID_IR[30], ID_IR[25], ID_IR[14:12]}), .OP(ID_IR[6:2]), .ALU_OP(\单周期硬布线控制器_1_alu_op ),
    .MemToReg(\单周期硬布线控制器_1_memtoreg ), .MemWrite(\单周期硬布线控制器_1_memwrite ), .ALU_SRC(\单周期硬布线控制器_1_alu_src ),
    .RegWrite(\单周期硬布线控制器_1_regwrite ), .ecall(ID_ecall), .S_type(\单周期硬布线控制器_1_s_type ),
    .Jalr(\单周期硬布线控制器_1_jalr ), .Beq(\单周期硬布线控制器_1_beq ), .JAL(\单周期硬布线控制器_1_jal ), .Bne(\单周期硬布线控制器_1_bne ),
    .in_3(ID_IR[21]), .uret(\单周期硬布线控制器_1_uret ), .BLTU(\单周期硬布线控制器_1_bltu ), .U_Type(\单周期硬布线控制器_1_u_type ),
    .LBU(\单周期硬布线控制器_1_lbu ), .R1(\单周期硬布线控制器_1_r1 ), .R2(\单周期硬布线控制器_1_r2 ));  // open: CSRRSI, CSRRCI
  Multiplexer #(.select(1), .width(5), .disabled("Z"), .enable("false")) multiplexer_4 (
    .in0(ID_IR[24:20]), .in1(5'b01010), .out(ID_R2_num), .sel(ID_ecall));
  assign bit_extender_1_out = {{20{ID_IR[31]}}, ID_IR[31:20]};  // Bit_Extender bit_extender_1
  assign bit_extender_2_out = {{20{ID_IR[31]}}, {ID_IR[31:25], ID_IR[11:7]}};  // Bit_Extender bit_extender_2
  assign CLK = nand_1_out ? clock_1_out : 1'bz;  // Controlled_Buffer controlled_buffer_1
  Multiplexer #(.select(1), .width(5), .disabled("Z"), .enable("false")) multiplexer_5 (
    .in0(ID_IR[19:15]), .in1(5'b10001), .out(ID_R1_num), .sel(ID_ecall));
  Shifter #(.width(12), .shift("ll")) shifter_1 (
    .in({ID_IR[31], ID_IR[7], ID_IR[30:25], ID_IR[11:8]}), .\dist (4'b0001), .out(shifter_1_out));
  Shifter #(.width(20), .shift("ll")) shifter_2 (
    .in({ID_IR[31], ID_IR[19:12], ID_IR[20], ID_IR[30:21]}), .\dist (5'b00001), .out(shifter_2_out));
  Pull_Resistor #(.pull(1)) pull_resistor_1 (.node(CLK));
  assign bit_extender_3_out = {{20{shifter_1_out[11]}}, shifter_1_out};  // Bit_Extender bit_extender_3
  assign bit_extender_4_out = {{12{shifter_2_out[19]}}, shifter_2_out};  // Bit_Extender bit_extender_4
  not not_2 (not_2_out, CLK);
  Regifile regifile_1 (
    .Din(RDin), .Clk(not_2_out), .R1(R1), .R2(R2), .WE(RegWrite), .W_num(W_num), .R1_num(ID_R1_num),
    .R2_num(ID_R2_num));
  or or_2 (or_2_out, LoadUse, or_1_out);
  ID_EX id_ex_1 (
    .PCin(ID_PC), .IRin(ID_IR), .ImmIin(bit_extender_1_out), .ImmSin(bit_extender_2_out),
    .ImmBin(bit_extender_3_out), .ImmJin(bit_extender_4_out), .R1in(R1), .R2in(R2),
    .AluOpin(\单周期硬布线控制器_1_alu_op ), .RST(or_2_out), .EN_H(en), .CLK(CLK), .Beqin(\单周期硬布线控制器_1_beq ),
    .Bnein(\单周期硬布线控制器_1_bne ), .MemToRegin(\单周期硬布线控制器_1_memtoreg ), .MemWritein(\单周期硬布线控制器_1_memwrite ),
    .AluSrcBin(\单周期硬布线控制器_1_alu_src ), .RegWritein(\单周期硬布线控制器_1_regwrite ), .S_typein(\单周期硬布线控制器_1_s_type ),
    .Jalin(\单周期硬布线控制器_1_jal ), .Jalrin(\单周期硬布线控制器_1_jalr ), .Haltin(1'b0), .Beqout(id_ex_1_beqout),
    .Bneout(id_ex_1_bneout), .MemToRegout(id_ex_1_memtoregout), .MemWriteout(id_ex_1_memwriteout),
    .AluSrcBout(EX_AluSrcB), .RegWriteout(EX_RegWrite), .S_Typeout(EX_S_Type), .Jalout(EX_jal),
    .Jalrout(EX_jalr), .AluOpout(id_ex_1_aluopout), .PCout(EX_PC), .IRout(EX_IR), .Imm_I_out(imm_I),
    .Imm_S_out(imm_S), .Imm_B_out(imm_B), .Imm_J_out(imm_J), .R1out(EX_R1F), .R2out(EX_R2F),
    .W_in(ID_IR[11:7]), .W_out(EX_W_num), .URETin(\单周期硬布线控制器_1_uret ), .LBUin(\单周期硬布线控制器_1_lbu ),
    .BLTUin(\单周期硬布线控制器_1_bltu ), .U_Typein(\单周期硬布线控制器_1_u_type ), .URETout(id_ex_1_uretout), .LBUout(BLTU),
    .BLTUout(id_ex_1_bltuout), .U_Typeout(id_ex_1_u_typeout), .ImmUin({ID_IR[31:12], {12{1'b0}}}),
    .ImmUout(id_ex_1_immuout), .Ecallin(ID_ecall), .Ecallout(EX_ecall), .R1Forwardin(R1Forward),
    .R1Forwardout(EX_R1Forward), .R2Forwardin(R2Forward), .R2Forwardout(EX_R2Forward));  // open: Haltout, PJin, PJout
  Comparator #(.width(32), .mode("twosComplement")) comparator_2 (
    .a(Ain), .b(32'h22), .eq(comparator_2_eq));  // open: gt, lt
  Multiplexer #(.select(2), .width(32), .disabled("Z"), .enable("false")) multiplexer_6 (
    .in0(EX_R1F), .in1(RDin), .in2(MEM_Result), .out(Ain), .sel(EX_R1Forward));  // open: in3
  Multiplexer #(.select(2), .width(32), .disabled("Z"), .enable("false")) multiplexer_7 (
    .in0(EX_R2F), .in1(RDin), .in2(MEM_Result), .out(EX_R2), .sel(EX_R2Forward));  // open: in3
  Multiplexer #(.select(1), .width(32), .disabled("Z"), .enable("false")) multiplexer_8 (
    .in0(imm_I), .in1(imm_S), .out(multiplexer_8_out), .sel(EX_S_Type));
  and and_4 (and_4_out, id_ex_1_beqout, EQ);
  or or_3 (Branch, and_4_out, and_5_out, and_6_out);
  and and_5 (and_5_out, ~EQ, id_ex_1_bneout);  // AND_Gate
  and and_6 (and_6_out, BLTU, LT);
  ALU alu_1 (
    .X(Ain), .Y(Bin), .AluOP(id_ex_1_aluopout), .Equal(EQ), .Result(JAddr), .out_6(LT));  // open: Result_2, out_4
  Multiplexer #(.select(1), .width(32), .disabled("Z"), .enable("false")) multiplexer_9 (
    .in0(EX_R2), .in1(multiplexer_8_out), .out(Bin), .sel(EX_AluSrcB));
  Register #(.width(32), .trigger("rising"), .Select("low")) register_1 (
    .D(EX_R2), .en(and_7_out), .Q(LedData), .clk(CLK), .clr(RST));
  and and_7 (and_7_out, EX_ecall, comparator_2_eq);
  and and_8 (EX_Halt, ~comparator_2_eq, EX_ecall, ~Go);  // AND_Gate
  Counter #(.width(16), .max('hffff), .ongoal("wrap"), .trigger("rising"), .behavior("new")) counter_3 (
    .count(Branch), .Q(\分支成功数 ), .clk(CLK), .clr(RST));  // open: load, D, carry, preset, down
  EX_MEM ex_mem_1 (
    .PCin(EX_PC), .IRin(EX_IR), .Resultin(JAddr), .MDatain(EX_R2), .PCout(M_PC), .IRout(MEM_IR),
    .Resultout(MEM_Result), .Mdataout(MDin), .MemToRegin(id_ex_1_memtoregout),
    .MemWritein(id_ex_1_memwriteout), .Jalin(EX_jal), .RegWritein(EX_RegWrite), .Haltin(EX_Halt),
    .MemToRegout(ex_mem_1_memtoregout), .MemWriteout(MemWrite), .Jalout(ex_mem_1_jalout),
    .RegWriteout(MEM_RegWrite), .Haltout(ex_mem_1_haltout), .RST(RST), .EN_H(en), .CLK(CLK), .W_in(EX_W_num),
    .W_out(MEM_W_num), .URETin(id_ex_1_uretout), .LBUin(BLTU), .BLTUin(id_ex_1_bltuout),
    .U_Typein(id_ex_1_u_typeout), .URETout(ex_mem_1_uretout), .LBUout(ex_mem_1_lbuout),
    .BLTUout(ex_mem_1_bltuout), .U_Typeout(ex_mem_1_u_typeout), .Jalrin(EX_jalr), .Jalrout(ex_mem_1_jalrout),
    .ImmUin(id_ex_1_immuout), .ImmUout(ex_mem_1_immuout));
  RAM #(.addrWidth(10), .dataWidth(32), .bus("separate"), .Select("high")) ram_1 (
    .addr(MEM_Result[11:2]), .din(MDin), .data(ram_1_data), .str(MemWrite), .clk(CLK),
    .ld(ex_mem_1_memtoregout), .clr(RST));  // open: sel
  MEM_WB mem_wb_1 (
    .PCin(M_PC), .IRin(MEM_IR), .Resultin(MEM_Result), .RMDatain(ram_1_data), .PCout(WB_PC), .IRout(WB_IR),
    .Resultout(mem_wb_1_resultout), .RMdataout(mem_wb_1_rmdataout), .RST(RST), .W_in(MEM_W_num), .EN_H(en),
    .W_out(W_num), .CLK(CLK), .MemToRegin(ex_mem_1_memtoregout), .Jalin(ex_mem_1_jalout),
    .RegWritein(MEM_RegWrite), .Haltin(ex_mem_1_haltout), .MemToRegout(mem_wb_1_memtoregout),
    .RegWriteout(RegWrite), .Jalrin(ex_mem_1_jalrout), .URETin(ex_mem_1_uretout), .LBUin(ex_mem_1_lbuout),
    .BLTUin(ex_mem_1_bltuout), .U_Typein(ex_mem_1_u_typeout), .Jalout(mem_wb_1_jalout),
    .Jalrout(mem_wb_1_jalrout), .LBUout(mem_wb_1_lbuout), .U_Typeout(WB_U_Type), .ImmUin(ex_mem_1_immuout),
    .ImmUout(mem_wb_1_immuout), .Indexin(MEM_Result[1:0]), .Indexout(mem_wb_1_indexout),
    .Haltout(mem_wb_1_haltout));  // open: URETout, BLTUout
  Multiplexer #(.select(2), .width(8), .disabled("Z"), .enable("false")) multiplexer_10 (
    .in0(mem_wb_1_rmdataout[7:0]), .in1(mem_wb_1_rmdataout[15:8]), .in2(mem_wb_1_rmdataout[23:16]),
    .in3(mem_wb_1_rmdataout[31:24]), .out(multiplexer_10_out), .sel(mem_wb_1_indexout));
  and and_9 (halt, mem_wb_1_haltout, ~Go);  // AND_Gate
  not not_3 (en, halt);
  or or_4 (or_4_out, mem_wb_1_jalout, mem_wb_1_jalrout, WB_U_Type);
  assign bit_extender_5_out = {{24{1'b0}}, multiplexer_10_out};  // Bit_Extender bit_extender_5
  Adder #(.width(32)) adder_4 (.a(WB_PC), .b(mem_wb_1_immuout), .out(adder_4_out));  // open: cin, cout
  Adder #(.width(32)) adder_5 (.a(32'h4), .b(WB_PC), .out(WB_PC_4));  // open: cin, cout
  Multiplexer #(.select(1), .width(32), .disabled("Z"), .enable("false")) multiplexer_11 (
    .in0(mem_wb_1_resultout), .in1(multiplexer_12_out), .out(multiplexer_11_out), .sel(mem_wb_1_memtoregout));
  Multiplexer #(.select(1), .width(32), .disabled("Z"), .enable("false")) multiplexer_12 (
    .in0(mem_wb_1_rmdataout), .in1(bit_extender_5_out), .out(multiplexer_12_out), .sel(mem_wb_1_lbuout));
  Multiplexer #(.select(1), .width(32), .disabled("Z"), .enable("false")) multiplexer_13 (
    .in0(WB_PC_4), .in1(adder_4_out), .out(multiplexer_13_out), .sel(WB_U_Type));
  Multiplexer #(.select(1), .width(32), .disabled("Z"), .enable("false")) multiplexer_14 (
    .in0(multiplexer_11_out), .in1(multiplexer_13_out), .out(RDin), .sel(or_4_out));

  // Other names for the same wires on the sheet: IR[31:0] = ID_IR; RD_num[4:0] = ID_IR[11:7]; EX_R1[31:0] = Ain;
  //   MEM_MemWrite = MemWrite; MEM_PC[31:0] = M_PC; WB_RegWrite = RegWrite; WriteBackData[31:0] = RDin

  // Notes on the sheet:
  //   中断源
  //   时空图监测，可删除
  //   中断等待指示
  //   数码管输出
  //   指令存储器
  //   contents of rom_1 (hex, n*v repeats v):
  //   13 430497 900533 2200893 73 430497 900533 2200893 73 430497 900533 2200893 73 430497 900533 2200893
  //   73 430497 900533 2200893 73 430497 900533 2200893 73 430497 900533 2200893 73 430497 900533 2200893
  //   73 a00893 73
  //   控制位
  //   流水调试日志用
  //   暂停节拍，不能为0
  //   戳工具置1进入计数暂停模式，ctrl+k时钟自动运行到对应节拍暂停
  //   ctrl+k关闭时钟连续运行，将控制位置零，进入单步调试模式调试
  //   ctrl+k关闭时钟连续运行，将控制位置零，进入单步调试模式调试
  //   rs1
  //   rs2
  //   指令字
  //   rd
  //   可计数暂停的时钟源
  //   为方便自动评测，需要输出流水线各段保存的PC值，注意是PC不是PC+4，另外ID段寄存器写入信息，Mem段内存写入信息也要输出
endmodule

module \中断按键参考电路  (
  input  \同步清零信号 ,
  output \与中断屏蔽位与 
);

  wire \_1号中断_out , and_1_out, clock_1_out, d_ff_1_q, or_1_out, or_2_out;

  Clock #(.highDuration(1), .lowDuration(1)) clock_1 (.out(clock_1_out));
  Button \_1号中断  (.out(\_1号中断_out ));
  LED #(.active("true")) \_1号中断等待指示灯  (.in(or_1_out));
  or or_1 (or_1_out, \与中断屏蔽位与 , d_ff_1_q);
  D_Flip_Flop #(.trigger("rising"), .Pre_Clr_Positions("LEGACY"), .NegatePresetClear("false"), .enable("true"), .NewFFLayout("false")) d_ff_1 (
    .clk(\_1号中断_out ), .D(1'b1), .Q(d_ff_1_q), .reset(\与中断屏蔽位与 ));  // open: Qn, preset, en
  or or_2 (or_2_out, d_ff_1_q, \与中断屏蔽位与 );
  and and_1 (and_1_out, or_2_out, ~\同步清零信号 );  // AND_Gate
  D_Flip_Flop #(.trigger("rising"), .Pre_Clr_Positions("LEGACY"), .NegatePresetClear("false"), .enable("true"), .NewFFLayout("false")) IR1 (
    .clk(clock_1_out), .D(and_1_out), .Q(\与中断屏蔽位与 ));  // open: Qn, preset, en, reset

  // Notes on the sheet:
  //   中断信号采样参考电路
  //   Reset 
endmodule

module \单周期_单级中断  (
  input  IR1,
  input  IR2,
  input  IR3,
  output RegWrite,
  output MemWrite,
  output [31:0] PC,
  output [31:0] IR,
  output [31:0] RDin,
  output [31:0] MDin,
  output [31:0] LedData
);

  wire AluSrcB, and_2_out, and_3_out, and_4_out, and_5_out, and_7_out, and_8_out, and_9_out, beq, bltu, bne,
       Branch, CLK, clock_1_out, comparator_1_eq, comparator_2_eq, comparator_3_eq, comparator_4_eq,
       comparator_5_eq, comparator_6_eq, comparator_6_lt, d_ff_1_q, d_ff_2_q, d_ff_3_q, d_ff_4_q,
       decoder_1_out1, decoder_1_out2, decoder_1_out3, ecall, EQ, Go, halt, IE_q, Inter1, Inter2, Inter3,
       Interr, Interrupt, IR1_t, IR2_t, IR3_t, IRA, IRB, IRC, jal, jalr, lbu, LT, MemToReg, nand_1_out,
       not_1_out, not_2_out, not_3_out, not_4_out, or_1_out, or_6_out, or_10_out, or_12_out, or_13_out,
       PCToReg, Ret1, Ret2, Ret3, RST, S_type, U_type, uret, W1, W2, W3;
  wire [1:0] Index, priority_encoder_1_out, \中断号_q ;
  wire [3:0] AluOP;
  wire [4:0] multiplexer_7_out, multiplexer_8_out;
  wire [7:0] multiplexer_14_out;
  wire [11:0] imm12_B;
  wire [12:0] CNT_num;
  wire [15:0] \分支成功数 , \总周期数 ;
  wire [19:0] imm20_J;
  wire [31:0] adder_1_out, adder_2_out, adder_3_out, and_1_out, bit_extender_1_out, bit_extender_2_out,
       bit_extender_3_out, bit_extender_4_out, bit_extender_5_out, EPC, InterAddr, MDout, multiplexer_1_out,
       multiplexer_2_out, multiplexer_4_out, multiplexer_5_out, multiplexer_9_out, multiplexer_11_out,
       multiplexer_12_out, nextPC, PC_4, R1, ram_1_data, RPCin;
  wire [31:2] Result;

  Button \u_继续运行  (.out(Go));
  Button _1 ();  // open: out
  Button _2 ();  // open: out
  Button _3 ();  // open: out
  LED #(.active("true")) led_1 (.in(W1));
  LED #(.active("true")) led_2 (.in(W2));
  LED #(.active("true")) led_3 (.in(W3));
  Button button_1 (.out(RST));
  Hex_Digit_Display hex_digit_display_1 (.value(LedData[31:28]));  // open: dp
  Comparator #(.width(16), .mode("twosComplement")) comparator_1 (
    .a(16'h23b), .b(\总周期数 ), .eq(comparator_1_eq));  // open: gt, lt
  Comparator #(.width(16), .mode("twosComplement")) comparator_2 (
    .a(\总周期数 ), .b(16'h1), .eq(comparator_2_eq));  // open: gt, lt
  Comparator #(.width(16), .mode("twosComplement")) comparator_3 (
    .a(\总周期数 ), .b(16'h4), .eq(comparator_3_eq));  // open: gt, lt
  Comparator #(.width(16), .mode("twosComplement")) comparator_4 (
    .a(\总周期数 ), .b(16'h7), .eq(comparator_4_eq));  // open: gt, lt
  Hex_Digit_Display hex_digit_display_2 (.value(LedData[27:24]));  // open: dp
  Hex_Digit_Display hex_digit_display_3 (.value(LedData[23:20]));  // open: dp
  or or_1 (or_1_out, comparator_1_eq, comparator_2_eq);
  assign IRA = or_1_out ? ~CLK : 1'bz;  // Controlled_Inverter controlled_inverter_1
  assign IRB = comparator_3_eq ? ~CLK : 1'bz;  // Controlled_Inverter controlled_inverter_2
  assign IRC = comparator_4_eq ? ~CLK : 1'bz;  // Controlled_Inverter controlled_inverter_3
  assign bit_extender_1_out = {{12{imm20_J[19]}}, imm20_J};  // Bit_Extender bit_extender_1
  Hex_Digit_Display hex_digit_display_4 (.value(LedData[19:16]));  // open: dp
  Hex_Digit_Display hex_digit_display_5 (.value(LedData[15:12]));  // open: dp
  Pull_Resistor #(.pull(0)) pull_resistor_1 (.node(IRA));
  Pull_Resistor #(.pull(0)) pull_resistor_2 (.node(IRB));
  Pull_Resistor #(.pull(0)) pull_resistor_3 (.node(IRC));
  Adder #(.width(32)) adder_1 (.a(bit_extender_1_out), .b(PC), .out(adder_1_out));  // open: cin, cout
  assign and_1_out = {Result, Index} & 32'hfffffffe;  // AND_Gate and_1, 32 bits wide
  assign bit_extender_2_out = {{20{imm12_B[11]}}, imm12_B};  // Bit_Extender bit_extender_2
  Hex_Digit_Display hex_digit_display_6 (.value(LedData[11:8]));  // open: dp
  Hex_Digit_Display hex_digit_display_7 (.value(LedData[7:4]));  // open: dp
  // Probe on \总周期数 
  not not_1 (not_1_out, EQ);
  Comparator #(.width(32), .mode("twosComplement")) comparator_5 (
    .a(R1), .b(32'h22), .eq(comparator_5_eq));  // open: gt, lt
  Multiplexer #(.select(1), .width(32), .disabled("Z"), .enable("false")) multiplexer_1 (
    .in0(PC_4), .in1(adder_1_out), .out(multiplexer_1_out), .sel(jal));
  Multiplexer #(.select(1), .width(32), .disabled("Z"), .enable("false")) multiplexer_2 (
    .in0(multiplexer_1_out), .in1(and_1_out), .out(multiplexer_2_out), .sel(jalr));
  Adder #(.width(32)) adder_2 (.a(bit_extender_2_out), .b(PC), .out(adder_2_out));  // open: cin, cout
  Hex_Digit_Display hex_digit_display_8 (.value(LedData[3:0]));  // open: dp
  and and_2 (and_2_out, beq, EQ);
  or or_2 (Branch, and_2_out, and_3_out, and_4_out);
  and and_3 (and_3_out, not_1_out, bne);
  and and_4 (and_4_out, LT, bltu);
  and and_5 (and_5_out, ecall, comparator_5_eq);
  Multiplexer #(.select(1), .width(32), .disabled("Z"), .enable("false")) multiplexer_3 (
    .in0(multiplexer_2_out), .in1(adder_2_out), .out(nextPC), .sel(Branch));
  D_Flip_Flop #(.trigger("rising"), .Pre_Clr_Positions("LEGACY"), .NegatePresetClear("false"), .enable("true"), .NewFFLayout("false")) d_ff_1 (
    .clk(IR1_t), .D(1'b1), .Q(d_ff_1_q), .reset(Inter1));  // open: Qn, preset, en
  or or_3 (W1, Inter1, d_ff_1_q);
  Counter #(.width(16), .max('hffff), .ongoal("wrap"), .trigger("rising"), .behavior("new")) counter_1 (
    .count(Branch), .Q(\分支成功数 ), .clk(CLK), .clr(RST));  // open: load, D, carry, preset, down
  Register #(.width(32), .trigger("rising"), .Select("low")) register_1 (
    .D(MDin), .en(and_5_out), .Q(LedData), .clk(CLK), .clr(RST));
  and and_6 (halt, ~comparator_5_eq, ecall, ~Go);  // AND_Gate
  Multiplexer #(.select(1), .width(32), .disabled("Z"), .enable("false")) multiplexer_4 (
    .in0(nextPC), .in1(InterAddr), .out(multiplexer_4_out), .sel(Interrupt));
  or or_4 (IR1_t, IR1, IRA);
  Register #(.width(32), .trigger("rising"), .Select("low")) u_PC (
    .D(multiplexer_5_out), .en(not_2_out), .Q(PC), .clk(CLK), .clr(RST));
  Multiplexer #(.select(1), .width(32), .disabled("Z"), .enable("false")) multiplexer_5 (
    .in0(multiplexer_4_out), .in1(EPC), .out(multiplexer_5_out), .sel(uret));
  not not_2 (not_2_out, halt);
  or or_5 (IR2_t, IR2, IRB);
  or or_6 (or_6_out, d_ff_1_q, Inter1);
  and and_7 (and_7_out, or_6_out, ~Ret1);  // AND_Gate
  not not_3 (not_3_out, halt);
  D_Flip_Flop #(.trigger("rising"), .Pre_Clr_Positions("LEGACY"), .NegatePresetClear("false"), .enable("true"), .NewFFLayout("false")) u_IR1 (
    .clk(CLK), .D(and_7_out), .Q(Inter1));  // open: Qn, preset, en, reset
  Counter #(.width(16), .max('hffff), .ongoal("wrap"), .trigger("rising"), .behavior("new")) counter_2 (
    .count(not_3_out), .Q(\总周期数 ), .clk(CLK), .clr(RST));  // open: load, D, carry, preset, down
  Adder #(.width(32)) adder_3 (.a({IR[31:12], {12{1'b0}}}), .b(PC), .out(adder_3_out));  // open: cin, cout
  // RiscV_Probe riscv_probe_1: pin names not known; wires that end beside it: IR
  or or_7 (IR3_t, IR3, IRC);
  or or_8 (PCToReg, jal, jalr, U_type);
  Multiplexer #(.select(1), .width(32), .disabled("Z"), .enable("false")) multiplexer_6 (
    .in0(PC_4), .in1(adder_3_out), .out(RPCin), .sel(U_type));
  ROM #(.addrWidth(10), .dataWidth(32), .Select("high")) rom_1 (.addr(PC[11:2]), .data(IR));
  Adder #(.width(32)) adder_4 (.a(PC), .b(32'h4), .out(PC_4));  // open: cin, cout
  or or_9 (W2, Inter2, d_ff_2_q);
  \单周期硬布线控制器  \u_单周期硬布线控制器_1  (
    .Funct({IR[30], IR[25], IR[14:12]}), .OP(IR[6:2]), .ALU_OP(AluOP), .MemToReg(MemToReg),
    .MemWrite(MemWrite), .ALU_SRC(AluSrcB), .RegWrite(RegWrite), .ecall(ecall), .S_type(S_type), .Jalr(jalr),
    .Beq(beq), .JAL(jal), .Bne(bne), .in_3(IR[21]), .uret(uret), .BLTU(bltu), .U_Type(U_type), .LBU(lbu));  // open: R1, R2, CSRRSI, CSRRCI
  Multiplexer #(.select(1), .width(5), .disabled("Z"), .enable("false")) multiplexer_7 (
    .in0(IR[19:15]), .in1(5'b10001), .out(multiplexer_7_out), .sel(ecall));
  Multiplexer #(.select(1), .width(5), .disabled("Z"), .enable("false")) multiplexer_8 (
    .in0(IR[24:20]), .in1(5'b01010), .out(multiplexer_8_out), .sel(ecall));
  Multiplexer #(.select(1), .width(32), .disabled("Z"), .enable("false")) multiplexer_9 (
    .in0({Result, Index}), .in1(MDout), .out(multiplexer_9_out), .sel(MemToReg));
  Shifter #(.width(20), .shift("ll")) shifter_1 (
    .in({IR[31], IR[19:12], IR[20], IR[30:21]}), .\dist (5'b00001), .out(imm20_J));
  D_Flip_Flop #(.trigger("rising"), .Pre_Clr_Positions("LEGACY"), .NegatePresetClear("false"), .enable("true"), .NewFFLayout("false")) d_ff_2 (
    .clk(IR2_t), .D(1'b1), .Q(d_ff_2_q), .reset(Inter2));  // open: Qn, preset, en
  Multiplexer #(.select(1), .width(32), .disabled("Z"), .enable("false")) multiplexer_10 (
    .in0(multiplexer_9_out), .in1(RPCin), .out(RDin), .sel(PCToReg));
  Shifter #(.width(12), .shift("ll")) shifter_2 (
    .in({IR[31], IR[7], IR[30:25], IR[11:8]}), .\dist (4'b0001), .out(imm12_B));
  or or_10 (or_10_out, d_ff_2_q, Inter2);
  and and_8 (and_8_out, or_10_out, ~Ret2);  // AND_Gate
  Regifile regifile_1 (
    .Din(RDin), .Clk(CLK), .R1(R1), .R2(MDin), .WE(RegWrite), .W_num(IR[11:7]), .R1_num(multiplexer_7_out),
    .R2_num(multiplexer_8_out));
  assign bit_extender_3_out = {{20{IR[31]}}, IR[31:20]};  // Bit_Extender bit_extender_3
  assign bit_extender_4_out = {{20{IR[31]}}, {IR[31:25], IR[11:7]}};  // Bit_Extender bit_extender_4
  D_Flip_Flop #(.trigger("rising"), .Pre_Clr_Positions("LEGACY"), .NegatePresetClear("false"), .enable("true"), .NewFFLayout("false")) u_IR2 (
    .clk(CLK), .D(and_8_out), .Q(Inter2));  // open: Qn, preset, en, reset
  Multiplexer #(.select(1), .width(32), .disabled("Z"), .enable("false")) multiplexer_11 (
    .in0(bit_extender_3_out), .in1(bit_extender_4_out), .out(multiplexer_11_out), .sel(S_type));
  D_Flip_Flop #(.trigger("high"), .Pre_Clr_Positions("LEGACY"), .NegatePresetClear("false"), .enable("true"), .NewFFLayout("false")) d_ff_3 (.Q(d_ff_3_q));  // open: clk, D, Qn, preset, en, reset
  // Probe on 13'hc
  Multiplexer #(.select(1), .width(32), .disabled("Z"), .enable("false")) multiplexer_12 (
    .in0(MDin), .in1(multiplexer_11_out), .out(multiplexer_12_out), .sel(AluSrcB));
  Comparator #(.width(13), .mode("twosComplement")) comparator_6 (
    .a(CNT_num), .b(13'hc), .eq(comparator_6_eq), .lt(comparator_6_lt));  // open: gt
  Clock #(.highDuration(1), .lowDuration(1)) clock_1 (.out(clock_1_out));
  Priority_Encoder #(.select(2), .disabled("Z")) priority_encoder_1 (
    .in0(1'b0), .in1(Inter1), .in2(Inter2), .in3(Inter3), .out(priority_encoder_1_out), .gs(Interr));  // open: en_out, en_in
  Register #(.width(32), .trigger("rising"), .Select("low")) u_EPC (
    .D(nextPC), .en(Interrupt), .Q(EPC), .clk(CLK));  // open: clr
  ALU alu_1 (
    .X(R1), .Y(multiplexer_12_out), .AluOP(AluOP), .Equal(EQ), .Result({Result, Index}), .out_6(LT));  // open: Result_2, out_4
  Counter #(.width(13), .max('h1fff), .ongoal("stay"), .trigger("rising"), .behavior("old")) counter_3 (
    .count(comparator_6_lt), .Q(CNT_num), .clk(clock_1_out));  // open: load, D, carry, clr, preset
  D_Flip_Flop #(.trigger("rising"), .Pre_Clr_Positions("LEGACY"), .NegatePresetClear("false"), .enable("true"), .NewFFLayout("false")) d_ff_4 (
    .clk(IR3_t), .D(1'b1), .Q(d_ff_4_q), .reset(Inter3));  // open: Qn, preset, en
  or or_11 (W3, Inter3, d_ff_4_q);
  nand nand_1 (nand_1_out, d_ff_3_q, comparator_6_eq);
  Multiplexer #(.select(2), .width(32), .disabled("Z"), .enable("false")) multiplexer_13 (
    .in1(32'h30ac), .in2(32'h3150), .in3(32'h31f4), .out(InterAddr), .sel(priority_encoder_1_out));  // open: in0
  assign CLK = nand_1_out ? clock_1_out : 1'bz;  // Controlled_Buffer controlled_buffer_1
  Pull_Resistor #(.pull(1)) pull_resistor_4 (.node(CLK));
  or or_12 (or_12_out, d_ff_4_q, Inter3);
  and and_9 (and_9_out, or_12_out, ~Ret3);  // AND_Gate
  Register #(.width(1), .trigger("rising"), .Select("low")) IE (
    .D(Interrupt), .en(or_13_out), .Q(IE_q), .clk(CLK));  // open: clr
  or or_13 (or_13_out, Interrupt, uret);
  D_Flip_Flop #(.trigger("rising"), .Pre_Clr_Positions("LEGACY"), .NegatePresetClear("false"), .enable("true"), .NewFFLayout("false")) u_IR3 (
    .clk(CLK), .D(and_9_out), .Q(Inter3));  // open: Qn, preset, en, reset
  Register #(.width(2), .trigger("rising"), .Select("low")) \u_中断号  (
    .D(priority_encoder_1_out), .en(Interrupt), .Q(\中断号_q ), .clk(CLK));  // open: clr
  Decoder #(.select(2), .tristate("false"), .disabled("Z"), .enable("false")) decoder_1 (
    .out1(decoder_1_out1), .out2(decoder_1_out2), .out3(decoder_1_out3), .sel(\中断号_q ));  // open: out0
  not not_4 (not_4_out, IE_q);
  and and_10 (Interrupt, not_4_out, Interr);
  RAM #(.addrWidth(10), .dataWidth(32), .bus("separate"), .Select("high")) ram_1 (
    .addr(Result[11:2]), .din(MDin), .data(ram_1_data), .str(MemWrite), .clk(CLK), .ld(MemToReg), .clr(RST));  // open: sel
  and and_11 (Ret1, uret, decoder_1_out1);
  and and_12 (Ret2, decoder_1_out2, uret);
  and and_13 (Ret3, decoder_1_out3, uret);
  Multiplexer #(.select(2), .width(8), .disabled("Z"), .enable("false")) multiplexer_14 (
    .in0(ram_1_data[7:0]), .in1(ram_1_data[15:8]), .in2(ram_1_data[23:16]), .in3(ram_1_data[31:24]),
    .out(multiplexer_14_out), .sel(Index));
  assign bit_extender_5_out = {{24{1'b0}}, multiplexer_14_out};  // Bit_Extender bit_extender_5
  Multiplexer #(.select(1), .width(32), .disabled("Z"), .enable("false")) multiplexer_15 (
    .in0(ram_1_data), .in1(bit_extender_5_out), .out(MDout), .sel(lbu));

  // Other names for the same wires on the sheet: imm12_S[11:0] = {IR[31:25], IR[11:7]}; imm32_U[31:12] = IR[31:12];
  //   imm12_I[11:0] = IR[31:20]; R2_num[4:0] = IR[24:20]; R2[31:0] = MDin; Result[1:0] = Index

  // Notes on the sheet:
  //   中断源
  //   中断等待指示
  //   总复位信号应将除ROM以外所有存储组件全部清零
  //   单级中断测试信号模拟器
  //   数码管输出
  //   数码管输出应该用寄存器锁存，否则显示数据只能一闪而过
  //   指令存储器
  //   指令字
  //   contents of rom_1 (hex, n*v repeats v):
  //   7d000113 100413 1f41993 41f9d993 433 c00913 800b13 140413 f47413 800293 100313 499993 89e9b3 1300533
  //   2200893 73 406282b3 fe0294e3 140413 f00f93 1f47433 1c41413 800293 100313 49d993 89e9b3 1300533
  //   2200893 73 406282b3 fe0294e3 1c45413 406b0b33 b0463 f95ff06f 2b3 fff2c293 1029293 fff2e293 500533
  //   2200893 73 f5dff06f 1112023 410113 a12023 410113 812023 410113 1312023 410113 1412023 410113 1512023
  //   410113 1612023 410113 100b13 300a13 100a93 1600433 441413 14469b3 1300533 2200893 73 fe0416e3
  //   415a0a33 fe0a10e3 ffc10113 12b03 ffc10113 12a83 ffc10113 12a03 ffc10113 12983 ffc10113 12403
  //   ffc10113 12503 ffc10113 12883 200073 1112023 410113 a12023 410113 812023 410113 1312023 410113
  //   1412023 410113 1512023 410113 1612023 410113 200b13 300a13 100a93 1600433 441413 14469b3 1300533
  //   2200893 73 fe0416e3 415a0a33 fe0a10e3 ffc10113 12b03 ffc10113 12a83 ffc10113 12a03 ffc10113 12983
  //   ffc10113 12403 ffc10113 12503 ffc10113 12883 200073 1112023 410113 a12023 410113 812023 410113
  //   1312023 410113 1412023 410113 1512023 410113 1612023 410113 300b13 300a13 100a93 1600433 441413
  //   14469b3 1300533 2200893 73 fe0416e3 415a0a33 fe0a10e3 ffc10113 12b03 ffc10113 12a83 ffc10113 12a03
  //   ffc10113 12983 ffc10113 12403 ffc10113 12503 ffc10113 12883 200073
  //   rs1
  //   rs2
  //   rd
  //   为方便自动评测，需要输出PC，IR，寄存器堆写如数据RDin
  //   RAM写使能MemWrite、RAM写入数据MDin等信号
  //   Reset 
  //   控制位
  //   暂停节拍，不能为0
  //   戳工具置1进入计数暂停模式，ctrl+k时钟自动运行到对应节拍暂停
  //   ctrl+k关闭时钟连续运行，将控制位置零，进入单步调试模式调试
  //   可计数暂停的时钟源
  //   Reset 
  //   数据存储器
endmodule

module \单周期_多级中断  (
  input  IR1,
  input  IR2,
  input  IR3,
  output RegWrite,
  output MemWrite,
  output [31:0] PC,
  output [31:0] IR,
  output [31:0] RDin,
  output [31:0] MDin,
  output [31:0] LedData
);

  wire AluSrcB, and_2_out, and_3_out, and_4_out, and_5_out, and_7_out, and_8_out, and_10_out, and_11_out,
       beq, bltu, bne, Branch, CLK, clock_1_out, comparator_2_eq, comparator_3_eq, comparator_4_eq,
       comparator_5_eq, comparator_6_eq, comparator_7_eq, comparator_7_lt, csrrci, csrrsi, d_ff_1_q,
       d_ff_2_q, d_ff_3_q, d_ff_4_q, decoder_1_out1, decoder_1_out2, decoder_1_out3, demultiplexer_1_out1,
       demultiplexer_1_out2, demultiplexer_1_out3, demultiplexer_2_out0, demultiplexer_2_out1,
       demultiplexer_2_out2, ecall, EQ, Go, halt, IE, init, Inter1, Inter2, Inter3, Interrupt, IR1_t, IR2_t,
       IR3_t, IRA, IRB, IRC, jal, jalr, lbu, LT, MemToReg, nand_1_out, not_1_out, not_2_out, not_3_out,
       or_1_out, or_6_out, or_7_out, or_11_out, or_13_out, or_14_out, or_15_out, PCToReg,
       priority_encoder_1_gs, pull_resistor_1_node, pull_resistor_2_node, pull_resistor_3_node, Ret1, Ret2,
       Ret3, RST, S_type, shield, U_type, uret, W1, W2, W3;
  wire [1:0] counter_4_q, Index, Inter_Num, Inter_Num_Pri, IR1_2_q, IR2_2_q, IR3_2_q;
  wire [3:0] AluOP;
  wire [4:0] multiplexer_7_out, multiplexer_9_out;
  wire [7:0] multiplexer_15_out;
  wire [11:0] imm12_B;
  wire [12:0] CNT_num;
  wire [15:0] \分支成功数 , \总周期数 ;
  wire [19:0] imm20_J;
  wire [31:0] adder_1_out, adder_2_out, adder_3_out, and_1_out, bit_extender_1_out, bit_extender_2_out,
       bit_extender_3_out, bit_extender_4_out, bit_extender_5_out, EPC, EPC1_q, EPC2_q, EPC3_q, InterAddr,
       MDout, multiplexer_1_out, multiplexer_2_out, multiplexer_4_out, multiplexer_5_out, multiplexer_8_out,
       multiplexer_11_out, multiplexer_12_out, nextPC, PC_4, R1, ram_1_data, RPCin;
  wire [31:2] Result;

  Button \u_继续运行  (.out(Go));
  Button _1 (.out(IRA));
  Button _2 (.out(IRB));
  Button _3 (.out(IRC));
  LED #(.active("true")) led_1 (.in(W1));
  LED #(.active("true")) led_2 (.in(W2));
  LED #(.active("true")) led_3 (.in(W3));
  Hex_Digit_Display hex_digit_display_1 (.value(LedData[31:28]));  // open: dp
  Hex_Digit_Display hex_digit_display_2 (.value(LedData[23:20]));  // open: dp
  Hex_Digit_Display hex_digit_display_3 (.value(LedData[27:24]));  // open: dp
  Comparator #(.width(16), .mode("twosComplement")) comparator_1 (
    .a({16{1'b0}}), .b(\总周期数 ), .eq(init));  // open: gt, lt
  Comparator #(.width(16), .mode("twosComplement")) comparator_2 (
    .a(16'h23b), .b(\总周期数 ), .eq(comparator_2_eq));  // open: gt, lt
  Comparator #(.width(16), .mode("twosComplement")) comparator_3 (
    .a(\总周期数 ), .b(16'h1), .eq(comparator_3_eq));  // open: gt, lt
  Comparator #(.width(16), .mode("twosComplement")) comparator_4 (
    .a(\总周期数 ), .b(16'h4), .eq(comparator_4_eq));  // open: gt, lt
  Comparator #(.width(16), .mode("twosComplement")) comparator_5 (
    .a(\总周期数 ), .b(16'h7), .eq(comparator_5_eq));  // open: gt, lt
  assign bit_extender_1_out = {{12{imm20_J[19]}}, imm20_J};  // Bit_Extender bit_extender_1
  Hex_Digit_Display hex_digit_display_4 (.value(LedData[19:16]));  // open: dp
  Hex_Digit_Display hex_digit_display_5 (.value(LedData[15:12]));  // open: dp
  or or_1 (or_1_out, comparator_2_eq, comparator_3_eq);
  Pull_Resistor #(.pull(0)) pull_resistor_1 (.node(pull_resistor_1_node));
  assign pull_resistor_1_node = or_1_out ? ~CLK : 1'bz;  // Controlled_Inverter controlled_inverter_1
  Pull_Resistor #(.pull(0)) pull_resistor_2 (.node(pull_resistor_2_node));
  assign pull_resistor_2_node = comparator_4_eq ? ~CLK : 1'bz;  // Controlled_Inverter controlled_inverter_2
  Pull_Resistor #(.pull(0)) pull_resistor_3 (.node(pull_resistor_3_node));
  assign pull_resistor_3_node = comparator_5_eq ? ~CLK : 1'bz;  // Controlled_Inverter controlled_inverter_3
  Adder #(.width(32)) adder_1 (.a(bit_extender_1_out), .b(PC), .out(adder_1_out));  // open: cin, cout
  assign bit_extender_2_out = {{20{imm12_B[11]}}, imm12_B};  // Bit_Extender bit_extender_2
  Hex_Digit_Display hex_digit_display_6 (.value(LedData[11:8]));  // open: dp
  Hex_Digit_Display hex_digit_display_7 (.value(LedData[7:4]));  // open: dp
  // Probe on \总周期数 
  not not_1 (not_1_out, EQ);
  Multiplexer #(.select(1), .width(32), .disabled("Z"), .enable("false")) multiplexer_1 (
    .in0(PC_4), .in1(adder_1_out), .out(multiplexer_1_out), .sel(jal));
  assign and_1_out = {Result, Index} & 32'hfffffffe;  // AND_Gate and_1, 32 bits wide
  Adder #(.width(32)) adder_2 (.a(bit_extender_2_out), .b(PC), .out(adder_2_out));  // open: cin, cout
  Hex_Digit_Display hex_digit_display_8 (.value(LedData[3:0]));  // open: dp
  Button button_1 (.out(RST));
  and and_2 (and_2_out, beq, EQ);
  and and_3 (and_3_out, not_1_out, bne);
  and and_4 (and_4_out, LT, bltu);
  Comparator #(.width(32), .mode("twosComplement")) comparator_6 (
    .a(R1), .b(32'h22), .eq(comparator_6_eq));  // open: gt, lt
  Multiplexer #(.select(1), .width(32), .disabled("Z"), .enable("false")) multiplexer_2 (
    .in0(multiplexer_1_out), .in1(and_1_out), .out(multiplexer_2_out), .sel(jalr));
  Multiplexer #(.select(1), .width(32), .disabled("Z"), .enable("false")) multiplexer_3 (
    .in0(multiplexer_2_out), .in1(adder_2_out), .out(nextPC), .sel(Branch));
  or or_2 (W1, Inter1, d_ff_1_q);
  or or_3 (Branch, and_2_out, and_3_out, and_4_out);
  Counter #(.width(16), .max('hffff), .ongoal("wrap"), .trigger("rising"), .behavior("new")) counter_1 (
    .count(Branch), .Q(\分支成功数 ), .clk(CLK), .clr(RST));  // open: load, D, carry, preset, down
  Register #(.width(32), .trigger("rising"), .Select("low")) register_1 (
    .D(MDin), .en(and_5_out), .Q(LedData), .clk(CLK), .clr(RST));
  and and_5 (and_5_out, ecall, comparator_6_eq);
  and and_6 (halt, ~comparator_6_eq, ecall, ~Go);  // AND_Gate
  Multiplexer #(.select(1), .width(32), .disabled("Z"), .enable("false")) multiplexer_4 (
    .in0(nextPC), .in1(InterAddr), .out(multiplexer_4_out), .sel(Interrupt));
  or or_4 (IR1_t, IR1, IRA);
  D_Flip_Flop #(.trigger("rising"), .Pre_Clr_Positions("LEGACY"), .NegatePresetClear("false"), .enable("true"), .NewFFLayout("false")) d_ff_1 (
    .clk(IR1_t), .D(1'b1), .Q(d_ff_1_q), .reset(Inter1));  // open: Qn, preset, en
  Multiplexer #(.select(1), .width(32), .disabled("Z"), .enable("false")) multiplexer_5 (
    .in0(multiplexer_4_out), .in1(EPC), .out(multiplexer_5_out), .sel(uret));
  not not_2 (not_2_out, halt);
  or or_5 (IR2_t, IR2, IRB);
  or or_6 (or_6_out, d_ff_1_q, Inter1);
  Register #(.width(32), .trigger("rising"), .Select("low")) u_PC (
    .D(multiplexer_5_out), .en(not_2_out), .Q(PC), .clk(CLK), .clr(RST));
  and and_7 (and_7_out, or_6_out, ~Ret1);  // AND_Gate
  not not_3 (not_3_out, halt);
  Counter #(.width(16), .max('hffff), .ongoal("wrap"), .trigger("rising"), .behavior("new")) counter_2 (
    .count(not_3_out), .Q(\总周期数 ), .clk(CLK), .clr(RST));  // open: load, D, carry, preset, down
  or or_7 (or_7_out, jal, jalr);
  Adder #(.width(32)) adder_3 (.a({IR[31:12], {12{1'b0}}}), .b(PC), .out(adder_3_out));  // open: cin, cout
  or or_8 (IR3_t, IR3, IRC);
  D_Flip_Flop #(.trigger("rising"), .Pre_Clr_Positions("LEGACY"), .NegatePresetClear("false"), .enable("true"), .NewFFLayout("false")) u_IR1 (
    .clk(CLK), .D(and_7_out), .Q(Inter1));  // open: Qn, preset, en, reset
  or or_9 (PCToReg, or_7_out, U_type);
  Multiplexer #(.select(1), .width(32), .disabled("Z"), .enable("false")) multiplexer_6 (
    .in0(PC_4), .in1(adder_3_out), .out(RPCin), .sel(U_type));
  // RiscV_Probe riscv_probe_1: pin names not known; wires that end beside it: IR
  ROM #(.addrWidth(10), .dataWidth(32), .Select("high")) rom_1 (.addr(PC[11:2]), .data(IR));
  Adder #(.width(32)) adder_4 (.a(PC), .b(32'h4), .out(PC_4));  // open: cin, cout
  or or_10 (W2, Inter2, d_ff_2_q);
  \单周期硬布线控制器  \u_单周期硬布线控制器_1  (
    .Funct({IR[30], IR[25], IR[14:12]}), .OP(IR[6:2]), .ALU_OP(AluOP), .MemToReg(MemToReg),
    .MemWrite(MemWrite), .ALU_SRC(AluSrcB), .RegWrite(RegWrite), .ecall(ecall), .S_type(S_type), .Jalr(jalr),
    .Beq(beq), .JAL(jal), .Bne(bne), .in_3(IR[21]), .uret(uret), .BLTU(bltu), .U_Type(U_type), .LBU(lbu),
    .CSRRSI(csrrsi), .CSRRCI(csrrci));  // open: R1, R2
  Multiplexer #(.select(1), .width(5), .disabled("Z"), .enable("false")) multiplexer_7 (
    .in0(IR[24:20]), .in1(5'b01010), .out(multiplexer_7_out), .sel(ecall));
  Multiplexer #(.select(1), .width(32), .disabled("Z"), .enable("false")) multiplexer_8 (
    .in0({Result, Index}), .in1(MDout), .out(multiplexer_8_out), .sel(MemToReg));
  D_Flip_Flop #(.trigger("rising"), .Pre_Clr_Positions("LEGACY"), .NegatePresetClear("false"), .enable("true"), .NewFFLayout("false")) d_ff_2 (
    .clk(IR2_t), .D(1'b1), .Q(d_ff_2_q), .reset(Inter2));  // open: Qn, preset, en
  Multiplexer #(.select(1), .width(5), .disabled("Z"), .enable("false")) multiplexer_9 (
    .in0(IR[19:15]), .in1(5'b10001), .out(multiplexer_9_out), .sel(ecall));
  Shifter #(.width(12), .shift("ll")) shifter_1 (
    .in({IR[31], IR[7], IR[30:25], IR[11:8]}), .\dist (4'b0001), .out(imm12_B));
  Shifter #(.width(20), .shift("ll")) shifter_2 (
    .in({IR[31], IR[19:12], IR[20], IR[30:21]}), .\dist (5'b00001), .out(imm20_J));
  or or_11 (or_11_out, d_ff_2_q, Inter2);
  Multiplexer #(.select(1), .width(32), .disabled("Z"), .enable("false")) multiplexer_10 (
    .in0(multiplexer_8_out), .in1(RPCin), .out(RDin), .sel(PCToReg));
  and and_8 (and_8_out, or_11_out, ~Ret2);  // AND_Gate
  Regifile regifile_1 (
    .Din(RDin), .Clk(CLK), .R1(R1), .R2(MDin), .WE(RegWrite), .W_num(IR[11:7]), .R1_num(multiplexer_9_out),
    .R2_num(multiplexer_7_out));
  D_Flip_Flop #(.trigger("rising"), .Pre_Clr_Positions("LEGACY"), .NegatePresetClear("false"), .enable("true"), .NewFFLayout("false")) u_IR2 (
    .clk(CLK), .D(and_8_out), .Q(Inter2));  // open: Qn, preset, en, reset
  assign bit_extender_3_out = {{20{IR[31]}}, IR[31:20]};  // Bit_Extender bit_extender_3
  Multiplexer #(.select(1), .width(32), .disabled("Z"), .enable("false")) multiplexer_11 (
    .in0(bit_extender_3_out), .in1(bit_extender_4_out), .out(multiplexer_11_out), .sel(S_type));
  assign bit_extender_4_out = {{20{IR[31]}}, {IR[31:25], IR[11:7]}};  // Bit_Extender bit_extender_4
  D_Flip_Flop #(.trigger("high"), .Pre_Clr_Positions("LEGACY"), .NegatePresetClear("false"), .enable("true"), .NewFFLayout("false")) d_ff_3 (.Q(d_ff_3_q));  // open: clk, D, Qn, preset, en, reset
  // Probe on 13'hc
  Multiplexer #(.select(1), .width(32), .disabled("Z"), .enable("false")) multiplexer_12 (
    .in0(MDin), .in1(multiplexer_11_out), .out(multiplexer_12_out), .sel(AluSrcB));
  Comparator #(.width(13), .mode("twosComplement")) comparator_7 (
    .a(CNT_num), .b(13'hc), .eq(comparator_7_eq), .lt(comparator_7_lt));  // open: gt
  Clock #(.highDuration(1), .lowDuration(1)) clock_1 (.out(clock_1_out));
  Priority_Encoder #(.select(2), .disabled("Z")) priority_encoder_1 (
    .in0(1'b0), .in1(Inter1), .in2(Inter2), .in3(Inter3), .out(Inter_Num), .gs(priority_encoder_1_gs));  // open: en_out, en_in
  Counter #(.width(13), .max('h1fff), .ongoal("stay"), .trigger("rising"), .behavior("old")) counter_3 (
    .count(comparator_7_lt), .Q(CNT_num), .clk(clock_1_out));  // open: load, D, carry, clr, preset
  or or_12 (W3, Inter3, d_ff_4_q);
  and and_9 (Interrupt, priority_encoder_1_gs, shield, IE);
  and and_10 (and_10_out, ~Interrupt, ~csrrci);  // AND_Gate
  Register #(.width(1), .trigger("rising"), .Select("low")) u_IE (
    .D(and_10_out), .en(or_13_out), .Q(IE), .clk(CLK));  // open: clr
  or or_13 (or_13_out, Interrupt, csrrci, csrrsi, uret, init);
  ALU alu_1 (
    .X(R1), .Y(multiplexer_12_out), .AluOP(AluOP), .Equal(EQ), .Result({Result, Index}), .out_6(LT));  // open: Result_2, out_4
  nand nand_1 (nand_1_out, d_ff_3_q, comparator_7_eq);
  D_Flip_Flop #(.trigger("rising"), .Pre_Clr_Positions("LEGACY"), .NegatePresetClear("false"), .enable("true"), .NewFFLayout("false")) d_ff_4 (
    .clk(IR3_t), .D(1'b1), .Q(d_ff_4_q), .reset(Inter3));  // open: Qn, preset, en
  Decoder #(.select(2), .tristate("false"), .disabled("Z"), .enable("false")) decoder_1 (
    .out1(decoder_1_out1), .out2(decoder_1_out2), .out3(decoder_1_out3), .sel(Inter_Num));  // open: out0
  Pull_Resistor #(.pull(0)) pull_resistor_4 (.node(decoder_1_out1));
  Pull_Resistor #(.pull(0)) pull_resistor_5 (.node(decoder_1_out2));
  Pull_Resistor #(.pull(0)) pull_resistor_6 (.node(decoder_1_out3));
  assign CLK = nand_1_out ? clock_1_out : 1'bz;  // Controlled_Buffer controlled_buffer_1
  Pull_Resistor #(.pull(1)) pull_resistor_7 (.node(CLK));
  or or_14 (or_14_out, d_ff_4_q, Inter3);
  and and_11 (and_11_out, or_14_out, ~Ret3);  // AND_Gate
  and and_12 (Ret1, uret, decoder_1_out1);
  and and_13 (Ret2, decoder_1_out2, uret);
  and and_14 (Ret3, decoder_1_out3, uret);
  Demultiplexer #(.select(2), .width(1), .tristate("false"), .disabled("Z"), .enable("false")) demultiplexer_1 (
    .out1(demultiplexer_1_out1), .out2(demultiplexer_1_out2), .out3(demultiplexer_1_out3), .in(Interrupt),
    .sel(Inter_Num));  // open: out0
  Pull_Resistor #(.pull(0)) pull_resistor_8 (.node(demultiplexer_1_out1));
  Pull_Resistor #(.pull(0)) pull_resistor_9 (.node(demultiplexer_1_out2));
  Pull_Resistor #(.pull(0)) pull_resistor_10 (.node(demultiplexer_1_out3));
  D_Flip_Flop #(.trigger("rising"), .Pre_Clr_Positions("LEGACY"), .NegatePresetClear("false"), .enable("true"), .NewFFLayout("false")) u_IR3 (
    .clk(CLK), .D(and_11_out), .Q(Inter3));  // open: Qn, preset, en, reset
  Register #(.width(32), .trigger("rising"), .Select("low")) EPC1 (
    .D(nextPC), .en(demultiplexer_1_out1), .Q(EPC1_q), .clk(CLK));  // open: clr
  Register #(.width(32), .trigger("rising"), .Select("low")) EPC2 (
    .D(nextPC), .en(demultiplexer_1_out2), .Q(EPC2_q), .clk(CLK));  // open: clr
  Register #(.width(32), .trigger("rising"), .Select("low")) EPC3 (
    .D(nextPC), .en(demultiplexer_1_out3), .Q(EPC3_q), .clk(CLK));  // open: clr
  RAM #(.addrWidth(10), .dataWidth(32), .bus("separate"), .Select("high")) ram_1 (
    .addr(Result[11:2]), .din(MDin), .data(ram_1_data), .str(MemWrite), .clk(CLK), .ld(MemToReg), .clr(RST));  // open: sel
  Multiplexer #(.select(2), .width(32), .disabled("Z"), .enable("false")) multiplexer_13 (
    .in1(32'h30ac), .in2(32'h3158), .in3(32'h3204), .out(InterAddr), .sel(Inter_Num));  // open: in0
  Multiplexer #(.select(2), .width(32), .disabled("Z"), .enable("false")) multiplexer_14 (
    .in1(EPC1_q), .in2(EPC2_q), .in3(EPC3_q), .out(EPC), .sel(Inter_Num_Pri));  // open: in0
  Multiplexer #(.select(2), .width(8), .disabled("Z"), .enable("false")) multiplexer_15 (
    .in0(ram_1_data[7:0]), .in1(ram_1_data[15:8]), .in2(ram_1_data[23:16]), .in3(ram_1_data[31:24]),
    .out(multiplexer_15_out), .sel(Index));
  assign bit_extender_5_out = {{24{1'b0}}, multiplexer_15_out};  // Bit_Extender bit_extender_5
  or or_15 (or_15_out, uret, Interrupt);
  Counter #(.width(2), .max('h3), .ongoal("wrap"), .trigger("rising"), .behavior("new")) counter_4 (
    .count(or_15_out), .Q(counter_4_q), .clk(CLK), .down(uret));  // open: load, D, carry, clr, preset
  Demultiplexer #(.select(2), .width(1), .tristate("false"), .disabled("Z"), .enable("false")) demultiplexer_2 (
    .out0(demultiplexer_2_out0), .out1(demultiplexer_2_out1), .out2(demultiplexer_2_out2), .in(Interrupt),
    .sel(counter_4_q));  // open: out3
  Multiplexer #(.select(1), .width(32), .disabled("Z"), .enable("false")) multiplexer_16 (
    .in0(ram_1_data), .in1(bit_extender_5_out), .out(MDout), .sel(lbu));
  Pull_Resistor #(.pull(0)) pull_resistor_11 (.node(demultiplexer_2_out0));
  Pull_Resistor #(.pull(0)) pull_resistor_12 (.node(demultiplexer_2_out1));
  Pull_Resistor #(.pull(0)) pull_resistor_13 (.node(demultiplexer_2_out2));
  Register #(.width(2), .trigger("rising"), .Select("low")) IR1_2 (
    .D(Inter_Num), .en(demultiplexer_2_out0), .Q(IR1_2_q), .clk(CLK));  // open: clr
  Register #(.width(2), .trigger("rising"), .Select("low")) IR2_2 (
    .D(Inter_Num), .en(demultiplexer_2_out1), .Q(IR2_2_q), .clk(CLK));  // open: clr
  Register #(.width(2), .trigger("rising"), .Select("low")) IR3_2 (
    .D(Inter_Num), .en(demultiplexer_2_out2), .Q(IR3_2_q), .clk(CLK));  // open: clr
  Multiplexer #(.select(2), .width(2), .disabled("Z"), .enable("false")) multiplexer_17 (
    .in1(IR1_2_q), .in2(IR2_2_q), .in3(IR3_2_q), .out(Inter_Num_Pri), .sel(counter_4_q));  // open: in0
  Comparator #(.width(2), .mode("unsigned")) comparator_8 (
    .a(Inter_Num_Pri), .b(Inter_Num), .lt(shield));  // open: gt, eq
  Pull_Resistor #(.pull(1)) pull_resistor_14 (.node(shield));

  // Other names for the same wires on the sheet: imm12_S[11:0] = {IR[31:25], IR[11:7]}; imm32_U[31:12] = IR[31:12];
  //   imm12_I[11:0] = IR[31:20]; R2_num[4:0] = IR[24:20]; R2[31:0] = MDin; Result[1:0] = Index

  // Notes on the sheet:
  //   中断源
  //   中断等待指示
  //   总复位信号应将除ROM以外所有存储组件全部清零
  //   单级中断测试信号模拟器
  //   数码管输出
  //   数码管输出应该用寄存器锁存，否则显示数据只能一闪而过
  //   Reset 
  //   指令存储器
  //   contents of rom_1 (hex, n*v repeats v):
  //   7d000113 100413 1f41993 41f9d993 433 c00913 800b13 140413 f47413 800293 100313 499993 89e9b3 1300533
  //   2200893 73 406282b3 fe0294e3 140413 f00f93 1f47433 1c41413 800293 100313 49d993 89e9b3 1300533
  //   2200893 73 406282b3 fe0294e3 1c45413 406b0b33 b0463 f95ff06f 2b3 fff2c293 1029293 fff2e293 500533
  //   2200893 73 f5dff06f 1112023 410113 a12023 410113 812023 410113 1312023 410113 1412023 410113 1512023
  //   410113 1612023 410113 40e073 100b13 300a13 100a93 1600433 441413 14469b3 1300533 2200893 73 fe0416e3
  //   415a0a33 fe0a10e3 40f073 ffc10113 12b03 ffc10113 12a83 ffc10113 12a03 ffc10113 12983 ffc10113 12403
  //   ffc10113 12503 ffc10113 12883 200073 1112023 410113 a12023 410113 812023 410113 1312023 410113
  //   1412023 410113 1512023 410113 1612023 410113 40e073 200b13 300a13 100a93 1600433 441413 14469b3
  //   1300533 2200893 73 fe0416e3 415a0a33 fe0a10e3 40f073 ffc10113 12b03 ffc10113 12a83 ffc10113 12a03
  //   ffc10113 12983 ffc10113 12403 ffc10113 12503 ffc10113 12883 200073 1112023 410113 a12023 410113
  //   812023 410113 1312023 410113 1412023 410113 1512023 410113 1612023 410113 40e073 300b13 300a13
  //   100a93 1600433 441413 14469b3 1300533 2200893 73 fe0416e3 415a0a33 fe0a10e3 40f073 ffc10113 12b03
  //   ffc10113 12a83 ffc10113 12a03 ffc10113 12983 ffc10113 12403 ffc10113 12503 ffc10113 12883 200073
  //   rs1
  //   rs2
  //   指令字
  //   rd
  //   为方便自动评测，需要输出PC，IR，寄存器堆写如数据RDin
  //   RAM写使能MemWrite、RAM写入数据MDin等信号
  //   Reset 
  //   控制位
  //   暂停节拍，不能为0
  //   戳工具置1进入计数暂停模式，ctrl+k时钟自动运行到对应节拍暂停
  //   ctrl+k关闭时钟连续运行，将控制位置零，进入单步调试模式调试
  //   可计数暂停的时钟源
  //   Reset 
  //   数据存储器
endmodule

module \封装正确性测试  (
);

  wire IR1, IR2, IR3, MemW, RegW;
  wire [31:0] EX_PC, ID_PC, IF_PC, IR, LED, MDin, MDinr, MEM_PC, PC, RDin, RDinr, WB_PC;

  \单周期RISC_V  \u_单周期risc_v_1  (
    .IR1(IR1), .IR2(IR2), .IR3(IR3), .RegWrite(RegW), .MemWrite(MemW), .PC(PC), .IR(IR), .RDin(RDin),
    .MDin(MDin), .LedData(LED));
  \气泡流水线  \u_气泡流水线_1  (
    .RegWrite(RegW), .MemWrite(MemW), .IF_PC(IF_PC), .ID_PC(ID_PC), .EX_PC(EX_PC), .M_PC(MEM_PC),
    .WB_PC(WB_PC), .RDin(RDinr), .MDin(MDinr), .LedData(LED));
  \单周期_单级中断  \u_单周期_单级中断_1  (
    .IR1(IR1), .IR2(IR2), .IR3(IR3), .RegWrite(RegW), .MemWrite(MemW), .PC(PC), .IR(IR), .RDin(RDin),
    .MDin(MDin), .LedData(LED));
  \理想流水线  \u_理想流水线_1  (
    .RegWrite(RegW), .MemWrite(MemW), .IF_PC(IF_PC), .ID_PC(ID_PC), .EX_PC(EX_PC), .M_PC(MEM_PC),
    .WB_PC(WB_PC), .RDin(RDinr), .MDin(MDinr), .LedData(LED));
  \重定向流水线  \u_重定向流水线_1  (
    .RegWrite(RegW), .MemWrite(MemW), .IF_PC(IF_PC), .ID_PC(ID_PC), .EX_PC(EX_PC), .M_PC(MEM_PC),
    .WB_PC(WB_PC), .RDin(RDinr), .MDin(MDinr), .LedData(LED));
  \单周期_多级中断  \u_单周期_多级中断_1  (
    .IR1(IR1), .IR2(IR2), .IR3(IR3), .RegWrite(RegW), .MemWrite(MemW), .PC(PC), .IR(IR), .RDin(RDin),
    .MDin(MDin), .LedData(LED));

  // Notes on the sheet:
  //   单周期封装测试
  //   气泡流水封装测试
  //   单周期+单级中断封装测试
  //   请检查上面封装有无位宽不匹配，引脚标签是否和连接的标签相对应，否则无法在educoder平台上正确测试
  //   理想流水封装测试
  //   重定向流水封装测试
  //   单周期+多级中断封装测试
endmodule

// IF/ID
module IF_ID (
  input  [31:0] PCin,
  input  [31:0] IRin,
  input  RST,
  input  EN_H,
  input  CLK,
  input  PJin,
  output [31:0] PCout,
  output [31:0] IRout,
  output PJout
);

  wire multiplexer_3_out;
  wire [31:0] multiplexer_1_out, multiplexer_2_out;

  Multiplexer #(.select(1), .width(32), .disabled("Z"), .enable("false")) multiplexer_1 (
    .in0(PCin), .in1({32{1'b0}}), .out(multiplexer_1_out), .sel(RST));
  Multiplexer #(.select(1), .width(32), .disabled("Z"), .enable("false")) multiplexer_2 (
    .in0(IRin), .in1({32{1'b0}}), .out(multiplexer_2_out), .sel(RST));
  Register #(.width(32), .trigger("rising"), .Select("low")) register_1 (
    .D(multiplexer_1_out), .en(EN_H), .Q(PCout), .clk(CLK));  // open: clr
  Register #(.width(32), .trigger("rising"), .Select("low")) register_2 (
    .D(multiplexer_2_out), .en(EN_H), .Q(IRout), .clk(CLK));  // open: clr
  Multiplexer #(.select(1), .width(1), .disabled("Z"), .enable("false")) multiplexer_3 (
    .in0(PJin), .in1(1'b0), .out(multiplexer_3_out), .sel(RST));
  Register #(.width(1), .trigger("rising"), .Select("low")) register_3 (
    .D(multiplexer_3_out), .en(EN_H), .Q(PJout), .clk(CLK));  // open: clr
endmodule

// ID/EX
module ID_EX (
  input  PJin,
  input  [3:0] AluOpin,
  input  [4:0] W_in,
  input  [31:0] PCin,
  input  [31:0] ImmBin,
  input  Beqin,
  input  Bnein,
  input  MemToRegin,
  input  [31:0] ImmUin,
  input  MemWritein,
  input  [1:0] R1Forwardin,
  input  AluSrcBin,
  input  [31:0] IRin,
  input  [31:0] ImmJin,
  input  RegWritein,
  input  S_typein,
  input  [1:0] R2Forwardin,
  input  Jalin,
  input  Jalrin,
  input  Haltin,
  input  [31:0] ImmIin,
  input  [31:0] R1in,
  input  URETin,
  input  LBUin,
  input  BLTUin,
  input  U_Typein,
  input  CLK,
  input  Ecallin,
  input  [31:0] ImmSin,
  input  [31:0] R2in,
  input  RST,
  input  EN_H,
  output PJout,
  output [31:0] PCout,
  output [31:0] Imm_B_out,
  output [3:0] AluOpout,
  output [4:0] W_out,
  output Beqout,
  output Bneout,
  output MemToRegout,
  output [31:0] IRout,
  output [31:0] Imm_J_out,
  output [1:0] R1Forwardout,
  output MemWriteout,
  output AluSrcBout,
  output RegWriteout,
  output [1:0] R2Forwardout,
  output S_Typeout,
  output Jalout,
  output [31:0] Imm_I_out,
  output [31:0] R1out,
  output Jalrout,
  output Haltout,
  output [31:0] ImmUout,
  output URETout,
  output LBUout,
  output BLTUout,
  output [31:0] Imm_S_out,
  output [31:0] R2out,
  output U_Typeout,
  output Ecallout
);

  wire multiplexer_14_out;
  wire [1:0] multiplexer_12_out, multiplexer_13_out;
  wire [4:0] multiplexer_11_out;
  wire [18:0] multiplexer_10_out;
  wire [31:0] multiplexer_1_out, multiplexer_2_out, multiplexer_3_out, multiplexer_4_out, multiplexer_5_out,
       multiplexer_6_out, multiplexer_7_out, multiplexer_8_out, multiplexer_9_out;

  Multiplexer #(.select(1), .width(32), .disabled("Z"), .enable("false")) multiplexer_1 (
    .in0(PCin), .in1({32{1'b0}}), .out(multiplexer_1_out), .sel(RST));
  Multiplexer #(.select(1), .width(32), .disabled("Z"), .enable("false")) multiplexer_2 (
    .in0(IRin), .in1({32{1'b0}}), .out(multiplexer_2_out), .sel(RST));
  Multiplexer #(.select(1), .width(32), .disabled("Z"), .enable("false")) multiplexer_3 (
    .in0(R1in), .in1({32{1'b0}}), .out(multiplexer_3_out), .sel(RST));
  Multiplexer #(.select(1), .width(32), .disabled("Z"), .enable("false")) multiplexer_4 (
    .in0(R2in), .in1({32{1'b0}}), .out(multiplexer_4_out), .sel(RST));
  Register #(.width(32), .trigger("rising"), .Select("low")) register_1 (
    .D(multiplexer_1_out), .en(EN_H), .Q(PCout), .clk(CLK));  // open: clr
  Register #(.width(32), .trigger("rising"), .Select("low")) register_2 (
    .D(multiplexer_2_out), .en(EN_H), .Q(IRout), .clk(CLK));  // open: clr
  Register #(.width(32), .trigger("rising"), .Select("low")) register_3 (
    .D(multiplexer_3_out), .en(EN_H), .Q(R1out), .clk(CLK));  // open: clr
  Register #(.width(32), .trigger("rising"), .Select("low")) register_4 (
    .D(multiplexer_4_out), .en(EN_H), .Q(R2out), .clk(CLK));  // open: clr
  Multiplexer #(.select(1), .width(32), .disabled("Z"), .enable("false")) multiplexer_5 (
    .in0(ImmIin), .in1({32{1'b0}}), .out(multiplexer_5_out), .sel(RST));
  Multiplexer #(.select(1), .width(32), .disabled("Z"), .enable("false")) multiplexer_6 (
    .in0(ImmSin), .in1({32{1'b0}}), .out(multiplexer_6_out), .sel(RST));
  Multiplexer #(.select(1), .width(32), .disabled("Z"), .enable("false")) multiplexer_7 (
    .in0(ImmBin), .in1({32{1'b0}}), .out(multiplexer_7_out), .sel(RST));
  Multiplexer #(.select(1), .width(32), .disabled("Z"), .enable("false")) multiplexer_8 (
    .in0(ImmJin), .in1({32{1'b0}}), .out(multiplexer_8_out), .sel(RST));
  Multiplexer #(.select(1), .width(32), .disabled("Z"), .enable("false")) multiplexer_9 (
    .in0(ImmUin), .in1({32{1'b0}}), .out(multiplexer_9_out), .sel(RST));
  Register #(.width(32), .trigger("rising"), .Select("low")) register_5 (
    .D(multiplexer_5_out), .en(EN_H), .Q(Imm_I_out), .clk(CLK));  // open: clr
  Register #(.width(32), .trigger("rising"), .Select("low")) register_6 (
    .D(multiplexer_6_out), .en(EN_H), .Q(Imm_S_out), .clk(CLK));  // open: clr
  Register #(.width(32), .trigger("rising"), .Select("low")) register_7 (
    .D(multiplexer_7_out), .en(EN_H), .Q(Imm_B_out), .clk(CLK));  // open: clr
  Register #(.width(32), .trigger("rising"), .Select("low")) register_8 (
    .D(multiplexer_8_out), .en(EN_H), .Q(Imm_J_out), .clk(CLK));  // open: clr
  Register #(.width(32), .trigger("rising"), .Select("low")) register_9 (
    .D(multiplexer_9_out), .en(EN_H), .Q(ImmUout), .clk(CLK));  // open: clr
  Multiplexer #(.select(1), .width(19), .disabled("Z"), .enable("false")) multiplexer_10 (
    .in0({Ecallin, U_Typein, BLTUin, LBUin, URETin, Haltin, Jalrin, Jalin, S_typein, RegWritein, AluSrcBin, MemWritein, MemToRegin, Bnein, Beqin, AluOpin}),
    .in1({19{1'b0}}), .out(multiplexer_10_out), .sel(RST));
  Multiplexer #(.select(1), .width(5), .disabled("Z"), .enable("false")) multiplexer_11 (
    .in0(W_in), .in1({5{1'b0}}), .out(multiplexer_11_out), .sel(RST));
  Multiplexer #(.select(1), .width(2), .disabled("Z"), .enable("false")) multiplexer_12 (
    .in0(R1Forwardin), .in1(2'b00), .out(multiplexer_12_out), .sel(RST));
  Multiplexer #(.select(1), .width(2), .disabled("Z"), .enable("false")) multiplexer_13 (
    .in0(R2Forwardin), .in1(2'b00), .out(multiplexer_13_out), .sel(RST));
  Register #(.width(19), .trigger("rising"), .Select("low")) register_10 (
    .D(multiplexer_10_out), .en(EN_H),
    .Q({Ecallout, U_Typeout, BLTUout, LBUout, URETout, Haltout, Jalrout, Jalout, S_Typeout, RegWriteout, AluSrcBout, MemWriteout, MemToRegout, Bneout, Beqout, AluOpout}),
    .clk(CLK));  // open: clr
  Register #(.width(5), .trigger("rising"), .Select("low")) register_11 (
    .D(multiplexer_11_out), .en(EN_H), .Q(W_out), .clk(CLK));  // open: clr
  Register #(.width(2), .trigger("rising"), .Select("low")) register_12 (
    .D(multiplexer_12_out), .en(EN_H), .Q(R1Forwardout), .clk(CLK));  // open: clr
  Register #(.width(2), .trigger("rising"), .Select("low")) register_13 (
    .D(multiplexer_13_out), .en(EN_H), .Q(R2Forwardout), .clk(CLK));  // open: clr
  Multiplexer #(.select(1), .width(1), .disabled("Z"), .enable("false")) multiplexer_14 (
    .in0(PJin), .in1(1'b0), .out(multiplexer_14_out), .sel(RST));
  Register #(.width(1), .trigger("rising"), .Select("low")) register_14 (
    .D(multiplexer_14_out), .en(EN_H), .Q(PJout), .clk(CLK));  // open: clr

  // Other names for the same wires on the sheet: flagsin[18:0] = {Ecallin, U_Typein, BLTUin, LBUin, URETin, Haltin, Jalrin, Jalin, S_typein, RegWritein, AluSrcBin, MemWritein, MemToRegin, Bnein, Beqin, AluOpin};
  //   flagsout[18:0] = {Ecallout, U_Typeout, BLTUout, LBUout, URETout, Haltout, Jalrout, Jalout, S_Typeout, RegWriteout, AluSrcBout, MemWriteout, MemToRegout, Bneout, Beqout, AluOpout};
  //   ImmBout[31:0] = Imm_B_out; ImmIout[31:0] = Imm_I_out; ImmJout[31:0] = Imm_J_out; ImmSout[31:0] = Imm_S_out
endmodule

// EX/MEM
module EX_MEM (
  input  MemToRegin,
  input  [31:0] PCin,
  input  MemWritein,
  input  Jalin,
  input  Jalrin,
  input  [31:0] ImmUin,
  input  RegWritein,
  input  Haltin,
  input  [31:0] IRin,
  input  URETin,
  input  LBUin,
  input  BLTUin,
  input  U_Typein,
  input  [31:0] Resultin,
  input  RST,
  input  [4:0] W_in,
  input  EN_H,
  input  CLK,
  input  [31:0] MDatain,
  output MemToRegout,
  output [31:0] PCout,
  output MemWriteout,
  output Jalout,
  output Jalrout,
  output RegWriteout,
  output Haltout,
  output [31:0] IRout,
  output URETout,
  output LBUout,
  output BLTUout,
  output U_Typeout,
  output [31:0] Resultout,
  output [31:0] ImmUout,
  output [4:0] W_out,
  output [31:0] Mdataout
);

  wire [4:0] multiplexer_7_out;
  wire [9:0] multiplexer_6_out;
  wire [31:0] multiplexer_1_out, multiplexer_2_out, multiplexer_3_out, multiplexer_4_out, multiplexer_5_out;

  Multiplexer #(.select(1), .width(32), .disabled("Z"), .enable("false")) multiplexer_1 (
    .in0(PCin), .in1({32{1'b0}}), .out(multiplexer_1_out), .sel(RST));
  Multiplexer #(.select(1), .width(32), .disabled("Z"), .enable("false")) multiplexer_2 (
    .in0(IRin), .in1({32{1'b0}}), .out(multiplexer_2_out), .sel(RST));
  Register #(.width(32), .trigger("rising"), .Select("low")) register_1 (
    .D(multiplexer_1_out), .en(EN_H), .Q(PCout), .clk(CLK));  // open: clr
  Register #(.width(32), .trigger("rising"), .Select("low")) register_2 (
    .D(multiplexer_2_out), .en(EN_H), .Q(IRout), .clk(CLK));  // open: clr
  Multiplexer #(.select(1), .width(32), .disabled("Z"), .enable("false")) multiplexer_3 (
    .in0(Resultin), .in1({32{1'b0}}), .out(multiplexer_3_out), .sel(RST));
  Multiplexer #(.select(1), .width(32), .disabled("Z"), .enable("false")) multiplexer_4 (
    .in0(MDatain), .in1({32{1'b0}}), .out(multiplexer_4_out), .sel(RST));
  Multiplexer #(.select(1), .width(32), .disabled("Z"), .enable("false")) multiplexer_5 (
    .in0(ImmUin), .in1({32{1'b0}}), .out(multiplexer_5_out), .sel(RST));
  Register #(.width(32), .trigger("rising"), .Select("low")) register_3 (
    .D(multiplexer_3_out), .en(EN_H), .Q(Resultout), .clk(CLK));  // open: clr
  Register #(.width(32), .trigger("rising"), .Select("low")) register_4 (
    .D(multiplexer_4_out), .en(EN_H), .Q(Mdataout), .clk(CLK));  // open: clr
  Register #(.width(32), .trigger("rising"), .Select("low")) register_5 (
    .D(multiplexer_5_out), .en(EN_H), .Q(ImmUout), .clk(CLK));  // open: clr
  Multiplexer #(.select(1), .width(10), .disabled("Z"), .enable("false")) multiplexer_6 (
    .in0({U_Typein, BLTUin, LBUin, URETin, Haltin, RegWritein, Jalrin, Jalin, MemWritein, MemToRegin}),
    .in1({10{1'b0}}), .out(multiplexer_6_out), .sel(RST));
  Multiplexer #(.select(1), .width(5), .disabled("Z"), .enable("false")) multiplexer_7 (
    .in0(W_in), .in1({5{1'b0}}), .out(multiplexer_7_out), .sel(RST));
  Register #(.width(10), .trigger("rising"), .Select("low")) register_6 (
    .D(multiplexer_6_out), .en(EN_H),
    .Q({U_Typeout, BLTUout, LBUout, URETout, Haltout, RegWriteout, Jalrout, Jalout, MemWriteout, MemToRegout}),
    .clk(CLK));  // open: clr
  Register #(.width(5), .trigger("rising"), .Select("low")) register_7 (
    .D(multiplexer_7_out), .en(EN_H), .Q(W_out), .clk(CLK));  // open: clr

  // Other names for the same wires on the sheet: flagsin[9:0] = {U_Typein, BLTUin, LBUin, URETin, Haltin, RegWritein, Jalrin, Jalin, MemWritein, MemToRegin};
  //   flagsout[9:0] = {U_Typeout, BLTUout, LBUout, URETout, Haltout, RegWriteout, Jalrout, Jalout, MemWriteout, MemToRegout}
endmodule

// MEM/WB
module MEM_WB (
  input  MemToRegin,
  input  [31:0] PCin,
  input  Jalin,
  input  Jalrin,
  input  RegWritein,
  input  URETin,
  input  LBUin,
  input  [31:0] IRin,
  input  BLTUin,
  input  U_Typein,
  input  Haltin,
  input  [1:0] Indexin,
  input  [31:0] Resultin,
  input  RST,
  input  [4:0] W_in,
  input  [31:0] RMDatain,
  input  EN_H,
  input  [31:0] ImmUin,
  input  CLK,
  output MemToRegout,
  output [31:0] PCout,
  output Jalout,
  output Jalrout,
  output RegWriteout,
  output URETout,
  output LBUout,
  output [31:0] IRout,
  output BLTUout,
  output U_Typeout,
  output Haltout,
  output [31:0] Resultout,
  output [1:0] Indexout,
  output [31:0] ImmUout,
  output [31:0] RMdataout,
  output [4:0] W_out
);

  wire [4:0] multiplexer_7_out;
  wire [8:0] multiplexer_6_out;
  wire [31:0] multiplexer_1_out, multiplexer_2_out, multiplexer_3_out, multiplexer_4_out, multiplexer_5_out;

  Multiplexer #(.select(1), .width(32), .disabled("Z"), .enable("false")) multiplexer_1 (
    .in0(PCin), .in1({32{1'b0}}), .out(multiplexer_1_out), .sel(RST));
  Multiplexer #(.select(1), .width(32), .disabled("Z"), .enable("false")) multiplexer_2 (
    .in0(IRin), .in1({32{1'b0}}), .out(multiplexer_2_out), .sel(RST));
  Register #(.width(32), .trigger("rising"), .Select("low")) register_1 (
    .D(multiplexer_1_out), .en(EN_H), .Q(PCout), .clk(CLK));  // open: clr
  Register #(.width(32), .trigger("rising"), .Select("low")) register_2 (
    .D(multiplexer_2_out), .en(EN_H), .Q(IRout), .clk(CLK));  // open: clr
  Multiplexer #(.select(1), .width(32), .disabled("Z"), .enable("false")) multiplexer_3 (
    .in0(Resultin), .in1({32{1'b0}}), .out(multiplexer_3_out), .sel(RST));
  Multiplexer #(.select(1), .width(32), .disabled("Z"), .enable("false")) multiplexer_4 (
    .in0(RMDatain), .in1({32{1'b0}}), .out(multiplexer_4_out), .sel(RST));
  Multiplexer #(.select(1), .width(32), .disabled("Z"), .enable("false")) multiplexer_5 (
    .in0(ImmUin), .in1({32{1'b0}}), .out(multiplexer_5_out), .sel(RST));
  Register #(.width(32), .trigger("rising"), .Select("low")) register_3 (
    .D(multiplexer_3_out), .en(EN_H), .Q(Resultout), .clk(CLK));  // open: clr
  Register #(.width(32), .trigger("rising"), .Select("low")) register_4 (
    .D(multiplexer_4_out), .en(EN_H), .Q(RMdataout), .clk(CLK));  // open: clr
  Register #(.width(32), .trigger("rising"), .Select("low")) register_5 (
    .D(multiplexer_5_out), .en(EN_H), .Q(ImmUout), .clk(CLK));  // open: clr
  Multiplexer #(.select(1), .width(9), .disabled("Z"), .enable("false")) multiplexer_6 (
    .in0({Haltin, U_Typein, BLTUin, LBUin, URETin, RegWritein, Jalrin, Jalin, MemToRegin}), .in1({9{1'b0}}),
    .out(multiplexer_6_out), .sel(RST));
  Multiplexer #(.select(1), .width(5), .disabled("Z"), .enable("false")) multiplexer_7 (
    .in0(W_in), .in1({5{1'b0}}), .out(multiplexer_7_out), .sel(RST));
  Register #(.width(9), .trigger("rising"), .Select("low")) register_6 (
    .D(multiplexer_6_out), .en(EN_H),
    .Q({Haltout, U_Typeout, BLTUout, LBUout, URETout, RegWriteout, Jalrout, Jalout, MemToRegout}), .clk(CLK));  // open: clr
  Register #(.width(5), .trigger("rising"), .Select("low")) register_7 (
    .D(multiplexer_7_out), .en(EN_H), .Q(W_out), .clk(CLK));  // open: clr

  // Other names for the same wires on the sheet: flagsin[8:0] = {Haltin, U_Typein, BLTUin, LBUin, URETin, RegWritein, Jalrin, Jalin, MemToRegin};
  //   flagsout[8:0] = {Haltout, U_Typeout, BLTUout, LBUout, URETout, RegWriteout, Jalrout, Jalout, MemToRegout}
endmodule

module \数据冲突处理_气泡  (
  input  ID_R1,
  input  EX_RW,
  input  ID_R2,
  input  MEM_RW,
  input  [4:0] ID_R1_num,
  input  [4:0] EX_W_num,
  input  [4:0] ID_R2_num,
  input  [4:0] MEM_W_num,
  output out_9
);

  wire and_1_out, and_2_out, and_3_out, and_4_out, and_5_out, and_6_out, comparator_1_eq, comparator_2_eq,
       comparator_3_eq, comparator_4_eq, comparator_5_eq, comparator_6_eq, comparator_7_eq, comparator_8_eq,
       or_1_out, or_2_out;

  Comparator #(.width(5), .mode("twosComplement")) comparator_1 (
    .a({5{1'b0}}), .b(EX_W_num), .eq(comparator_1_eq));  // open: gt, lt
  Comparator #(.width(5), .mode("twosComplement")) comparator_2 (
    .a(EX_W_num), .b(ID_R1_num), .eq(comparator_2_eq));  // open: gt, lt
  Comparator #(.width(5), .mode("twosComplement")) comparator_3 (
    .a(ID_R1_num), .b(MEM_W_num), .eq(comparator_3_eq));  // open: gt, lt
  Comparator #(.width(5), .mode("twosComplement")) comparator_4 (
    .a(MEM_W_num), .b({5{1'b0}}), .eq(comparator_4_eq));  // open: gt, lt
  Comparator #(.width(5), .mode("twosComplement")) comparator_5 (
    .a({5{1'b0}}), .b(MEM_W_num), .eq(comparator_5_eq));  // open: gt, lt
  Comparator #(.width(5), .mode("twosComplement")) comparator_6 (
    .a(MEM_W_num), .b(ID_R2_num), .eq(comparator_6_eq));  // open: gt, lt
  Comparator #(.width(5), .mode("twosComplement")) comparator_7 (
    .a(ID_R2_num), .b(EX_W_num), .eq(comparator_7_eq));  // open: gt, lt
  Comparator #(.width(5), .mode("twosComplement")) comparator_8 (
    .a(EX_W_num), .b({5{1'b0}}), .eq(comparator_8_eq));  // open: gt, lt
  and and_1 (and_1_out, EX_RW, ~comparator_1_eq, comparator_2_eq);  // AND_Gate
  and and_2 (and_2_out, comparator_3_eq, ~comparator_4_eq, MEM_RW);  // AND_Gate
  and and_3 (and_3_out, MEM_RW, ~comparator_5_eq, comparator_6_eq);  // AND_Gate
  and and_4 (and_4_out, comparator_7_eq, ~comparator_8_eq, EX_RW);  // AND_Gate
  or or_1 (or_1_out, and_1_out, and_2_out);
  or or_2 (or_2_out, and_3_out, and_4_out);
  and and_5 (and_5_out, or_1_out, ID_R1);
  and and_6 (and_6_out, ID_R2, or_2_out);
  or or_3 (out_9, and_5_out, and_6_out);

  // Other names for the same wires on the sheet: 相关 = out_9
endmodule

module \数据冲突处理_重定向  (
  input  ID_R1,
  input  EX_RW,
  input  ID_R2,
  input  MEM_RW,
  input  [4:0] ID_R1_num,
  input  [4:0] EX_W_num,
  input  [4:0] ID_R2_num,
  input  [4:0] MEM_W_num,
  input  [4:0] EX_OP,
  output \数据相关 ,
  output LoadUse,
  output [1:0] R1Forward,
  output [1:0] R2Forward
);

  wire and_1_out, and_2_out, and_5_out, and_6_out, and_7_out, and_8_out, and_11_out, and_12_out,
       comparator_1_eq, comparator_2_eq, comparator_3_eq, comparator_4_eq, comparator_5_eq, comparator_6_eq,
       comparator_7_eq, comparator_8_eq, comparator_9_eq, comparator_10_eq, \EX_R1冲突 , \EX_R2冲突 , \MEM_R1冲突 ,
       \MEM_R2冲突 , or_1_out, or_2_out, or_4_out, or_5_out;

  or or_1 (or_1_out, \EX_R1冲突 , \MEM_R1冲突 );
  or or_2 (or_2_out, \MEM_R2冲突 , \EX_R2冲突 );
  Comparator #(.width(5), .mode("twosComplement")) comparator_1 (
    .a({5{1'b0}}), .b(EX_W_num), .eq(comparator_1_eq));  // open: gt, lt
  Comparator #(.width(5), .mode("twosComplement")) comparator_2 (
    .a(EX_W_num), .b(ID_R1_num), .eq(comparator_2_eq));  // open: gt, lt
  Comparator #(.width(5), .mode("twosComplement")) comparator_3 (
    .a(ID_R1_num), .b(MEM_W_num), .eq(comparator_3_eq));  // open: gt, lt
  Comparator #(.width(5), .mode("twosComplement")) comparator_4 (
    .a(MEM_W_num), .b({5{1'b0}}), .eq(comparator_4_eq));  // open: gt, lt
  and and_1 (and_1_out, or_1_out, ID_R1);
  and and_2 (and_2_out, ID_R2, or_2_out);
  and and_3 (\EX_R1冲突 , EX_RW, ~comparator_1_eq, comparator_2_eq);  // AND_Gate
  and and_4 (\MEM_R1冲突 , comparator_3_eq, ~comparator_4_eq, MEM_RW);  // AND_Gate
  or or_3 (\数据相关 , and_1_out, and_2_out);
  and and_5 (and_5_out, \MEM_R1冲突 , ID_R1);
  and and_6 (and_6_out, ID_R1, \EX_R1冲突 );
  and and_7 (and_7_out, \MEM_R2冲突 , ID_R2);
  and and_8 (and_8_out, ID_R2, \EX_R2冲突 );
  Comparator #(.width(5), .mode("twosComplement")) comparator_5 (
    .a({5{1'b0}}), .b(MEM_W_num), .eq(comparator_5_eq));  // open: gt, lt
  Comparator #(.width(5), .mode("twosComplement")) comparator_6 (
    .a(MEM_W_num), .b(ID_R2_num), .eq(comparator_6_eq));  // open: gt, lt
  Comparator #(.width(5), .mode("twosComplement")) comparator_7 (
    .a(ID_R2_num), .b(EX_W_num), .eq(comparator_7_eq));  // open: gt, lt
  Comparator #(.width(5), .mode("twosComplement")) comparator_8 (
    .a(EX_W_num), .b({5{1'b0}}), .eq(comparator_8_eq));  // open: gt, lt
  Priority_Encoder #(.select(2), .disabled("Z")) priority_encoder_1 (
    .in0(1'b1), .in1(and_5_out), .in2(and_6_out), .out(R1Forward));  // open: in3, gs, en_out, en_in
  Priority_Encoder #(.select(2), .disabled("Z")) priority_encoder_2 (
    .in0(1'b1), .in1(and_7_out), .in2(and_8_out), .out(R2Forward));  // open: in3, gs, en_out, en_in
  and and_9 (\MEM_R2冲突 , MEM_RW, ~comparator_5_eq, comparator_6_eq);  // AND_Gate
  and and_10 (\EX_R2冲突 , comparator_7_eq, ~comparator_8_eq, EX_RW);  // AND_Gate
  Comparator #(.width(5), .mode("twosComplement")) comparator_9 (
    .a({5{1'b0}}), .b(EX_OP), .eq(comparator_9_eq));  // open: gt, lt
  Comparator #(.width(5), .mode("twosComplement")) comparator_10 (
    .a(EX_OP), .b(5'b00101), .eq(comparator_10_eq));  // open: gt, lt
  and and_11 (and_11_out, \EX_R1冲突 , ID_R1);
  and and_12 (and_12_out, ID_R2, \EX_R2冲突 );
  or or_4 (or_4_out, comparator_9_eq, comparator_10_eq);
  or or_5 (or_5_out, and_11_out, and_12_out);
  and and_13 (LoadUse, or_4_out, or_5_out);

  // Other names for the same wires on the sheet: Load_Use = LoadUse; R1F[1:0] = R1Forward; R2F[1:0] = R2Forward;
  //   相关 = \数据相关 
endmodule

module \动态分支预测  (
  output RegWrite,
  output MemWrite,
  output [31:0] IF_PC,
  output [31:0] ID_PC,
  output [31:0] EX_PC,
  output [31:0] M_PC,
  output [31:0] WB_PC,
  output [31:0] RDin,
  output [31:0] MDin,
  output [31:0] LedData
);

  wire and_2_out, and_3_out, and_4_out, and_5_out, and_6_out, and_7_out, BLTU, Branch, Branchd, BranchTaken,
       CLK, clock_1_out, comparator_1_eq, comparator_1_lt, comparator_2_eq, d_ff_1_q, en, EQ, EX_AluSrcB,
       EX_ecall, EX_Halt, EX_jal, EX_jalr, ex_mem_1_bltuout, ex_mem_1_haltout, ex_mem_1_jalout,
       ex_mem_1_jalrout, ex_mem_1_lbuout, ex_mem_1_memtoregout, ex_mem_1_u_typeout, ex_mem_1_uretout,
       EX_PredictErr, EX_PredictJump, EX_RegWrite, EX_S_Type, Go, halt, ID_ecall, id_ex_1_beqout,
       id_ex_1_bltuout, id_ex_1_bneout, id_ex_1_memtoregout, id_ex_1_memwriteout, id_ex_1_u_typeout,
       id_ex_1_uretout, if_id_1_pjout, IR1, IR2, IR3, LoadUse, LT, MEM_RegWrite, mem_wb_1_haltout,
       mem_wb_1_jalout, mem_wb_1_jalrout, mem_wb_1_lbuout, mem_wb_1_memtoregout, nand_1_out, not_1_out,
       not_2_out, not_3_out, or_1_out, or_3_out, or_4_out, or_5_out, or_8_out, PredictJump, RST, W1, W2, W3,
       WB_U_Type, \单周期硬布线控制器_1_alu_src , \单周期硬布线控制器_1_beq , \单周期硬布线控制器_1_bltu , \单周期硬布线控制器_1_bne ,
       \单周期硬布线控制器_1_jal , \单周期硬布线控制器_1_jalr , \单周期硬布线控制器_1_lbu , \单周期硬布线控制器_1_memtoreg ,
       \单周期硬布线控制器_1_memwrite , \单周期硬布线控制器_1_r1 , \单周期硬布线控制器_1_r2 , \单周期硬布线控制器_1_regwrite ,
       \单周期硬布线控制器_1_s_type , \单周期硬布线控制器_1_u_type , \单周期硬布线控制器_1_uret , \数据相关 ;
  wire [1:0] EX_R1Forward, EX_R2Forward, mem_wb_1_indexout, R1Forward, R2Forward;
  wire [3:0] id_ex_1_aluopout, \单周期硬布线控制器_1_alu_op ;
  wire [4:0] EX_W_num, ID_R1_num, ID_R2_num, MEM_W_num, W_num;
  wire [7:0] multiplexer_13_out;
  wire [11:0] shifter_1_out;
  wire [12:0] CNT_num;
  wire [15:0] \LoadUse次数 , \分支成功数 , \总周期数 , \插入气泡数 , \无条件分支数 , \条件分支成功数 ;
  wire [19:0] shifter_2_out;
  wire [31:0] adder_1_out, adder_2_out, adder_3_out, adder_5_out, Ain, and_1_out, Bin, bit_extender_1_out,
       bit_extender_2_out, bit_extender_3_out, bit_extender_4_out, bit_extender_5_out, BranchAddr, EX_IR,
       ex_mem_1_immuout, EX_R1F, EX_R2, EX_R2F, id_ex_1_immuout, ID_IR, IF_IR, imm_B, imm_I, imm_J, imm_S,
       JAddr, JumpAddr, MEM_IR, MEM_Result, mem_wb_1_immuout, mem_wb_1_resultout, mem_wb_1_rmdataout,
       multiplexer_1_out, multiplexer_3_out, multiplexer_4_out, multiplexer_5_out, multiplexer_6_out,
       multiplexer_11_out, multiplexer_14_out, multiplexer_15_out, multiplexer_16_out, PC_4, R1, R2,
       ram_1_data, WB_IR, WB_PC_4;

  Button \u_总复位  (.out(RST));
  Button _1 (.out(IR1));
  Button _2 (.out(IR2));
  Button _3 (.out(IR3));
  // Probe on \总周期数 
  // Probe on \总周期数 
  Button \u_继续运行  (.out(Go));
  LED #(.active("true")) led_1 (.in(W1));
  LED #(.active("true")) led_2 (.in(W2));
  LED #(.active("true")) led_3 (.in(W3));
  // Probe on \分支成功数 
  Hex_Digit_Display hex_digit_display_1 (.value(LedData[31:28]));  // open: dp
  // Probe on IF_PC[19:0]
  // RiscV_Probe riscv_probe_1: pin names not known; wires that end beside it: IF_IR
  Adder #(.width(32)) adder_1 (.a(imm_J), .b(EX_PC), .out(adder_1_out));  // open: cin, cout
  Adder #(.width(32)) adder_2 (.a(imm_B), .b(EX_PC), .out(adder_2_out));  // open: cin, cout
  Hex_Digit_Display hex_digit_display_2 (.value(LedData[27:24]));  // open: dp
  Hex_Digit_Display hex_digit_display_3 (.value(LedData[23:20]));  // open: dp
  // Probe on ID_PC[19:0]
  // RiscV_Probe riscv_probe_2: pin names not known; wires that end beside it: ID_IR
  not not_1 (not_1_out, halt);
  or or_1 (or_1_out, Branch, EX_jal);
  or or_2 (Branchd, EX_jal, BranchTaken);
  Adder #(.width(32)) adder_3 (.a(EX_PC), .b(32'h4), .out(adder_3_out));  // open: cin, cout
  Multiplexer #(.select(1), .width(32), .disabled("Z"), .enable("false")) multiplexer_1 (
    .in0(PC_4), .in1(adder_1_out), .out(multiplexer_1_out), .sel(EX_jal));
  Multiplexer #(.select(1), .width(32), .disabled("Z"), .enable("false")) multiplexer_2 (
    .in0(multiplexer_1_out), .in1(adder_2_out), .out(BranchAddr), .sel(Branch));
  Hex_Digit_Display hex_digit_display_4 (.value(LedData[15:12]));  // open: dp
  Hex_Digit_Display hex_digit_display_5 (.value(LedData[19:16]));  // open: dp
  Counter #(.width(16), .max('hffff), .ongoal("wrap"), .trigger("rising"), .behavior("new")) counter_1 (
    .count(not_1_out), .Q(\总周期数 ), .clk(CLK), .clr(RST));  // open: load, D, carry, preset, down
  Multiplexer #(.select(1), .width(32), .disabled("Z"), .enable("false")) multiplexer_3 (
    .in0(multiplexer_6_out), .in1(multiplexer_4_out), .out(multiplexer_3_out), .sel(EX_PredictErr));
  Multiplexer #(.select(1), .width(32), .disabled("Z"), .enable("false")) multiplexer_4 (
    .in0(adder_3_out), .in1(BranchAddr), .out(multiplexer_4_out), .sel(Branchd));
  Hex_Digit_Display hex_digit_display_6 (.value(LedData[11:8]));  // open: dp
  Hex_Digit_Display hex_digit_display_7 (.value(LedData[7:4]));  // open: dp
  // Probe on EX_PC[19:0]
  // RiscV_Probe riscv_probe_3: pin names not known; wires that end beside it: EX_IR
  BHT bht_1 (
    .Clk(CLK), .EX_Branch(or_1_out), .PC(IF_PC), .EX_PC(EX_PC), .EX_BranchAddr(BranchAddr),
    .EX_Branched(Branchd), .JumpAddr(JumpAddr), .PredictJump(PredictJump));
  Multiplexer #(.select(1), .width(32), .disabled("Z"), .enable("false")) multiplexer_5 (
    .in0(multiplexer_3_out), .in1(and_1_out), .out(multiplexer_5_out), .sel(EX_jalr));
  assign and_1_out = JAddr & 32'hfffffffe;  // AND_Gate and_1, 32 bits wide
  Hex_Digit_Display hex_digit_display_8 (.value(LedData[3:0]));  // open: dp
  Multiplexer #(.select(1), .width(32), .disabled("Z"), .enable("false")) multiplexer_6 (
    .in0(PC_4), .in1(JumpAddr), .out(multiplexer_6_out), .sel(PredictJump));
  Register #(.width(32), .trigger("rising"), .Select("low")) PC (
    .D(multiplexer_5_out), .en(and_2_out), .Q(IF_PC), .clk(CLK), .clr(RST));
  and and_2 (and_2_out, ~LoadUse, ~halt);  // AND_Gate
  // Probe on \总周期数 
  // Probe on M_PC[19:0]
  // RiscV_Probe riscv_probe_4: pin names not known; wires that end beside it: MEM_IR
  // Probe on \总周期数 
  // Probe on \无条件分支数 
  // Probe on \条件分支成功数 
  // Probe on \插入气泡数 
  // Probe on \LoadUse次数 
  or or_3 (or_3_out, BranchTaken, EX_jalr, EX_jal);
  Adder #(.width(32)) adder_4 (.a(IF_PC), .b(32'h4), .out(PC_4));  // open: cin, cout
  // Probe on IF_PC[11:0]
  // Probe on WB_PC[19:0]
  // RiscV_Probe riscv_probe_5: pin names not known; wires that end beside it: WB_IR
  xor xor_1 (EX_PredictErr, EX_PredictJump, or_3_out);
  ROM #(.addrWidth(10), .dataWidth(32), .Select("high")) rom_1 (.addr(IF_PC[11:2]), .data(IF_IR));
  // Probe on ID_PC[11:0]
  // Probe on EX_PC[11:0]
  or or_4 (or_4_out, RST, EX_PredictErr);
  IF_ID if_id_1 (
    .PCin(IF_PC), .IRin(IF_IR), .PCout(ID_PC), .IRout(ID_IR), .RST(or_4_out), .EN_H(and_3_out), .CLK(CLK),
    .PJin(PredictJump), .PJout(if_id_1_pjout));
  and and_3 (and_3_out, ~LoadUse, en);  // AND_Gate
  // Probe on M_PC[11:0]
  D_Flip_Flop #(.trigger("high"), .Pre_Clr_Positions("LEGACY"), .NegatePresetClear("false"), .enable("true"), .NewFFLayout("false")) d_ff_1 (.Q(d_ff_1_q));  // open: clk, D, Qn, preset, en, reset
  // Probe on 13'hc
  // Probe on WB_PC[11:0]
  Comparator #(.width(13), .mode("twosComplement")) comparator_1 (
    .a(CNT_num), .b(13'hc), .eq(comparator_1_eq), .lt(comparator_1_lt));  // open: gt
  Clock #(.highDuration(1), .lowDuration(1)) clock_1 (.out(clock_1_out));
  nand nand_1 (nand_1_out, d_ff_1_q, comparator_1_eq);
  Counter #(.width(13), .max('h1fff), .ongoal("stay"), .trigger("rising"), .behavior("old")) counter_2 (
    .count(comparator_1_lt), .Q(CNT_num), .clk(clock_1_out));  // open: load, D, carry, clr, preset
  \数据冲突处理_重定向  \u_数据冲突处理_重定向_1  (
    .ID_R1(\单周期硬布线控制器_1_r1 ), .EX_RW(EX_RegWrite), .ID_R2(\单周期硬布线控制器_1_r2 ), .MEM_RW(MEM_RegWrite),
    .ID_R1_num(ID_R1_num), .EX_W_num(EX_W_num), .ID_R2_num(ID_R2_num), .MEM_W_num(MEM_W_num),
    .EX_OP(EX_IR[6:2]), .\数据相关 (\数据相关 ), .LoadUse(LoadUse), .R1Forward(R1Forward), .R2Forward(R2Forward));
  \单周期硬布线控制器  \u_单周期硬布线控制器_1  (
    .Funct({ID_IR[30], ID_IR[25], ID_IR[14:12]}), .OP(ID_IR[6:2]), .ALU_OP(\单周期硬布线控制器_1_alu_op ),
    .MemToReg(\单周期硬布线控制器_1_memtoreg ), .MemWrite(\单周期硬布线控制器_1_memwrite ), .ALU_SRC(\单周期硬布线控制器_1_alu_src ),
    .RegWrite(\单周期硬布线控制器_1_regwrite ), .ecall(ID_ecall), .S_type(\单周期硬布线控制器_1_s_type ),
    .Jalr(\单周期硬布线控制器_1_jalr ), .Beq(\单周期硬布线控制器_1_beq ), .JAL(\单周期硬布线控制器_1_jal ), .Bne(\单周期硬布线控制器_1_bne ),
    .in_3(ID_IR[21]), .uret(\单周期硬布线控制器_1_uret ), .BLTU(\单周期硬布线控制器_1_bltu ), .U_Type(\单周期硬布线控制器_1_u_type ),
    .LBU(\单周期硬布线控制器_1_lbu ), .R1(\单周期硬布线控制器_1_r1 ), .R2(\单周期硬布线控制器_1_r2 ));  // open: CSRRSI, CSRRCI
  Multiplexer #(.select(1), .width(5), .disabled("Z"), .enable("false")) multiplexer_7 (
    .in0(ID_IR[24:20]), .in1(5'b01010), .out(ID_R2_num), .sel(ID_ecall));
  assign bit_extender_1_out = {{20{ID_IR[31]}}, ID_IR[31:20]};  // Bit_Extender bit_extender_1
  assign bit_extender_2_out = {{20{ID_IR[31]}}, {ID_IR[31:25], ID_IR[11:7]}};  // Bit_Extender bit_extender_2
  assign CLK = nand_1_out ? clock_1_out : 1'bz;  // Controlled_Buffer controlled_buffer_1
  Multiplexer #(.select(1), .width(5), .disabled("Z"), .enable("false")) multiplexer_8 (
    .in0(ID_IR[19:15]), .in1(5'b10001), .out(ID_R1_num), .sel(ID_ecall));
  Shifter #(.width(12), .shift("ll")) shifter_1 (
    .in({ID_IR[31], ID_IR[7], ID_IR[30:25], ID_IR[11:8]}), .\dist (4'b0001), .out(shifter_1_out));
  Shifter #(.width(20), .shift("ll")) shifter_2 (
    .in({ID_IR[31], ID_IR[19:12], ID_IR[20], ID_IR[30:21]}), .\dist (5'b00001), .out(shifter_2_out));
  Pull_Resistor #(.pull(1)) pull_resistor_1 (.node(CLK));
  assign bit_extender_3_out = {{20{shifter_1_out[11]}}, shifter_1_out};  // Bit_Extender bit_extender_3
  assign bit_extender_4_out = {{12{shifter_2_out[19]}}, shifter_2_out};  // Bit_Extender bit_extender_4
  not not_2 (not_2_out, CLK);
  Regifile regifile_1 (
    .Din(RDin), .Clk(not_2_out), .R1(R1), .R2(R2), .WE(RegWrite), .W_num(W_num), .R1_num(ID_R1_num),
    .R2_num(ID_R2_num));
  or or_5 (or_5_out, LoadUse, or_4_out);
  ID_EX id_ex_1 (
    .PCin(ID_PC), .IRin(ID_IR), .ImmIin(bit_extender_1_out), .ImmSin(bit_extender_2_out),
    .ImmBin(bit_extender_3_out), .ImmJin(bit_extender_4_out), .R1in(R1), .R2in(R2),
    .AluOpin(\单周期硬布线控制器_1_alu_op ), .RST(or_5_out), .EN_H(en), .CLK(CLK), .Beqin(\单周期硬布线控制器_1_beq ),
    .Bnein(\单周期硬布线控制器_1_bne ), .MemToRegin(\单周期硬布线控制器_1_memtoreg ), .MemWritein(\单周期硬布线控制器_1_memwrite ),
    .AluSrcBin(\单周期硬布线控制器_1_alu_src ), .RegWritein(\单周期硬布线控制器_1_regwrite ), .S_typein(\单周期硬布线控制器_1_s_type ),
    .Jalin(\单周期硬布线控制器_1_jal ), .Jalrin(\单周期硬布线控制器_1_jalr ), .Haltin(1'b0), .Beqout(id_ex_1_beqout),
    .Bneout(id_ex_1_bneout), .MemToRegout(id_ex_1_memtoregout), .MemWriteout(id_ex_1_memwriteout),
    .AluSrcBout(EX_AluSrcB), .RegWriteout(EX_RegWrite), .S_Typeout(EX_S_Type), .Jalout(EX_jal),
    .Jalrout(EX_jalr), .AluOpout(id_ex_1_aluopout), .PCout(EX_PC), .IRout(EX_IR), .Imm_I_out(imm_I),
    .Imm_S_out(imm_S), .Imm_B_out(imm_B), .Imm_J_out(imm_J), .R1out(EX_R1F), .R2out(EX_R2F),
    .W_in(ID_IR[11:7]), .W_out(EX_W_num), .URETin(\单周期硬布线控制器_1_uret ), .LBUin(\单周期硬布线控制器_1_lbu ),
    .BLTUin(\单周期硬布线控制器_1_bltu ), .U_Typein(\单周期硬布线控制器_1_u_type ), .URETout(id_ex_1_uretout), .LBUout(BLTU),
    .BLTUout(id_ex_1_bltuout), .U_Typeout(id_ex_1_u_typeout), .ImmUin({ID_IR[31:12], {12{1'b0}}}),
    .ImmUout(id_ex_1_immuout), .Ecallin(ID_ecall), .Ecallout(EX_ecall), .R1Forwardin(R1Forward),
    .R1Forwardout(EX_R1Forward), .R2Forwardin(R2Forward), .R2Forwardout(EX_R2Forward), .PJin(if_id_1_pjout),
    .PJout(EX_PredictJump));  // open: Haltout
  or or_6 (Branch, id_ex_1_beqout, id_ex_1_bneout, id_ex_1_bltuout);
  Comparator #(.width(32), .mode("twosComplement")) comparator_2 (
    .a(Ain), .b(32'h22), .eq(comparator_2_eq));  // open: gt, lt
  not not_3 (not_3_out, EQ);
  Multiplexer #(.select(2), .width(32), .disabled("Z"), .enable("false")) multiplexer_9 (
    .in0(EX_R1F), .in1(RDin), .in2(MEM_Result), .out(Ain), .sel(EX_R1Forward));  // open: in3
  Multiplexer #(.select(2), .width(32), .disabled("Z"), .enable("false")) multiplexer_10 (
    .in0(EX_R2F), .in1(RDin), .in2(MEM_Result), .out(EX_R2), .sel(EX_R2Forward));  // open: in3
  Multiplexer #(.select(1), .width(32), .disabled("Z"), .enable("false")) multiplexer_11 (
    .in0(imm_I), .in1(imm_S), .out(multiplexer_11_out), .sel(EX_S_Type));
  and and_4 (and_4_out, id_ex_1_beqout, EQ);
  or or_7 (BranchTaken, and_4_out, and_5_out, and_6_out);
  and and_5 (and_5_out, not_3_out, id_ex_1_bneout);
  and and_6 (and_6_out, LT, id_ex_1_bltuout);
  ALU alu_1 (
    .X(Ain), .Y(Bin), .AluOP(id_ex_1_aluopout), .Equal(EQ), .Result(JAddr), .out_6(LT));  // open: Result_2, out_4
  Multiplexer #(.select(1), .width(32), .disabled("Z"), .enable("false")) multiplexer_12 (
    .in0(EX_R2), .in1(multiplexer_11_out), .out(Bin), .sel(EX_AluSrcB));
  Register #(.width(32), .trigger("rising"), .Select("low")) register_1 (
    .D(EX_R2), .en(and_7_out), .Q(LedData), .clk(CLK), .clr(RST));
  and and_7 (and_7_out, EX_ecall, comparator_2_eq);
  and and_8 (EX_Halt, ~comparator_2_eq, EX_ecall, ~Go);  // AND_Gate
  EX_MEM ex_mem_1 (
    .PCin(EX_PC), .IRin(EX_IR), .Resultin(JAddr), .MDatain(EX_R2), .PCout(M_PC), .IRout(MEM_IR),
    .Resultout(MEM_Result), .Mdataout(MDin), .MemToRegin(id_ex_1_memtoregout),
    .MemWritein(id_ex_1_memwriteout), .Jalin(EX_jal), .RegWritein(EX_RegWrite), .Haltin(EX_Halt),
    .MemToRegout(ex_mem_1_memtoregout), .MemWriteout(MemWrite), .Jalout(ex_mem_1_jalout),
    .RegWriteout(MEM_RegWrite), .Haltout(ex_mem_1_haltout), .RST(RST), .EN_H(en), .CLK(CLK), .W_in(EX_W_num),
    .W_out(MEM_W_num), .URETin(id_ex_1_uretout), .LBUin(BLTU), .BLTUin(id_ex_1_bltuout),
    .U_Typein(id_ex_1_u_typeout), .URETout(ex_mem_1_uretout), .LBUout(ex_mem_1_lbuout),
    .BLTUout(ex_mem_1_bltuout), .U_Typeout(ex_mem_1_u_typeout), .Jalrin(EX_jalr), .Jalrout(ex_mem_1_jalrout),
    .ImmUin(id_ex_1_immuout), .ImmUout(ex_mem_1_immuout));
  RAM #(.addrWidth(10), .dataWidth(32), .bus("separate"), .Select("high")) ram_1 (
    .addr(MEM_Result[11:2]), .din(MDin), .data(ram_1_data), .str(MemWrite), .clk(CLK),
    .ld(ex_mem_1_memtoregout), .clr(RST));  // open: sel
  MEM_WB mem_wb_1 (
    .PCin(M_PC), .IRin(MEM_IR), .Resultin(MEM_Result), .RMDatain(ram_1_data), .PCout(WB_PC), .IRout(WB_IR),
    .Resultout(mem_wb_1_resultout), .RMdataout(mem_wb_1_rmdataout), .RST(RST), .W_in(MEM_W_num), .EN_H(en),
    .W_out(W_num), .CLK(CLK), .MemToRegin(ex_mem_1_memtoregout), .Jalin(ex_mem_1_jalout),
    .RegWritein(MEM_RegWrite), .Haltin(ex_mem_1_haltout), .MemToRegout(mem_wb_1_memtoregout),
    .RegWriteout(RegWrite), .Jalrin(ex_mem_1_jalrout), .URETin(ex_mem_1_uretout), .LBUin(ex_mem_1_lbuout),
    .BLTUin(ex_mem_1_bltuout), .U_Typein(ex_mem_1_u_typeout), .Jalout(mem_wb_1_jalout),
    .Jalrout(mem_wb_1_jalrout), .LBUout(mem_wb_1_lbuout), .U_Typeout(WB_U_Type), .ImmUin(ex_mem_1_immuout),
    .ImmUout(mem_wb_1_immuout), .Indexin(MEM_Result[1:0]), .Indexout(mem_wb_1_indexout),
    .Haltout(mem_wb_1_haltout));  // open: URETout, BLTUout
  Multiplexer #(.select(2), .width(8), .disabled("Z"), .enable("false")) multiplexer_13 (
    .in0(mem_wb_1_rmdataout[7:0]), .in1(mem_wb_1_rmdataout[15:8]), .in2(mem_wb_1_rmdataout[23:16]),
    .in3(mem_wb_1_rmdataout[31:24]), .out(multiplexer_13_out), .sel(mem_wb_1_indexout));
  and and_9 (halt, mem_wb_1_haltout, ~Go);  // AND_Gate
  not not_4 (en, halt);
  or or_8 (or_8_out, mem_wb_1_jalout, mem_wb_1_jalrout, WB_U_Type);
  assign bit_extender_5_out = {{24{1'b0}}, multiplexer_13_out};  // Bit_Extender bit_extender_5
  Adder #(.width(32)) adder_5 (.a(WB_PC), .b(mem_wb_1_immuout), .out(adder_5_out));  // open: cin, cout
  Adder #(.width(32)) adder_6 (.a(32'h4), .b(WB_PC), .out(WB_PC_4));  // open: cin, cout
  Multiplexer #(.select(1), .width(32), .disabled("Z"), .enable("false")) multiplexer_14 (
    .in0(mem_wb_1_resultout), .in1(multiplexer_15_out), .out(multiplexer_14_out), .sel(mem_wb_1_memtoregout));
  Multiplexer #(.select(1), .width(32), .disabled("Z"), .enable("false")) multiplexer_15 (
    .in0(mem_wb_1_rmdataout), .in1(bit_extender_5_out), .out(multiplexer_15_out), .sel(mem_wb_1_lbuout));
  Multiplexer #(.select(1), .width(32), .disabled("Z"), .enable("false")) multiplexer_16 (
    .in0(WB_PC_4), .in1(adder_5_out), .out(multiplexer_16_out), .sel(WB_U_Type));
  Multiplexer #(.select(1), .width(32), .disabled("Z"), .enable("false")) multiplexer_17 (
    .in0(multiplexer_14_out), .in1(multiplexer_16_out), .out(RDin), .sel(or_8_out));

  // Other names for the same wires on the sheet: IR[31:0] = ID_IR; RD_num[4:0] = ID_IR[11:7]; EX_R1[31:0] = Ain;
  //   MEM_MemWrite = MemWrite; MEM_PC[31:0] = M_PC; WB_RegWrite = RegWrite; WriteBackData[31:0] = RDin

  // Notes on the sheet:
  //   中断源
  //   时空图监测，可删除
  //   中断等待指示
  //   数码管输出
  //   指令存储器
  //   contents of rom_1 (hex, n*v repeats v):
  //   100493 100006f 100493 200913 300993 100006f 100493 200913 300993 100006f 100493 200913 300993
  //   100006f 100493 200913 300993 29c000ef 100413 100493 1f49493 900533 2200893 73 24d493 48463 fedff06f
  //   900533 2200893 73 100493 249493 900533 2200893 73 48463 fedff06f 100493 1f49493 900533 2200893 73
  //   4034d493 900533 2200893 73 4044d493 900533 2200893 73 4044d493 900533 2200893 73 4044d493 900533
  //   2200893 73 4044d493 900533 2200893 73 4044d493 900533 2200893 73 4044d493 900533 2200893 73 4044d493
  //   900533 2200893 73 100413 1f41993 41f9d993 433 c00913 300b13 140413 f47413 800293 100313 499993
  //   89e9b3 1300533 2200893 73 406282b3 fe0294e3 140413 f00f93 1f47433 1c41413 800293 100313 49d993
  //   89e9b3 1300533 2200893 73 406282b3 fe0294e3 1c45413 406b0b33 b0463 f95ff06f 2b3 fff2c293 829293
  //   ff2e293 500533 2200893 73 fff00413 493 84a023 140413 448493 84a023 140413 448493 84a023 140413
  //   448493 84a023 140413 448493 84a023 140413 448493 84a023 140413 448493 84a023 140413 448493 84a023
  //   140413 448493 84a023 140413 448493 84a023 140413 448493 84a023 140413 448493 84a023 140413 448493
  //   84a023 140413 448493 84a023 140413 448493 84a023 140413 448493 84a023 140413 448493 140413 433
  //   3c00493 42983 4aa03 149a2b3 28663 134a023 1442023 ffc48493 fe9412e3 800533 2200893 73 440413 3c00493
  //   fc9416e3 a00893 73 413 140413 800533 2200893 73 240413 800533 2200893 73 340413 800533 2200893 73
  //   440413 800533 2200893 73 540413 800533 2200893 73 640413 800533 2200893 73 740413 800533 2200893 73
  //   840413 800533 2200893 2200893 73 8067
  //   控制位
  //   流水调试日志用
  //   暂停节拍，不能为0
  //   戳工具置1进入计数暂停模式，ctrl+k时钟自动运行到对应节拍暂停
  //   ctrl+k关闭时钟连续运行，将控制位置零，进入单步调试模式调试
  //   ctrl+k关闭时钟连续运行，将控制位置零，进入单步调试模式调试
  //   rs1
  //   rs2
  //   指令字
  //   rd
  //   可计数暂停的时钟源
  //   为方便自动评测，需要输出流水线各段保存的PC值，注意是PC不是PC+4，另外ID段寄存器写入信息，Mem段内存写入信息也要输出
endmodule
module BHT (
  input  Clk,
  input  EX_Branch,
  input  [31:0] PC,
  input  [31:0] EX_PC,
  input  [31:0] EX_BranchAddr,
  input  EX_Branched,
  output [31:0] JumpAddr,
  output PredictJump
);

  wire A0, A1, A2, A3, A4, A5, A6, A7, and_1_out, comparator_1_eq, comparator_2_eq, comparator_3_eq,
       comparator_4_eq, comparator_5_eq, comparator_6_eq, comparator_7_eq, comparator_8_eq, comparator_9_eq,
       comparator_10_eq, comparator_11_eq, comparator_12_eq, comparator_13_eq, comparator_14_eq,
       comparator_15_eq, comparator_16_eq, decoder_1_out0, decoder_1_out1, decoder_1_out2, decoder_1_out3,
       decoder_1_out4, decoder_1_out5, decoder_1_out6, decoder_1_out7, decoder_2_out0, decoder_2_out1,
       decoder_2_out2, decoder_2_out3, decoder_2_out4, decoder_2_out5, decoder_2_out6, decoder_2_out7,
       EX_Hit, EX_Miss, IF_Hit, IF_Miss, L0, L1, L2, L3, L4, L5, L6, L7, M0, M1, M2, M3, M4, M5, M6, M7,
       not_1_out, not_2_out, not_3_out, not_4_out, not_5_out, not_6_out, not_7_out, not_8_out, or_1_out,
       or_2_out, or_3_out, or_4_out, or_5_out, or_6_out, or_7_out, or_8_out, or_9_out, or_10_out, or_11_out,
       or_12_out, or_13_out, or_14_out, or_17_out, or_18_out, priority_encoder_1_gs, V0, V1, V2, V3, V4, V5,
       V6, V7, WriteL0, WriteL1, WriteL2, WriteL3, WriteL4, WriteL5, WriteL6, WriteL7;
  wire [0:0] controlled_buffer_1_out, controlled_buffer_2_out, controlled_buffer_3_out,
       controlled_buffer_4_out, controlled_buffer_5_out, controlled_buffer_6_out, controlled_buffer_7_out,
       controlled_buffer_8_out;
  wire [1:0] adder_1_out, adder_2_out, adder_3_out, adder_4_out, adder_5_out, adder_6_out, adder_7_out,
       adder_8_out, multiplexer_1_out, multiplexer_2_out, multiplexer_3_out, multiplexer_4_out,
       multiplexer_5_out, multiplexer_6_out, multiplexer_7_out, multiplexer_8_out, multiplexer_9_out,
       multiplexer_10_out, multiplexer_11_out, multiplexer_12_out, multiplexer_13_out, multiplexer_14_out,
       multiplexer_15_out, multiplexer_16_out, multiplexer_17_out, multiplexer_18_out, multiplexer_19_out,
       multiplexer_20_out, multiplexer_21_out, multiplexer_22_out, multiplexer_23_out, multiplexer_24_out,
       multiplexer_25_out, multiplexer_26_out, multiplexer_27_out, multiplexer_28_out, multiplexer_29_out,
       multiplexer_30_out, multiplexer_31_out, multiplexer_32_out, multiplexer_33_out, multiplexer_34_out,
       multiplexer_35_out, multiplexer_36_out, multiplexer_37_out, multiplexer_38_out, multiplexer_39_out,
       multiplexer_40_out, Predict0, Predict1, Predict2, Predict3, Predict4, Predict5, Predict6, Predict7;
  wire [2:0] max2_1_max_num, max2_2_max_num, max2_3_max_num, max2_4_max_num, max2_5_max_num, max2_6_max_num,
       max2_7_max_num, priority_encoder_1_out;
  wire [15:0] C0, C1, C2, C3, C4, C5, C6, C7, max2_1_max, max2_2_max, max2_3_max, max2_4_max, max2_5_max,
       max2_6_max;
  wire [31:0] Tag0, Tag1, Tag2, Tag3, Tag4, Tag5, Tag6, Tag7, \分支目标地址_2_q , \分支目标地址_3_q , \分支目标地址_4_q ,
       \分支目标地址_5_q , \分支目标地址_6_q , \分支目标地址_7_q , \分支目标地址_8_q , \分支目标地址_q ;

  Register #(.width(1), .trigger("rising"), .Select("low")) VALID (
    .D(1'b1), .en(WriteL0), .Q(V0), .clk(Clk));  // open: clr
  Register #(.width(1), .trigger("rising"), .Select("low")) VALID_2 (
    .D(1'b1), .en(WriteL1), .Q(V1), .clk(Clk));  // open: clr
  Register #(.width(1), .trigger("rising"), .Select("low")) VALID_3 (
    .D(1'b1), .en(WriteL2), .Q(V2), .clk(Clk));  // open: clr
  Register #(.width(1), .trigger("rising"), .Select("low")) VALID_4 (
    .D(1'b1), .en(WriteL3), .Q(V3), .clk(Clk));  // open: clr
  Register #(.width(1), .trigger("rising"), .Select("low")) VALID_5 (
    .D(1'b1), .en(WriteL4), .Q(V4), .clk(Clk));  // open: clr
  Register #(.width(1), .trigger("rising"), .Select("low")) VALID_6 (
    .D(1'b1), .en(WriteL5), .Q(V5), .clk(Clk));  // open: clr
  Register #(.width(1), .trigger("rising"), .Select("low")) VALID_7 (
    .D(1'b1), .en(WriteL6), .Q(V6), .clk(Clk));  // open: clr
  Register #(.width(1), .trigger("rising"), .Select("low")) VALID_8 (
    .D(1'b1), .en(WriteL7), .Q(V7), .clk(Clk));  // open: clr
  not not_1 (not_1_out, V0);
  not not_2 (not_2_out, V1);
  not not_3 (not_3_out, V2);
  not not_4 (not_4_out, V3);
  not not_5 (not_5_out, V4);
  not not_6 (not_6_out, V5);
  not not_7 (not_7_out, V6);
  not not_8 (not_8_out, V7);
  MAX2 max2_1 (.Y(C1), .X(C0), .Y_num(3'b001), .X_num(3'b000), .MAX(max2_1_max), .MAX_num(max2_1_max_num));
  MAX2 max2_2 (.Y(C3), .X(C2), .Y_num(3'b011), .X_num(3'b010), .MAX(max2_2_max), .MAX_num(max2_2_max_num));
  MAX2 max2_3 (.Y(C5), .X(C4), .Y_num(3'b101), .X_num(3'b100), .MAX(max2_3_max), .MAX_num(max2_3_max_num));
  MAX2 max2_4 (.Y(C7), .X(C6), .Y_num(3'b111), .X_num(3'b110), .MAX(max2_4_max), .MAX_num(max2_4_max_num));
  Pull_Resistor #(.pull(0)) pull_resistor_1 (.node(PredictJump));
  assign {PredictJump, controlled_buffer_1_out[0]} = L0 ? Predict0 : 2'bz;  // Controlled_Buffer controlled_buffer_1
  assign {PredictJump, controlled_buffer_2_out[0]} = L1 ? Predict1 : 2'bz;  // Controlled_Buffer controlled_buffer_2
  assign {PredictJump, controlled_buffer_3_out[0]} = L2 ? Predict2 : 2'bz;  // Controlled_Buffer controlled_buffer_3
  assign {PredictJump, controlled_buffer_4_out[0]} = L3 ? Predict3 : 2'bz;  // Controlled_Buffer controlled_buffer_4
  assign {PredictJump, controlled_buffer_5_out[0]} = L4 ? Predict4 : 2'bz;  // Controlled_Buffer controlled_buffer_5
  assign {PredictJump, controlled_buffer_6_out[0]} = L5 ? Predict5 : 2'bz;  // Controlled_Buffer controlled_buffer_6
  assign {PredictJump, controlled_buffer_7_out[0]} = L6 ? Predict6 : 2'bz;  // Controlled_Buffer controlled_buffer_7
  assign {PredictJump, controlled_buffer_8_out[0]} = L7 ? Predict7 : 2'bz;  // Controlled_Buffer controlled_buffer_8
  Priority_Encoder #(.select(3), .disabled("Z")) priority_encoder_1 (
    .in0(not_1_out), .in1(not_2_out), .in2(not_3_out), .in3(not_4_out), .in4(not_5_out), .in5(not_6_out),
    .in6(not_7_out), .in7(not_8_out), .out(priority_encoder_1_out), .gs(priority_encoder_1_gs));  // open: en_out, en_in
  MAX2 max2_5 (
    .Y(max2_2_max), .X(max2_1_max), .Y_num(max2_2_max_num), .X_num(max2_1_max_num), .MAX(max2_5_max),
    .MAX_num(max2_5_max_num));
  MAX2 max2_6 (
    .Y(max2_4_max), .X(max2_3_max), .Y_num(max2_4_max_num), .X_num(max2_3_max_num), .MAX(max2_6_max),
    .MAX_num(max2_6_max_num));
  and and_1 (and_1_out, V0, V1, V2, V3, V4, V5, V6, V7);
  or or_1 (or_1_out, L1, L2, L3, L4, L5, L6, L7, WriteL1, WriteL2, WriteL3, WriteL4, WriteL5, WriteL6, WriteL7);
  or or_2 (or_2_out, L0, L1, L2, L3, L5, L6, L7, WriteL0, WriteL1, WriteL2, WriteL3, WriteL5, WriteL6, WriteL7);
  Register #(.width(32), .trigger("rising"), .Select("low")) \u_分支指令地址  (
    .D(EX_PC), .en(WriteL0), .Q(Tag0), .clk(Clk));  // open: clr
  Register #(.width(32), .trigger("rising"), .Select("low")) \u_分支指令地址_2  (
    .D(EX_PC), .en(WriteL1), .Q(Tag1), .clk(Clk));  // open: clr
  Register #(.width(32), .trigger("rising"), .Select("low")) \u_分支指令地址_3  (
    .D(EX_PC), .en(WriteL2), .Q(Tag2), .clk(Clk));  // open: clr
  Register #(.width(32), .trigger("rising"), .Select("low")) \u_分支指令地址_4  (
    .D(EX_PC), .en(WriteL3), .Q(Tag3), .clk(Clk));  // open: clr
  Register #(.width(32), .trigger("rising"), .Select("low")) \u_分支指令地址_5  (
    .D(EX_PC), .en(WriteL4), .Q(Tag4), .clk(Clk));  // open: clr
  Register #(.width(32), .trigger("rising"), .Select("low")) \u_分支指令地址_6  (
    .D(EX_PC), .en(WriteL5), .Q(Tag5), .clk(Clk));  // open: clr
  Register #(.width(32), .trigger("rising"), .Select("low")) \u_分支指令地址_7  (
    .D(EX_PC), .en(WriteL6), .Q(Tag6), .clk(Clk));  // open: clr
  Register #(.width(32), .trigger("rising"), .Select("low")) \u_分支指令地址_8  (
    .D(EX_PC), .en(WriteL7), .Q(Tag7), .clk(Clk));  // open: clr
  Decoder #(.select(3), .tristate("false"), .disabled(0), .enable("true")) decoder_1 (
    .out0(decoder_1_out0), .out1(decoder_1_out1), .out2(decoder_1_out2), .out3(decoder_1_out3),
    .out4(decoder_1_out4), .out5(decoder_1_out5), .out6(decoder_1_out6), .out7(decoder_1_out7),
    .sel(priority_encoder_1_out), .en(priority_encoder_1_gs));
  Decoder #(.select(3), .tristate("false"), .disabled(0), .enable("true")) decoder_2 (
    .out0(decoder_2_out0), .out1(decoder_2_out1), .out2(decoder_2_out2), .out3(decoder_2_out3),
    .out4(decoder_2_out4), .out5(decoder_2_out5), .out6(decoder_2_out6), .out7(decoder_2_out7),
    .sel(max2_7_max_num), .en(and_1_out));
  MAX2 max2_7 (
    .Y(max2_6_max), .X(max2_5_max), .Y_num(max2_6_max_num), .X_num(max2_5_max_num), .MAX_num(max2_7_max_num));  // open: MAX
  Multiplexer #(.select(1), .width(2), .disabled("Z"), .enable("false")) multiplexer_1 (
    .in0(2'b00), .in1(2'b01), .out(multiplexer_1_out), .sel(EX_Branched));
  Multiplexer #(.select(1), .width(2), .disabled("Z"), .enable("false")) multiplexer_2 (
    .in0(2'b11), .in1(2'b01), .out(multiplexer_2_out), .sel(EX_Branched));
  Multiplexer #(.select(1), .width(2), .disabled("Z"), .enable("false")) multiplexer_3 (
    .in0(2'b01), .in1(2'b00), .out(multiplexer_3_out), .sel(EX_Branched));
  Multiplexer #(.select(1), .width(2), .disabled("Z"), .enable("false")) multiplexer_4 (
    .in0(2'b01), .in1(2'b11), .out(multiplexer_4_out), .sel(EX_Branched));
  Multiplexer #(.select(1), .width(2), .disabled("Z"), .enable("false")) multiplexer_5 (
    .in0(2'b00), .in1(2'b01), .out(multiplexer_5_out), .sel(EX_Branched));
  Multiplexer #(.select(1), .width(2), .disabled("Z"), .enable("false")) multiplexer_6 (
    .in0(2'b11), .in1(2'b01), .out(multiplexer_6_out), .sel(EX_Branched));
  Multiplexer #(.select(1), .width(2), .disabled("Z"), .enable("false")) multiplexer_7 (
    .in0(2'b01), .in1(2'b00), .out(multiplexer_7_out), .sel(EX_Branched));
  Multiplexer #(.select(1), .width(2), .disabled("Z"), .enable("false")) multiplexer_8 (
    .in0(2'b01), .in1(2'b11), .out(multiplexer_8_out), .sel(EX_Branched));
  Counter #(.width(16), .max('hffff), .ongoal("wrap"), .trigger("rising"), .behavior("old")) \u_置换标记  (
    .count(A0), .Q(C0), .clk(Clk), .clr(L0));  // open: load, D, carry, preset
  Counter #(.width(16), .max('hffff), .ongoal("wrap"), .trigger("rising"), .behavior("old")) \u_置换标记_2  (
    .count(A1), .Q(C1), .clk(Clk), .clr(L1));  // open: load, D, carry, preset
  Counter #(.width(16), .max('hffff), .ongoal("wrap"), .trigger("rising"), .behavior("old")) \u_置换标记_3  (
    .count(A2), .Q(C2), .clk(Clk), .clr(L2));  // open: load, D, carry, preset
  Counter #(.width(16), .max('hffff), .ongoal("wrap"), .trigger("rising"), .behavior("old")) \u_置换标记_4  (
    .count(A3), .Q(C3), .clk(Clk), .clr(L3));  // open: load, D, carry, preset
  Counter #(.width(16), .max('hffff), .ongoal("wrap"), .trigger("rising"), .behavior("old")) \u_置换标记_5  (
    .count(A4), .Q(C4), .clk(Clk), .clr(L4));  // open: load, D, carry, preset
  Counter #(.width(16), .max('hffff), .ongoal("wrap"), .trigger("rising"), .behavior("old")) \u_置换标记_6  (
    .count(A5), .Q(C5), .clk(Clk), .clr(L5));  // open: load, D, carry, preset
  Counter #(.width(16), .max('hffff), .ongoal("wrap"), .trigger("rising"), .behavior("old")) \u_置换标记_7  (
    .count(A6), .Q(C6), .clk(Clk), .clr(L6));  // open: load, D, carry, preset
  Counter #(.width(16), .max('hffff), .ongoal("wrap"), .trigger("rising"), .behavior("old")) \u_置换标记_8  (
    .count(A7), .Q(C7), .clk(Clk), .clr(L7));  // open: load, D, carry, preset
  and and_2 (A0, or_1_out, V0);
  and and_3 (A4, or_2_out, V4);
  Multiplexer #(.select(2), .width(2), .disabled("Z"), .enable("false")) multiplexer_9 (
    .in0(multiplexer_1_out), .in1(multiplexer_2_out), .in2(multiplexer_3_out), .in3(multiplexer_4_out),
    .out(multiplexer_9_out), .sel(Predict0));
  Adder #(.width(2)) adder_1 (.a(Predict0), .b(multiplexer_9_out), .out(adder_1_out));  // open: cin, cout
  Adder #(.width(2)) adder_2 (.a(Predict4), .b(multiplexer_10_out), .out(adder_2_out));  // open: cin, cout
  Multiplexer #(.select(2), .width(2), .disabled("Z"), .enable("false")) multiplexer_10 (
    .in0(multiplexer_5_out), .in1(multiplexer_6_out), .in2(multiplexer_7_out), .in3(multiplexer_8_out),
    .out(multiplexer_10_out), .sel(Predict4));
  or or_3 (or_3_out, decoder_1_out0, decoder_2_out0);
  or or_4 (or_4_out, decoder_1_out1, decoder_2_out1);
  or or_5 (or_5_out, decoder_1_out2, decoder_2_out2);
  or or_6 (or_6_out, decoder_1_out3, decoder_2_out3);
  or or_7 (or_7_out, decoder_1_out4, decoder_2_out4);
  or or_8 (or_8_out, decoder_1_out5, decoder_2_out5);
  or or_9 (or_9_out, decoder_1_out6, decoder_2_out6);
  or or_10 (or_10_out, decoder_1_out7, decoder_2_out7);
  Register #(.width(2), .trigger("rising"), .Select("low")) \u_分支预测历史位  (
    .D(adder_1_out), .en(M0), .Q(Predict0), .clk(Clk));  // open: clr
  Register #(.width(2), .trigger("rising"), .Select("low")) \u_分支预测历史位_2  (
    .D(adder_2_out), .en(M4), .Q(Predict4), .clk(Clk));  // open: clr
  Register #(.width(32), .trigger("rising"), .Select("low")) \u_分支目标地址  (
    .D(EX_BranchAddr), .en(WriteL0), .Q(\分支目标地址_q ), .clk(Clk));  // open: clr
  assign JumpAddr = L0 ? \分支目标地址_q  : 32'bz;  // Controlled_Buffer controlled_buffer_9
  Register #(.width(32), .trigger("rising"), .Select("low")) \u_分支目标地址_2  (
    .D(EX_BranchAddr), .en(WriteL1), .Q(\分支目标地址_2_q ), .clk(Clk));  // open: clr
  assign JumpAddr = L1 ? \分支目标地址_2_q  : 32'bz;  // Controlled_Buffer controlled_buffer_10
  Register #(.width(32), .trigger("rising"), .Select("low")) \u_分支目标地址_3  (
    .D(EX_BranchAddr), .en(WriteL2), .Q(\分支目标地址_3_q ), .clk(Clk));  // open: clr
  assign JumpAddr = L2 ? \分支目标地址_3_q  : 32'bz;  // Controlled_Buffer controlled_buffer_11
  assign JumpAddr = L3 ? \分支目标地址_4_q  : 32'bz;  // Controlled_Buffer controlled_buffer_12
  Register #(.width(32), .trigger("rising"), .Select("low")) \u_分支目标地址_4  (
    .D(EX_BranchAddr), .en(WriteL3), .Q(\分支目标地址_4_q ), .clk(Clk));  // open: clr
  assign JumpAddr = L4 ? \分支目标地址_5_q  : 32'bz;  // Controlled_Buffer controlled_buffer_13
  Register #(.width(32), .trigger("rising"), .Select("low")) \u_分支目标地址_5  (
    .D(EX_BranchAddr), .en(WriteL4), .Q(\分支目标地址_5_q ), .clk(Clk));  // open: clr
  Register #(.width(32), .trigger("rising"), .Select("low")) \u_分支目标地址_6  (
    .D(EX_BranchAddr), .en(WriteL5), .Q(\分支目标地址_6_q ), .clk(Clk));  // open: clr
  assign JumpAddr = L5 ? \分支目标地址_6_q  : 32'bz;  // Controlled_Buffer controlled_buffer_14
  Register #(.width(32), .trigger("rising"), .Select("low")) \u_分支目标地址_7  (
    .D(EX_BranchAddr), .en(WriteL6), .Q(\分支目标地址_7_q ), .clk(Clk));  // open: clr
  assign JumpAddr = L6 ? \分支目标地址_7_q  : 32'bz;  // Controlled_Buffer controlled_buffer_15
  assign JumpAddr = L7 ? \分支目标地址_8_q  : 32'bz;  // Controlled_Buffer controlled_buffer_16
  Register #(.width(32), .trigger("rising"), .Select("low")) \u_分支目标地址_8  (
    .D(EX_BranchAddr), .en(WriteL7), .Q(\分支目标地址_8_q ), .clk(Clk));  // open: clr
  and and_4 (WriteL0, or_3_out, EX_Miss, EX_Branch);
  and and_5 (WriteL1, or_4_out, EX_Miss, EX_Branch);
  and and_6 (WriteL2, or_5_out, EX_Miss, EX_Branch);
  and and_7 (WriteL3, or_6_out, EX_Miss, EX_Branch);
  and and_8 (WriteL4, or_7_out, EX_Miss, EX_Branch);
  and and_9 (WriteL5, or_8_out, EX_Miss, EX_Branch);
  and and_10 (WriteL6, or_9_out, EX_Miss, EX_Branch);
  and and_11 (WriteL7, or_10_out, EX_Miss, EX_Branch);
  or or_11 (or_11_out, L0, L2, L3, L4, L5, L6, L7, WriteL0, WriteL2, WriteL3, WriteL4, WriteL5, WriteL6, WriteL7);
  or or_12 (or_12_out, L0, L1, L2, L3, L4, L6, L7, WriteL0, WriteL1, WriteL2, WriteL3, WriteL4, WriteL6, WriteL7);
  and and_12 (A1, or_11_out, V1);
  and and_13 (A5, or_12_out, V5);
  Multiplexer #(.select(1), .width(2), .disabled("Z"), .enable("false")) multiplexer_11 (
    .in0(2'b00), .in1(2'b01), .out(multiplexer_11_out), .sel(EX_Branched));
  Multiplexer #(.select(1), .width(2), .disabled("Z"), .enable("false")) multiplexer_12 (
    .in0(2'b11), .in1(2'b01), .out(multiplexer_12_out), .sel(EX_Branched));
  Multiplexer #(.select(1), .width(2), .disabled("Z"), .enable("false")) multiplexer_13 (
    .in0(2'b01), .in1(2'b00), .out(multiplexer_13_out), .sel(EX_Branched));
  Multiplexer #(.select(1), .width(2), .disabled("Z"), .enable("false")) multiplexer_14 (
    .in0(2'b01), .in1(2'b11), .out(multiplexer_14_out), .sel(EX_Branched));
  Multiplexer #(.select(1), .width(2), .disabled("Z"), .enable("false")) multiplexer_15 (
    .in0(2'b00), .in1(2'b01), .out(multiplexer_15_out), .sel(EX_Branched));
  Multiplexer #(.select(1), .width(2), .disabled("Z"), .enable("false")) multiplexer_16 (
    .in0(2'b11), .in1(2'b01), .out(multiplexer_16_out), .sel(EX_Branched));
  Multiplexer #(.select(1), .width(2), .disabled("Z"), .enable("false")) multiplexer_17 (
    .in0(2'b01), .in1(2'b00), .out(multiplexer_17_out), .sel(EX_Branched));
  Multiplexer #(.select(1), .width(2), .disabled("Z"), .enable("false")) multiplexer_18 (
    .in0(2'b01), .in1(2'b11), .out(multiplexer_18_out), .sel(EX_Branched));
  Multiplexer #(.select(2), .width(2), .disabled("Z"), .enable("false")) multiplexer_19 (
    .in0(multiplexer_11_out), .in1(multiplexer_12_out), .in2(multiplexer_13_out), .in3(multiplexer_14_out),
    .out(multiplexer_19_out), .sel(Predict1));
  Multiplexer #(.select(2), .width(2), .disabled("Z"), .enable("false")) multiplexer_20 (
    .in0(multiplexer_15_out), .in1(multiplexer_16_out), .in2(multiplexer_17_out), .in3(multiplexer_18_out),
    .out(multiplexer_20_out), .sel(Predict5));
  Comparator #(.width(32), .mode("twosComplement")) comparator_1 (
    .a(PC), .b(Tag0), .eq(comparator_1_eq));  // open: gt, lt
  Comparator #(.width(32), .mode("twosComplement")) comparator_2 (
    .a(PC), .b(Tag1), .eq(comparator_2_eq));  // open: gt, lt
  Comparator #(.width(32), .mode("twosComplement")) comparator_3 (
    .a(PC), .b(Tag2), .eq(comparator_3_eq));  // open: gt, lt
  Comparator #(.width(32), .mode("twosComplement")) comparator_4 (
    .a(PC), .b(Tag3), .eq(comparator_4_eq));  // open: gt, lt
  Comparator #(.width(32), .mode("twosComplement")) comparator_5 (
    .a(PC), .b(Tag4), .eq(comparator_5_eq));  // open: gt, lt
  Comparator #(.width(32), .mode("twosComplement")) comparator_6 (
    .a(PC), .b(Tag5), .eq(comparator_6_eq));  // open: gt, lt
  Comparator #(.width(32), .mode("twosComplement")) comparator_7 (
    .a(PC), .b(Tag6), .eq(comparator_7_eq));  // open: gt, lt
  Comparator #(.width(32), .mode("twosComplement")) comparator_8 (
    .a(PC), .b(Tag7), .eq(comparator_8_eq));  // open: gt, lt
  Comparator #(.width(32), .mode("twosComplement")) comparator_9 (
    .a(EX_PC), .b(Tag0), .eq(comparator_9_eq));  // open: gt, lt
  Comparator #(.width(32), .mode("twosComplement")) comparator_10 (
    .a(EX_PC), .b(Tag1), .eq(comparator_10_eq));  // open: gt, lt
  Comparator #(.width(32), .mode("twosComplement")) comparator_11 (
    .a(EX_PC), .b(Tag2), .eq(comparator_11_eq));  // open: gt, lt
  Comparator #(.width(32), .mode("twosComplement")) comparator_12 (
    .a(EX_PC), .b(Tag3), .eq(comparator_12_eq));  // open: gt, lt
  Comparator #(.width(32), .mode("twosComplement")) comparator_13 (
    .a(EX_PC), .b(Tag4), .eq(comparator_13_eq));  // open: gt, lt
  Comparator #(.width(32), .mode("twosComplement")) comparator_14 (
    .a(EX_PC), .b(Tag5), .eq(comparator_14_eq));  // open: gt, lt
  Comparator #(.width(32), .mode("twosComplement")) comparator_15 (
    .a(EX_PC), .b(Tag6), .eq(comparator_15_eq));  // open: gt, lt
  Comparator #(.width(32), .mode("twosComplement")) comparator_16 (
    .a(EX_PC), .b(Tag7), .eq(comparator_16_eq));  // open: gt, lt
  Adder #(.width(2)) adder_3 (.a(Predict1), .b(multiplexer_19_out), .out(adder_3_out));  // open: cin, cout
  Register #(.width(2), .trigger("rising"), .Select("low")) \u_分支预测历史位_3  (
    .D(adder_3_out), .en(M1), .Q(Predict1), .clk(Clk));  // open: clr
  Adder #(.width(2)) adder_4 (.a(Predict5), .b(multiplexer_20_out), .out(adder_4_out));  // open: cin, cout
  or or_13 (or_13_out, L0, L1, L3, L4, L5, L6, L7, WriteL0, WriteL1, WriteL3, WriteL4, WriteL5, WriteL6, WriteL7);
  or or_14 (or_14_out, L0, L1, L2, L3, L4, L5, L7, WriteL0, WriteL1, WriteL2, WriteL3, WriteL4, WriteL5, WriteL7);
  Register #(.width(2), .trigger("rising"), .Select("low")) \u_分支预测历史位_4  (
    .D(adder_4_out), .en(M5), .Q(Predict5), .clk(Clk));  // open: clr
  and and_14 (L0, comparator_1_eq, V0);
  and and_15 (L1, comparator_2_eq, V1);
  and and_16 (L2, comparator_3_eq, V2);
  and and_17 (L3, comparator_4_eq, V3);
  and and_18 (L4, comparator_5_eq, V4);
  and and_19 (L5, comparator_6_eq, V5);
  and and_20 (L6, comparator_7_eq, V6);
  and and_21 (L7, comparator_8_eq, V7);
  and and_22 (M0, comparator_9_eq, V0);
  and and_23 (M1, comparator_10_eq, V1);
  and and_24 (M2, comparator_11_eq, V2);
  and and_25 (M3, comparator_12_eq, V3);
  and and_26 (M4, comparator_13_eq, V4);
  and and_27 (M5, comparator_14_eq, V5);
  and and_28 (M6, comparator_15_eq, V6);
  and and_29 (M7, comparator_16_eq, V7);
  and and_30 (A2, or_13_out, V2);
  and and_31 (A6, or_14_out, V6);
  or or_15 (IF_Hit, L0, L1, L2, L3, L4, L5, L6, L7);
  or or_16 (EX_Hit, M0, M1, M2, M3, M4, M5, M6, M7);
  Multiplexer #(.select(1), .width(2), .disabled("Z"), .enable("false")) multiplexer_21 (
    .in0(2'b00), .in1(2'b01), .out(multiplexer_21_out), .sel(EX_Branched));
  Multiplexer #(.select(1), .width(2), .disabled("Z"), .enable("false")) multiplexer_22 (
    .in0(2'b11), .in1(2'b01), .out(multiplexer_22_out), .sel(EX_Branched));
  Multiplexer #(.select(1), .width(2), .disabled("Z"), .enable("false")) multiplexer_23 (
    .in0(2'b01), .in1(2'b00), .out(multiplexer_23_out), .sel(EX_Branched));
  Multiplexer #(.select(1), .width(2), .disabled("Z"), .enable("false")) multiplexer_24 (
    .in0(2'b01), .in1(2'b11), .out(multiplexer_24_out), .sel(EX_Branched));
  Multiplexer #(.select(1), .width(2), .disabled("Z"), .enable("false")) multiplexer_25 (
    .in0(2'b00), .in1(2'b01), .out(multiplexer_25_out), .sel(EX_Branched));
  Multiplexer #(.select(1), .width(2), .disabled("Z"), .enable("false")) multiplexer_26 (
    .in0(2'b11), .in1(2'b01), .out(multiplexer_26_out), .sel(EX_Branched));
  Multiplexer #(.select(1), .width(2), .disabled("Z"), .enable("false")) multiplexer_27 (
    .in0(2'b01), .in1(2'b00), .out(multiplexer_27_out), .sel(EX_Branched));
  Multiplexer #(.select(1), .width(2), .disabled("Z"), .enable("false")) multiplexer_28 (
    .in0(2'b01), .in1(2'b11), .out(multiplexer_28_out), .sel(EX_Branched));
  not not_9 (IF_Miss, IF_Hit);
  not not_10 (EX_Miss, EX_Hit);
  Adder #(.width(2)) adder_5 (.a(Predict2), .b(multiplexer_29_out), .out(adder_5_out));  // open: cin, cout
  Multiplexer #(.select(2), .width(2), .disabled("Z"), .enable("false")) multiplexer_29 (
    .in0(multiplexer_21_out), .in1(multiplexer_22_out), .in2(multiplexer_23_out), .in3(multiplexer_24_out),
    .out(multiplexer_29_out), .sel(Predict2));
  Multiplexer #(.select(2), .width(2), .disabled("Z"), .enable("false")) multiplexer_30 (
    .in0(multiplexer_25_out), .in1(multiplexer_26_out), .in2(multiplexer_27_out), .in3(multiplexer_28_out),
    .out(multiplexer_30_out), .sel(Predict6));
  or or_17 (or_17_out, L0, L1, L2, L4, L5, L6, L7, WriteL0, WriteL1, WriteL2, WriteL4, WriteL5, WriteL6, WriteL7);
  or or_18 (or_18_out, L0, L1, L2, L3, L4, L5, L6, WriteL0, WriteL1, WriteL2, WriteL3, WriteL4, WriteL5, WriteL6);
  Register #(.width(2), .trigger("rising"), .Select("low")) \u_分支预测历史位_5  (
    .D(adder_5_out), .en(M2), .Q(Predict2), .clk(Clk));  // open: clr
  Register #(.width(2), .trigger("rising"), .Select("low")) \u_分支预测历史位_6  (
    .D(adder_6_out), .en(M6), .Q(Predict6), .clk(Clk));  // open: clr
  Adder #(.width(2)) adder_6 (.a(Predict6), .b(multiplexer_30_out), .out(adder_6_out));  // open: cin, cout
  and and_32 (A3, or_17_out, V3);
  and and_33 (A7, or_18_out, V7);
  Multiplexer #(.select(1), .width(2), .disabled("Z"), .enable("false")) multiplexer_31 (
    .in0(2'b00), .in1(2'b01), .out(multiplexer_31_out), .sel(EX_Branched));
  Multiplexer #(.select(1), .width(2), .disabled("Z"), .enable("false")) multiplexer_32 (
    .in0(2'b11), .in1(2'b01), .out(multiplexer_32_out), .sel(EX_Branched));
  Multiplexer #(.select(1), .width(2), .disabled("Z"), .enable("false")) multiplexer_33 (
    .in0(2'b01), .in1(2'b00), .out(multiplexer_33_out), .sel(EX_Branched));
  Multiplexer #(.select(1), .width(2), .disabled("Z"), .enable("false")) multiplexer_34 (
    .in0(2'b01), .in1(2'b11), .out(multiplexer_34_out), .sel(EX_Branched));
  Multiplexer #(.select(1), .width(2), .disabled("Z"), .enable("false")) multiplexer_35 (
    .in0(2'b00), .in1(2'b01), .out(multiplexer_35_out), .sel(EX_Branched));
  Multiplexer #(.select(1), .width(2), .disabled("Z"), .enable("false")) multiplexer_36 (
    .in0(2'b11), .in1(2'b01), .out(multiplexer_36_out), .sel(EX_Branched));
  Multiplexer #(.select(1), .width(2), .disabled("Z"), .enable("false")) multiplexer_37 (
    .in0(2'b01), .in1(2'b00), .out(multiplexer_37_out), .sel(EX_Branched));
  Multiplexer #(.select(1), .width(2), .disabled("Z"), .enable("false")) multiplexer_38 (
    .in0(2'b01), .in1(2'b11), .out(multiplexer_38_out), .sel(EX_Branched));
  Multiplexer #(.select(2), .width(2), .disabled("Z"), .enable("false")) multiplexer_39 (
    .in0(multiplexer_31_out), .in1(multiplexer_32_out), .in2(multiplexer_33_out), .in3(multiplexer_34_out),
    .out(multiplexer_39_out), .sel(Predict3));
  Multiplexer #(.select(2), .width(2), .disabled("Z"), .enable("false")) multiplexer_40 (
    .in0(multiplexer_35_out), .in1(multiplexer_36_out), .in2(multiplexer_37_out), .in3(multiplexer_38_out),
    .out(multiplexer_40_out), .sel(Predict7));
  Adder #(.width(2)) adder_7 (.a(Predict3), .b(multiplexer_39_out), .out(adder_7_out));  // open: cin, cout
  Adder #(.width(2)) adder_8 (.a(Predict7), .b(multiplexer_40_out), .out(adder_8_out));  // open: cin, cout
  Register #(.width(2), .trigger("rising"), .Select("low")) \u_分支预测历史位_7  (
    .D(adder_7_out), .en(M3), .Q(Predict3), .clk(Clk));  // open: clr
  Register #(.width(2), .trigger("rising"), .Select("low")) \u_分支预测历史位_8  (
    .D(adder_8_out), .en(M7), .Q(Predict7), .clk(Clk));  // open: clr

  // Other names for the same wires on the sheet: Tag[31:0] = EX_PC

  // Notes on the sheet:
  //   Cache槽
  //   读缺失逻辑/块载入逻辑
  //   查找逻辑
endmodule

module MAX2 (
  input  [15:0] Y,
  input  [15:0] X,
  input  [2:0] Y_num,
  input  [2:0] X_num,
  output [15:0] MAX,
  output [2:0] MAX_num
);

  wire comparator_1_eq, comparator_1_gt, or_1_out;

  Comparator #(.width(16), .mode("unsigned")) comparator_1 (
    .a(X), .b(Y), .gt(comparator_1_gt), .eq(comparator_1_eq));  // open: lt
  Multiplexer #(.select(1), .width(16), .disabled("Z"), .enable("false")) multiplexer_1 (
    .in0(Y), .in1(X), .out(MAX), .sel(or_1_out));
  or or_1 (or_1_out, comparator_1_gt, comparator_1_eq);
  Multiplexer #(.select(1), .width(3), .disabled("Z"), .enable("false")) multiplexer_2 (
    .in0(Y_num), .in1(X_num), .out(MAX_num), .sel(or_1_out));
endmodule

module \流水线中断  (
  output RegWrite,
  output MemWrite,
  output [31:0] IF_PC,
  output [31:0] ID_PC,
  output [31:0] EX_PC,
  output [31:0] M_PC,
  output [31:0] WB_PC,
  output [31:0] RDin,
  output [31:0] MDin,
  output [31:0] LedData
);

  wire and_2_out, and_3_out, and_4_out, and_5_out, and_6_out, and_7_out, and_8_out, and_10_out, and_11_out,
       BLTU, Branch, CLK, clock_1_out, comparator_1_eq, comparator_2_eq, comparator_3_eq, comparator_4_eq,
       comparator_5_eq, comparator_5_lt, comparator_6_eq, d_ff_1_q, d_ff_2_q, d_ff_3_q, d_ff_4_q,
       decoder_1_out1, decoder_1_out2, decoder_1_out3, en, EQ, EX_AluSrcB, EX_ecall, EX_Halt, EX_jal,
       EX_jalr, ex_mem_1_bltuout, ex_mem_1_haltout, ex_mem_1_jalout, ex_mem_1_jalrout, ex_mem_1_lbuout,
       ex_mem_1_memtoregout, ex_mem_1_u_typeout, ex_mem_1_uretout, EX_RegWrite, EX_S_Type, Go, halt,
       ID_ecall, id_ex_1_beqout, id_ex_1_bltuout, id_ex_1_bneout, id_ex_1_memtoregout, id_ex_1_memwriteout,
       id_ex_1_u_typeout, id_ex_1_uretout, IE_q, Inter1, Inter2, Inter3, Interr, Interrupt, IR1, IR2, IR3,
       LoadUse, LT, MEM_RegWrite, mem_wb_1_haltout, mem_wb_1_jalout, mem_wb_1_jalrout, mem_wb_1_lbuout,
       mem_wb_1_memtoregout, nand_1_out, not_1_out, not_2_out, not_4_out, or_1_out, or_2_out, or_3_out,
       or_5_out, or_6_out, or_9_out, or_11_out, or_12_out, or_13_out, Ret1, Ret2, Ret3, RST, uret, W1, W2,
       W3, WB_U_Type, \单周期硬布线控制器_1_alu_src , \单周期硬布线控制器_1_beq , \单周期硬布线控制器_1_bltu , \单周期硬布线控制器_1_bne ,
       \单周期硬布线控制器_1_jal , \单周期硬布线控制器_1_jalr , \单周期硬布线控制器_1_lbu , \单周期硬布线控制器_1_memtoreg ,
       \单周期硬布线控制器_1_memwrite , \单周期硬布线控制器_1_r1 , \单周期硬布线控制器_1_r2 , \单周期硬布线控制器_1_regwrite ,
       \单周期硬布线控制器_1_s_type , \单周期硬布线控制器_1_u_type , \单周期硬布线控制器_1_uret , \数据相关 ;
  wire [1:0] EX_R1Forward, EX_R2Forward, mem_wb_1_indexout, priority_encoder_1_out, R1Forward, R2Forward,
       \中断号_q ;
  wire [3:0] id_ex_1_aluopout, \单周期硬布线控制器_1_alu_op ;
  wire [4:0] EX_W_num, ID_R1_num, ID_R2_num, MEM_W_num, W_num;
  wire [7:0] multiplexer_12_out;
  wire [11:0] shifter_1_out;
  wire [12:0] CNT_num;
  wire [15:0] \LoadUse次数 , \分支成功数 , \总周期数 , \插入气泡数 , \无条件分支数 , \条件分支成功数 ;
  wire [19:0] shifter_2_out;
  wire [31:0] adder_1_out, adder_2_out, adder_4_out, Ain, and_1_out, Bin, bit_extender_1_out,
       bit_extender_2_out, bit_extender_3_out, bit_extender_4_out, bit_extender_5_out, EPC, EX_IR,
       ex_mem_1_immuout, EX_R1F, EX_R2, EX_R2F, id_ex_1_immuout, ID_IR, IF_IR, IF_PC_4, imm_B, imm_I, imm_J,
       imm_S, InterAddr, JAddr, MEM_IR, MEM_Result, mem_wb_1_immuout, mem_wb_1_resultout, mem_wb_1_rmdataout,
       multiplexer_1_out, multiplexer_2_out, multiplexer_4_out, multiplexer_5_out, multiplexer_10_out,
       multiplexer_13_out, multiplexer_14_out, multiplexer_15_out, nextPC, R1, R2, ram_1_data, WB_IR, WB_PC_4;

  Button \u_总复位  (.out(RST));
  Button _1 ();  // open: out
  Button _2 ();  // open: out
  Button _3 ();  // open: out
  // Probe on \总周期数 
  // Probe on \总周期数 
  Button \u_继续运行  (.out(Go));
  LED #(.active("true")) led_1 (.in(W1));
  LED #(.active("true")) led_2 (.in(W2));
  LED #(.active("true")) led_3 (.in(W3));
  // Probe on \分支成功数 
  Hex_Digit_Display hex_digit_display_1 (.value(LedData[31:28]));  // open: dp
  // Probe on IF_PC[19:0]
  // RiscV_Probe riscv_probe_1: pin names not known; wires that end beside it: IR1, IR2, IR3, IF_IR
  Comparator #(.width(16), .mode("twosComplement")) comparator_1 (
    .a(16'h23b), .b(\总周期数 ), .eq(comparator_1_eq));  // open: gt, lt
  or or_1 (or_1_out, comparator_1_eq, comparator_2_eq);
  Comparator #(.width(16), .mode("twosComplement")) comparator_2 (
    .a(\总周期数 ), .b(16'h1), .eq(comparator_2_eq));  // open: gt, lt
  Comparator #(.width(16), .mode("twosComplement")) comparator_3 (
    .a(\总周期数 ), .b(16'h100), .eq(comparator_3_eq));  // open: gt, lt
  Comparator #(.width(16), .mode("twosComplement")) comparator_4 (
    .a(\总周期数 ), .b(16'h200), .eq(comparator_4_eq));  // open: gt, lt
  Adder #(.width(32)) adder_1 (.a(imm_J), .b(IF_PC), .out(adder_1_out));  // open: cin, cout
  Hex_Digit_Display hex_digit_display_2 (.value(LedData[23:20]));  // open: dp
  Hex_Digit_Display hex_digit_display_3 (.value(LedData[27:24]));  // open: dp
  // Probe on ID_PC[19:0]
  // RiscV_Probe riscv_probe_2: pin names not known; wires that end beside it: ID_IR
  not not_1 (not_1_out, halt);
  Pull_Resistor #(.pull(0)) pull_resistor_1 (.node(IR1));
  assign IR1 = or_1_out ? ~CLK : 1'bz;  // Controlled_Inverter controlled_inverter_1
  Pull_Resistor #(.pull(0)) pull_resistor_2 (.node(IR2));
  assign IR2 = comparator_3_eq ? ~CLK : 1'bz;  // Controlled_Inverter controlled_inverter_2
  Pull_Resistor #(.pull(0)) pull_resistor_3 (.node(IR3));
  assign IR3 = comparator_4_eq ? ~CLK : 1'bz;  // Controlled_Inverter controlled_inverter_3
  Multiplexer #(.select(1), .width(32), .disabled("Z"), .enable("false")) multiplexer_1 (
    .in0(IF_PC_4), .in1(adder_1_out), .out(multiplexer_1_out), .sel(EX_jal));
  assign and_1_out = JAddr & 32'hfffffffe;  // AND_Gate and_1, 32 bits wide
  Adder #(.width(32)) adder_2 (.a(imm_B), .b(EX_PC), .out(adder_2_out));  // open: cin, cout
  Hex_Digit_Display hex_digit_display_4 (.value(LedData[19:16]));  // open: dp
  Hex_Digit_Display hex_digit_display_5 (.value(LedData[15:12]));  // open: dp
  Counter #(.width(16), .max('hffff), .ongoal("wrap"), .trigger("rising"), .behavior("new")) counter_1 (
    .count(not_1_out), .Q(\总周期数 ), .clk(CLK), .clr(RST));  // open: load, D, carry, preset, down
  Multiplexer #(.select(1), .width(32), .disabled("Z"), .enable("false")) multiplexer_2 (
    .in0(multiplexer_1_out), .in1(and_1_out), .out(multiplexer_2_out), .sel(EX_jalr));
  Hex_Digit_Display hex_digit_display_6 (.value(LedData[11:8]));  // open: dp
  Hex_Digit_Display hex_digit_display_7 (.value(LedData[7:4]));  // open: dp
  // Probe on EX_PC[19:0]
  // RiscV_Probe riscv_probe_3: pin names not known; wires that end beside it: EX_IR
  Multiplexer #(.select(1), .width(32), .disabled("Z"), .enable("false")) multiplexer_3 (
    .in0(multiplexer_2_out), .in1(adder_2_out), .out(nextPC), .sel(Branch));
  Multiplexer #(.select(1), .width(32), .disabled("Z"), .enable("false")) multiplexer_4 (
    .in0(nextPC), .in1(InterAddr), .out(multiplexer_4_out), .sel(Interrupt));
  Hex_Digit_Display hex_digit_display_8 (.value(LedData[3:0]));  // open: dp
  Multiplexer #(.select(1), .width(32), .disabled("Z"), .enable("false")) multiplexer_5 (
    .in0(multiplexer_4_out), .in1(EPC), .out(multiplexer_5_out), .sel(uret));
  Register #(.width(32), .trigger("rising"), .Select("low")) PC (
    .D(multiplexer_5_out), .en(and_2_out), .Q(IF_PC), .clk(CLK), .clr(RST));
  and and_2 (and_2_out, ~LoadUse, ~halt);  // AND_Gate
  // Probe on \总周期数 
  // Probe on M_PC[19:0]
  // RiscV_Probe riscv_probe_4: pin names not known; wires that end beside it: MEM_IR
  // Probe on \总周期数 
  // Probe on \无条件分支数 
  // Probe on \条件分支成功数 
  // Probe on \插入气泡数 
  // Probe on \LoadUse次数 
  // Probe on IF_PC[11:0]
  // Probe on WB_PC[19:0]
  // RiscV_Probe riscv_probe_5: pin names not known; wires that end beside it: WB_IR
  or or_2 (or_2_out, Branch, EX_jal, EX_jalr);
  ROM #(.addrWidth(10), .dataWidth(32), .Select("high")) rom_1 (.addr(IF_PC[11:2]), .data(IF_IR));
  Adder #(.width(32)) adder_3 (.a(IF_PC), .b(32'h4), .out(IF_PC_4));  // open: cin, cout
  // Probe on ID_PC[11:0]
  // Probe on EX_PC[11:0]
  or or_3 (or_3_out, uret, Interrupt, RST, or_2_out);
  IF_ID if_id_1 (
    .PCin(IF_PC), .IRin(IF_IR), .PCout(ID_PC), .IRout(ID_IR), .RST(or_3_out), .EN_H(and_3_out), .CLK(CLK));  // open: PJin, PJout
  and and_3 (and_3_out, ~LoadUse, en);  // AND_Gate
  // Probe on M_PC[11:0]
  D_Flip_Flop #(.trigger("high"), .Pre_Clr_Positions("LEGACY"), .NegatePresetClear("false"), .enable("true"), .NewFFLayout("false")) d_ff_1 (.Q(d_ff_1_q));  // open: clk, D, Qn, preset, en, reset
  // Probe on 13'hc
  // Probe on WB_PC[11:0]
  Comparator #(.width(13), .mode("twosComplement")) comparator_5 (
    .a(CNT_num), .b(13'hc), .eq(comparator_5_eq), .lt(comparator_5_lt));  // open: gt
  Clock #(.highDuration(1), .lowDuration(1)) clock_1 (.out(clock_1_out));
  nand nand_1 (nand_1_out, d_ff_1_q, comparator_5_eq);
  Counter #(.width(13), .max('h1fff), .ongoal("stay"), .trigger("rising"), .behavior("old")) counter_2 (
    .count(comparator_5_lt), .Q(CNT_num), .clk(clock_1_out));  // open: load, D, carry, clr, preset
  \数据冲突处理_重定向  \u_数据冲突处理_重定向_1  (
    .ID_R1(\单周期硬布线控制器_1_r1 ), .EX_RW(EX_RegWrite), .ID_R2(\单周期硬布线控制器_1_r2 ), .MEM_RW(MEM_RegWrite),
    .ID_R1_num(ID_R1_num), .EX_W_num(EX_W_num), .ID_R2_num(ID_R2_num), .MEM_W_num(MEM_W_num),
    .EX_OP(EX_IR[6:2]), .\数据相关 (\数据相关 ), .LoadUse(LoadUse), .R1Forward(R1Forward), .R2Forward(R2Forward));
  \单周期硬布线控制器  \u_单周期硬布线控制器_1  (
    .Funct({ID_IR[30], ID_IR[25], ID_IR[14:12]}), .OP(ID_IR[6:2]), .ALU_OP(\单周期硬布线控制器_1_alu_op ),
    .MemToReg(\单周期硬布线控制器_1_memtoreg ), .MemWrite(\单周期硬布线控制器_1_memwrite ), .ALU_SRC(\单周期硬布线控制器_1_alu_src ),
    .RegWrite(\单周期硬布线控制器_1_regwrite ), .ecall(ID_ecall), .S_type(\单周期硬布线控制器_1_s_type ),
    .Jalr(\单周期硬布线控制器_1_jalr ), .Beq(\单周期硬布线控制器_1_beq ), .JAL(\单周期硬布线控制器_1_jal ), .Bne(\单周期硬布线控制器_1_bne ),
    .in_3(ID_IR[21]), .uret(\单周期硬布线控制器_1_uret ), .BLTU(\单周期硬布线控制器_1_bltu ), .U_Type(\单周期硬布线控制器_1_u_type ),
    .LBU(\单周期硬布线控制器_1_lbu ), .R1(\单周期硬布线控制器_1_r1 ), .R2(\单周期硬布线控制器_1_r2 ));  // open: CSRRSI, CSRRCI
  Multiplexer #(.select(1), .width(5), .disabled("Z"), .enable("false")) multiplexer_6 (
    .in0(ID_IR[24:20]), .in1(5'b01010), .out(ID_R2_num), .sel(ID_ecall));
  assign bit_extender_1_out = {{20{ID_IR[31]}}, ID_IR[31:20]};  // Bit_Extender bit_extender_1
  assign bit_extender_2_out = {{20{ID_IR[31]}}, {ID_IR[31:25], ID_IR[11:7]}};  // Bit_Extender bit_extender_2
  assign CLK = nand_1_out ? clock_1_out : 1'bz;  // Controlled_Buffer controlled_buffer_1
  Multiplexer #(.select(1), .width(5), .disabled("Z"), .enable("false")) multiplexer_7 (
    .in0(ID_IR[19:15]), .in1(5'b10001), .out(ID_R1_num), .sel(ID_ecall));
  Shifter #(.width(12), .shift("ll")) shifter_1 (
    .in({ID_IR[31], ID_IR[7], ID_IR[30:25], ID_IR[11:8]}), .\dist (4'b0001), .out(shifter_1_out));
  Shifter #(.width(20), .shift("ll")) shifter_2 (
    .in({ID_IR[31], ID_IR[19:12], ID_IR[20], ID_IR[30:21]}), .\dist (5'b00001), .out(shifter_2_out));
  Pull_Resistor #(.pull(1)) pull_resistor_4 (.node(CLK));
  assign bit_extender_3_out = {{20{shifter_1_out[11]}}, shifter_1_out};  // Bit_Extender bit_extender_3
  assign bit_extender_4_out = {{12{shifter_2_out[19]}}, shifter_2_out};  // Bit_Extender bit_extender_4
  not not_2 (not_2_out, CLK);
  Regifile regifile_1 (
    .Din(RDin), .Clk(not_2_out), .R1(R1), .R2(R2), .WE(RegWrite), .W_num(W_num), .R1_num(ID_R1_num),
    .R2_num(ID_R2_num));
  or or_4 (W1, Inter1, d_ff_2_q);
  D_Flip_Flop #(.trigger("rising"), .Pre_Clr_Positions("LEGACY"), .NegatePresetClear("false"), .enable("true"), .NewFFLayout("false")) d_ff_2 (
    .clk(IR1), .D(1'b1), .Q(d_ff_2_q), .reset(Inter1));  // open: Qn, preset, en
  or or_5 (or_5_out, d_ff_2_q, Inter1);
  and and_4 (and_4_out, or_5_out, ~Ret1);  // AND_Gate
  D_Flip_Flop #(.trigger("rising"), .Pre_Clr_Positions("LEGACY"), .NegatePresetClear("false"), .enable("true"), .NewFFLayout("false")) u_IR1 (
    .clk(CLK), .D(and_4_out), .Q(Inter1));  // open: Qn, preset, en, reset
  or or_6 (or_6_out, LoadUse, or_3_out);
  ID_EX id_ex_1 (
    .PCin(ID_PC), .IRin(ID_IR), .ImmIin(bit_extender_1_out), .ImmSin(bit_extender_2_out),
    .ImmBin(bit_extender_3_out), .ImmJin(bit_extender_4_out), .R1in(R1), .R2in(R2),
    .AluOpin(\单周期硬布线控制器_1_alu_op ), .RST(or_6_out), .EN_H(en), .CLK(CLK), .Beqin(\单周期硬布线控制器_1_beq ),
    .Bnein(\单周期硬布线控制器_1_bne ), .MemToRegin(\单周期硬布线控制器_1_memtoreg ), .MemWritein(\单周期硬布线控制器_1_memwrite ),
    .AluSrcBin(\单周期硬布线控制器_1_alu_src ), .RegWritein(\单周期硬布线控制器_1_regwrite ), .S_typein(\单周期硬布线控制器_1_s_type ),
    .Jalin(\单周期硬布线控制器_1_jal ), .Jalrin(\单周期硬布线控制器_1_jalr ), .Haltin(1'b0), .Beqout(id_ex_1_beqout),
    .Bneout(id_ex_1_bneout), .MemToRegout(id_ex_1_memtoregout), .MemWriteout(id_ex_1_memwriteout),
    .AluSrcBout(EX_AluSrcB), .RegWriteout(EX_RegWrite), .S_Typeout(EX_S_Type), .Jalout(EX_jal),
    .Jalrout(EX_jalr), .AluOpout(id_ex_1_aluopout), .PCout(EX_PC), .IRout(EX_IR), .Imm_I_out(imm_I),
    .Imm_S_out(imm_S), .Imm_B_out(imm_B), .Imm_J_out(imm_J), .R1out(EX_R1F), .R2out(EX_R2F),
    .W_in(ID_IR[11:7]), .W_out(EX_W_num), .URETin(\单周期硬布线控制器_1_uret ), .LBUin(\单周期硬布线控制器_1_lbu ),
    .BLTUin(\单周期硬布线控制器_1_bltu ), .U_Typein(\单周期硬布线控制器_1_u_type ), .URETout(id_ex_1_uretout), .LBUout(BLTU),
    .BLTUout(id_ex_1_bltuout), .U_Typeout(id_ex_1_u_typeout), .ImmUin({ID_IR[31:12], {12{1'b0}}}),
    .ImmUout(id_ex_1_immuout), .Ecallin(ID_ecall), .Ecallout(EX_ecall), .R1Forwardin(R1Forward),
    .R1Forwardout(EX_R1Forward), .R2Forwardin(R2Forward), .R2Forwardout(EX_R2Forward));  // open: Haltout, PJin, PJout
  Comparator #(.width(32), .mode("twosComplement")) comparator_6 (
    .a(Ain), .b(32'h22), .eq(comparator_6_eq));  // open: gt, lt
  or or_7 (W2, Inter2, d_ff_3_q);
  Multiplexer #(.select(2), .width(32), .disabled("Z"), .enable("false")) multiplexer_8 (
    .in0(EX_R1F), .in1(RDin), .in2(MEM_Result), .out(Ain), .sel(EX_R1Forward));  // open: in3
  Multiplexer #(.select(2), .width(32), .disabled("Z"), .enable("false")) multiplexer_9 (
    .in0(EX_R2F), .in1(RDin), .in2(MEM_Result), .out(EX_R2), .sel(EX_R2Forward));  // open: in3
  Multiplexer #(.select(1), .width(32), .disabled("Z"), .enable("false")) multiplexer_10 (
    .in0(imm_I), .in1(imm_S), .out(multiplexer_10_out), .sel(EX_S_Type));
  D_Flip_Flop #(.trigger("rising"), .Pre_Clr_Positions("LEGACY"), .NegatePresetClear("false"), .enable("true"), .NewFFLayout("false")) d_ff_3 (
    .clk(IR2), .D(1'b1), .Q(d_ff_3_q), .reset(Inter2));  // open: Qn, preset, en
  and and_5 (and_5_out, id_ex_1_beqout, EQ);
  or or_8 (Branch, and_5_out, and_6_out, and_7_out);
  and and_6 (and_6_out, ~EQ, id_ex_1_bneout);  // AND_Gate
  and and_7 (and_7_out, BLTU, LT);
  ALU alu_1 (
    .X(Ain), .Y(Bin), .AluOP(id_ex_1_aluopout), .Equal(EQ), .Result(JAddr), .out_6(LT));  // open: Result_2, out_4
  Multiplexer #(.select(1), .width(32), .disabled("Z"), .enable("false")) multiplexer_11 (
    .in0(EX_R2), .in1(multiplexer_10_out), .out(Bin), .sel(EX_AluSrcB));
  Register #(.width(32), .trigger("rising"), .Select("low")) register_1 (
    .D(EX_R2), .en(and_8_out), .Q(LedData), .clk(CLK), .clr(RST));
  and and_8 (and_8_out, EX_ecall, comparator_6_eq);
  and and_9 (EX_Halt, ~comparator_6_eq, EX_ecall, ~Go);  // AND_Gate
  or or_9 (or_9_out, d_ff_3_q, Inter2);
  Counter #(.width(16), .max('hffff), .ongoal("wrap"), .trigger("rising"), .behavior("new")) counter_3 (
    .count(Branch), .Q(\分支成功数 ), .clk(CLK), .clr(RST));  // open: load, D, carry, preset, down
  and and_10 (and_10_out, or_9_out, ~Ret2);  // AND_Gate
  D_Flip_Flop #(.trigger("rising"), .Pre_Clr_Positions("LEGACY"), .NegatePresetClear("false"), .enable("true"), .NewFFLayout("false")) u_IR2 (
    .clk(CLK), .D(and_10_out), .Q(Inter2));  // open: Qn, preset, en, reset
  EX_MEM ex_mem_1 (
    .PCin(EX_PC), .IRin(EX_IR), .Resultin(JAddr), .MDatain(EX_R2), .PCout(M_PC), .IRout(MEM_IR),
    .Resultout(MEM_Result), .Mdataout(MDin), .MemToRegin(id_ex_1_memtoregout),
    .MemWritein(id_ex_1_memwriteout), .Jalin(EX_jal), .RegWritein(EX_RegWrite), .Haltin(EX_Halt),
    .MemToRegout(ex_mem_1_memtoregout), .MemWriteout(MemWrite), .Jalout(ex_mem_1_jalout),
    .RegWriteout(MEM_RegWrite), .Haltout(ex_mem_1_haltout), .RST(RST), .EN_H(en), .CLK(CLK), .W_in(EX_W_num),
    .W_out(MEM_W_num), .URETin(id_ex_1_uretout), .LBUin(BLTU), .BLTUin(id_ex_1_bltuout),
    .U_Typein(id_ex_1_u_typeout), .URETout(ex_mem_1_uretout), .LBUout(ex_mem_1_lbuout),
    .BLTUout(ex_mem_1_bltuout), .U_Typeout(ex_mem_1_u_typeout), .Jalrin(EX_jalr), .Jalrout(ex_mem_1_jalrout),
    .ImmUin(id_ex_1_immuout), .ImmUout(ex_mem_1_immuout));
  or or_10 (W3, Inter3, d_ff_4_q);
  RAM #(.addrWidth(10), .dataWidth(32), .bus("separate"), .Select("high")) ram_1 (
    .addr(MEM_Result[11:2]), .din(MDin), .data(ram_1_data), .str(MemWrite), .clk(CLK),
    .ld(ex_mem_1_memtoregout), .clr(RST));  // open: sel
  D_Flip_Flop #(.trigger("rising"), .Pre_Clr_Positions("LEGACY"), .NegatePresetClear("false"), .enable("true"), .NewFFLayout("false")) d_ff_4 (
    .clk(IR3), .D(1'b1), .Q(d_ff_4_q), .reset(Inter3));  // open: Qn, preset, en
  MEM_WB mem_wb_1 (
    .PCin(M_PC), .IRin(MEM_IR), .Resultin(MEM_Result), .RMDatain(ram_1_data), .PCout(WB_PC), .IRout(WB_IR),
    .Resultout(mem_wb_1_resultout), .RMdataout(mem_wb_1_rmdataout), .RST(RST), .W_in(MEM_W_num), .EN_H(en),
    .W_out(W_num), .CLK(CLK), .MemToRegin(ex_mem_1_memtoregout), .Jalin(ex_mem_1_jalout),
    .RegWritein(MEM_RegWrite), .Haltin(ex_mem_1_haltout), .MemToRegout(mem_wb_1_memtoregout),
    .RegWriteout(RegWrite), .Jalrin(ex_mem_1_jalrout), .URETin(ex_mem_1_uretout), .LBUin(ex_mem_1_lbuout),
    .BLTUin(ex_mem_1_bltuout), .U_Typein(ex_mem_1_u_typeout), .Jalout(mem_wb_1_jalout),
    .Jalrout(mem_wb_1_jalrout), .URETout(uret), .LBUout(mem_wb_1_lbuout), .U_Typeout(WB_U_Type),
    .ImmUin(ex_mem_1_immuout), .ImmUout(mem_wb_1_immuout), .Indexin(MEM_Result[1:0]),
    .Indexout(mem_wb_1_indexout), .Haltout(mem_wb_1_haltout));  // open: BLTUout
  or or_11 (or_11_out, d_ff_4_q, Inter3);
  and and_11 (and_11_out, or_11_out, ~Ret3);  // AND_Gate
  Multiplexer #(.select(2), .width(8), .disabled("Z"), .enable("false")) multiplexer_12 (
    .in0(mem_wb_1_rmdataout[7:0]), .in1(mem_wb_1_rmdataout[15:8]), .in2(mem_wb_1_rmdataout[23:16]),
    .in3(mem_wb_1_rmdataout[31:24]), .out(multiplexer_12_out), .sel(mem_wb_1_indexout));
  and and_12 (halt, mem_wb_1_haltout, ~Go);  // AND_Gate
  not not_3 (en, halt);
  D_Flip_Flop #(.trigger("rising"), .Pre_Clr_Positions("LEGACY"), .NegatePresetClear("false"), .enable("true"), .NewFFLayout("false")) u_IR3 (
    .clk(CLK), .D(and_11_out), .Q(Inter3));  // open: Qn, preset, en, reset
  or or_12 (or_12_out, mem_wb_1_jalout, mem_wb_1_jalrout, WB_U_Type);
  assign bit_extender_5_out = {{24{1'b0}}, multiplexer_12_out};  // Bit_Extender bit_extender_5
  Adder #(.width(32)) adder_4 (.a(WB_PC), .b(mem_wb_1_immuout), .out(adder_4_out));  // open: cin, cout
  Adder #(.width(32)) adder_5 (.a(32'h4), .b(WB_PC), .out(WB_PC_4));  // open: cin, cout
  Multiplexer #(.select(1), .width(32), .disabled("Z"), .enable("false")) multiplexer_13 (
    .in0(mem_wb_1_resultout), .in1(multiplexer_14_out), .out(multiplexer_13_out), .sel(mem_wb_1_memtoregout));
  Multiplexer #(.select(1), .width(32), .disabled("Z"), .enable("false")) multiplexer_14 (
    .in0(mem_wb_1_rmdataout), .in1(bit_extender_5_out), .out(multiplexer_14_out), .sel(mem_wb_1_lbuout));
  Multiplexer #(.select(1), .width(32), .disabled("Z"), .enable("false")) multiplexer_15 (
    .in0(WB_PC_4), .in1(adder_4_out), .out(multiplexer_15_out), .sel(WB_U_Type));
  Multiplexer #(.select(1), .width(32), .disabled("Z"), .enable("false")) multiplexer_16 (
    .in0(multiplexer_13_out), .in1(multiplexer_15_out), .out(RDin), .sel(or_12_out));
  Priority_Encoder #(.select(2), .disabled("Z")) priority_encoder_1 (
    .in0(1'b0), .in1(Inter1), .in2(Inter2), .in3(Inter3), .out(priority_encoder_1_out), .gs(Interr));  // open: en_out, en_in
  Register #(.width(32), .trigger("rising"), .Select("low")) u_EPC (
    .D(nextPC), .en(Interrupt), .Q(EPC), .clk(CLK));  // open: clr
  Multiplexer #(.select(2), .width(32), .disabled("Z"), .enable("false")) multiplexer_17 (
    .in1(32'h30ac), .in2(32'h3150), .in3(32'h31f4), .out(InterAddr), .sel(priority_encoder_1_out));  // open: in0
  Register #(.width(1), .trigger("rising"), .Select("low")) IE (
    .D(Interrupt), .en(or_13_out), .Q(IE_q), .clk(CLK));  // open: clr
  or or_13 (or_13_out, Interrupt, uret);
  Register #(.width(2), .trigger("rising"), .Select("low")) \u_中断号  (
    .D(priority_encoder_1_out), .en(Interrupt), .Q(\中断号_q ), .clk(CLK));  // open: clr
  Decoder #(.select(2), .tristate("false"), .disabled("Z"), .enable("false")) decoder_1 (
    .out1(decoder_1_out1), .out2(decoder_1_out2), .out3(decoder_1_out3), .sel(\中断号_q ));  // open: out0
  not not_4 (not_4_out, IE_q);
  and and_13 (Interrupt, not_4_out, Interr);
  and and_14 (Ret1, uret, decoder_1_out1);
  and and_15 (Ret2, decoder_1_out2, uret);
  and and_16 (Ret3, decoder_1_out3, uret);

  // Other names for the same wires on the sheet: IR[31:0] = ID_IR; RD_num[4:0] = ID_IR[11:7]; EX_R1[31:0] = Ain;
  //   MEM_MemWrite = MemWrite; MEM_PC[31:0] = M_PC; WB_RegWrite = RegWrite; WriteBackData[31:0] = RDin

  // Notes on the sheet:
  //   中断源
  //   时空图监测，可删除
  //   中断等待指示
  //   单级中断测试信号模拟器
  //   数码管输出
  //   指令存储器
  //   contents of rom_1 (hex, n*v repeats v):
  //   7d000113 100413 1f41993 41f9d993 433 c00913 800b13 140413 f47413 800293 100313 499993 89e9b3 1300533
  //   2200893 73 406282b3 fe0294e3 140413 f00f93 1f47433 1c41413 800293 100313 49d993 89e9b3 1300533
  //   2200893 73 406282b3 fe0294e3 1c45413 406b0b33 b0463 f95ff06f 2b3 fff2c293 1029293 fff2e293 500533
  //   2200893 73 f5dff06f 1112023 410113 a12023 410113 812023 410113 1312023 410113 1412023 410113 1512023
  //   410113 1612023 410113 100b13 300a13 100a93 1600433 441413 14469b3 1300533 2200893 73 fe0416e3
  //   415a0a33 fe0a10e3 ffc10113 12b03 ffc10113 12a83 ffc10113 12a03 ffc10113 12983 ffc10113 12403
  //   ffc10113 12503 ffc10113 12883 200073 1112023 410113 a12023 410113 812023 410113 1312023 410113
  //   1412023 410113 1512023 410113 1612023 410113 200b13 300a13 100a93 1600433 441413 14469b3 1300533
  //   2200893 73 fe0416e3 415a0a33 fe0a10e3 ffc10113 12b03 ffc10113 12a83 ffc10113 12a03 ffc10113 12983
  //   ffc10113 12403 ffc10113 12503 ffc10113 12883 200073 1112023 410113 a12023 410113 812023 410113
  //   1312023 410113 1412023 410113 1512023 410113 1612023 410113 300b13 300a13 100a93 1600433 441413
  //   14469b3 1300533 2200893 73 fe0416e3 415a0a33 fe0a10e3 ffc10113 12b03 ffc10113 12a83 ffc10113 12a03
  //   ffc10113 12983 ffc10113 12403 ffc10113 12503 ffc10113 12883 200073
  //   控制位
  //   流水调试日志用
  //   暂停节拍，不能为0
  //   戳工具置1进入计数暂停模式，ctrl+k时钟自动运行到对应节拍暂停
  //   ctrl+k关闭时钟连续运行，将控制位置零，进入单步调试模式调试
  //   ctrl+k关闭时钟连续运行，将控制位置零，进入单步调试模式调试
  //   rs1
  //   rs2
  //   指令字
  //   rd
  //   可计数暂停的时钟源
  //   为方便自动评测，需要输出流水线各段保存的PC值，注意是PC不是PC+4，另外ID段寄存器写入信息，Mem段内存写入信息也要输出
  //   Reset 
  //   Reset 
endmodule
